// Logisim project arbiter.circ as structural Verilog: 4 circuits, main circuit main
module main (
  input  MCLK,
  input  rw_in,
  input  as_in,
  input  w33,
  input  w38,
  input  VCLK,
  input  uds_in,
  input  [22:0] va_in,
  input  w82,
  input  bgack_in,
  input  [15:0] vd_in,
  input  m3,
  input  iorq,
  input  [15:0] za,
  input  m1_in,
  input  ZCLK,
  output w12,
  output zrd_out,
  output zwr_out,
  output VD8_out,
  output w24,
  output w35,
  output w115,
  output ZA0_out,
  output w120,
  output w32,
  output w123,
  output w47,
  output o_TIME,
  output FDC
);

  wire and_1_out, and_2_out, cnt_bit_1_cout, cnt_bit_1_nq, cnt_bit_2_nq, cnt_bit_3_cout, cnt_bit_3_nq,
       cnt_bit_4_nq, cnt_bit_4_q, cnt_bit_5_cout, cnt_bit_5_nq, cnt_bit_6_nq, cnt_bit_6_q, cnt_bit_7_nq,
       d_ff_1_q, d_ff_1_qn, d_ff_2_qn, dff11_q, dff12_q, dff12_qn, dff13_qn, dff15_q, dff15_qn, dff16_q,
       dff17_q, dff19_q, dff20_q, dff20_qn, dff23_qn, dff24_q, nand_1_out, nor_1_out, nor_2_out, nor_3_out,
       nor_4_out, not_1_out, not_2_out, not_3_out, not_4_out, not_6_out, not_7_out, not_8_out, not_9_out,
       not_10_out, not_11_out, not_13_out, not_14_out, not_16_out, not_17_out, not_18_out, not_19_out,
       not_21_out, not_22_out, not_23_out, not_24_out, not_25_out, not_26_out, not_27_out, not_28_out,
       not_29_out, not_30_out, not_31_out, not_32_out, not_33_out, not_34_out, not_35_out, not_36_out,
       not_37_out, not_39_out, not_43_out, not_44_out, not_46_out, not_47_out, not_48_out, not_49_out,
       undriven, undriven_2, undriven_3, undriven_4, undriven_5, undriven_6, undriven_7, undriven_8,
       undriven_9, undriven_10, undriven_11, undriven_12, undriven_13, undriven_14, undriven_15, undriven_16,
       undriven_17, undriven_18, undriven_19, w26_out, w27_out, w34_out, w36_out, w40_out, w41_out, w42_out,
       w43_out, w44_out, w45_out, w46_out, w54_out, w58_out, w59_out, w60_out, w64_out, w65_out, w66_out,
       w68_out, w69_out, w70_out, w71_out, w72_out, w73_out, w75_out, w83_out, w84_out, w94_out, w95_out,
       w97_out, w102_out, w103_out, w107_out, w113_out, xor_delay_6x_1_out_2, xor_delay_6x_2_out_2,
       xor_delay_40x_1_out_2;

  not not_1 (not_1_out, VCLK);
  and w40 (w40_out, w26_out, w83_out);
  D_Flip_Flop d_ff_1 (
    .D(nor_3_out), .clk(not_46_out), .Q(d_ff_1_q), .Qn(d_ff_1_qn), .reset(not_2_out));  // open: preset
  not not_2 (not_2_out, not_33_out);
  // NOR_Gate nor_1 has open pins: out=nor_1_out
  D_Flip_Flop dff13 (.D(uds_in), .clk(not_1_out), .Qn(dff13_qn));  // open: Q, preset, reset
  not not_3 (not_3_out, w73_out);
  D_Flip_Flop dff15 (.D(w40_out), .clk(VCLK), .Q(dff15_q), .Qn(dff15_qn), .preset(not_3_out));  // open: reset
  not not_4 (not_4_out, m3);
  // NOT_Gate not_5 has open pins: in=ZCLK, out=open
  // NOT_Gate not_6 has open pins: in=open, out=not_6_out
  D_Flip_Flop d_ff_2 (.D(nor_4_out), .clk(not_46_out), .Qn(d_ff_2_qn), .preset(not_13_out));  // open: Q, reset
  not not_7 (not_7_out, not_46_out);
  and and_1 (and_1_out, 1'b0, d_ff_1_q);
  nor nor_2 (nor_2_out, d_ff_1_q, w27_out);
  not not_8 (not_8_out, rw_in);
  not not_9 (not_9_out, undriven_2);
  D_Flip_Flop dff11 (.D(w43_out), .clk(not_1_out), .Q(dff11_q));  // open: Qn, preset, reset
  nand w42 (w42_out, dff19_q, w71_out);
  or w44 (w44_out, w42_out, undriven, va_in[22]);
  D_Flip_Flop dff16 (.D(w44_out), .clk(VCLK), .Q(dff16_q));  // open: Qn, preset, reset
  or w59 (w59_out, as_in, not_4_out);
  xor_delay_6x xor_delay_6x_1 (.in_1(m1_in), .out_2(xor_delay_6x_1_out_2));
  not not_10 (not_10_out, not_6_out);
  not not_11 (not_11_out, not_7_out);
  nor nor_3 (nor_3_out, and_1_out, nor_2_out);
  not not_12 (w24, not_9_out);
  or w41 (w41_out, dff15_q, w27_out);
  or w36 (w36_out, undriven_3, rw_in);
  nand nand_1 (nand_1_out, cnt_bit_2_nq, cnt_bit_4_nq, cnt_bit_6_nq);
  not not_13 (not_13_out, not_10_out);
  not not_14 (not_14_out, not_11_out);
  // NOT_Gate not_15 has open pins: in=not_14_out, out=open
  buf or_1 (w12, not_8_out);  // OR_Gate
  or or_2 (zrd_out, as_in, not_8_out);
  or or_3 (zwr_out, rw_in, as_in);
  D_Flip_Flop dff12 (.D(w41_out), .clk(not_1_out), .Q(dff12_q), .Qn(dff12_qn));  // open: preset, reset
  not not_16 (not_16_out, w73_out);
  D_Flip_Flop dff19 (.D(w71_out), .clk(not_1_out), .Q(dff19_q), .preset(not_16_out));  // open: Qn, reset
  or w43 (w43_out, w44_out, dff16_q);
  and w45 (w45_out, undriven_4, w46_out);
  or w46 (w46_out, w45_out, bgack_in);
  not not_17 (not_17_out, w38);
  not not_18 (not_18_out, not_17_out);
  and and_2 (and_2_out, cnt_bit_6_q, cnt_bit_4_q);
  not not_19 (not_19_out, w73_out);
  D_Flip_Flop dff17 (.D(w58_out), .clk(VCLK), .Q(dff17_q), .preset(not_19_out));  // open: Qn, reset
  // NOT_Gate not_20 has open pins: in=w45_out, out=open
  not not_21 (not_21_out, za[14]);
  cnt_bit cnt_bit_1 (
    .cin(d_ff_1_q), .val(1'b1), .load(d_ff_1_q), .clk(not_49_out), .res(not_10_out), .cout(cnt_bit_1_cout),
    .nq(cnt_bit_1_nq));  // open: q
  not w26 (w26_out, dff12_q);  // NAND_Gate
  buf w27 (w27_out, dff11_q);  // OR_Gate
  not not_22 (not_22_out, dff17_q);
  not not_23 (not_23_out, m1_in);
  not not_24 (not_24_out, za[15]);
  not not_25 (not_25_out, w12);
  D_Flip_Flop dff14 (.D(undriven_5), .clk(w36_out), .Qn(w35), .reset(not_26_out));  // open: Q, preset
  // NOT_Gate not_26 has open pins: in=open, out=not_26_out
  not not_27 (not_27_out, not_22_out);
  not not_28 (not_28_out, not_27_out);
  not w54 (w54_out, va_in[22]);  // NAND_Gate
  not not_29 (not_29_out, d_ff_2_qn);
  assign VD8_out = not_25_out ? w33 : 1'bz;  // Controlled_Buffer controlled_buffer_1
  or w34 (w34_out, w33, w35);
  nor w69 (w69_out, dff12_qn, w44_out);
  not not_30 (not_30_out, not_28_out);
  and w58 (w58_out, w84_out, w54_out);
  not not_31 (not_31_out, not_29_out);
  not not_32 (not_32_out, not_31_out);
  buf w60 (w60_out, w33);  // OR_Gate
  cnt_bit cnt_bit_2 (
    .cin(and_2_out), .val(1'b1), .load(nand_1_out), .clk(MCLK), .res(not_18_out), .nq(cnt_bit_2_nq));  // open: cout, q
  cnt_bit cnt_bit_3 (
    .cin(cnt_bit_1_cout), .val(1'b0), .load(d_ff_1_q), .clk(not_49_out), .res(not_10_out),
    .cout(cnt_bit_3_cout), .nq(cnt_bit_3_nq));  // open: q
  not not_33 (not_33_out, not_32_out);
  or w107 (w107_out, m3, undriven_6, not_21_out, not_24_out);
  or w113 (w113_out, m3, iorq, not_23_out);
  D_Flip_Flop dff27 (.D(xor_delay_6x_1_out_2), .clk(ZCLK));  // open: Q, Qn, preset, reset
  nor nor_4 (nor_4_out, cnt_bit_7_nq, cnt_bit_5_nq, cnt_bit_3_nq, cnt_bit_1_nq);
  nor w95 (w95_out, rw_in, uds_in);
  and w73 (w73_out, undriven_8, m3);
  // AND_Gate w112 has open pins: in1=w113_out, out=open
  xor_delay_6x xor_delay_6x_2 (.in_1(w113_out), .out_2(xor_delay_6x_2_out_2));
  cnt_bit cnt_bit_4 (
    .cin(1'b1), .val(d_ff_1_qn), .load(nand_1_out), .clk(MCLK), .res(not_18_out), .q(cnt_bit_4_q),
    .nq(cnt_bit_4_nq));  // open: cout
  cnt_bit cnt_bit_5 (
    .cin(cnt_bit_3_cout), .val(1'b0), .load(d_ff_1_q), .clk(not_49_out), .res(not_10_out),
    .cout(cnt_bit_5_cout), .nq(cnt_bit_5_nq));  // open: q
  not not_34 (not_34_out, uds_in);
  or w66 (w66_out, as_in, undriven_10);
  not w68 (w68_out, vd_in[8]);  // NOR_Gate
  and w71 (w71_out, dff20_q, not_30_out);
  not not_35 (not_35_out, w73_out);
  D_Flip_Flop dff20 (.D(not_30_out), .clk(not_1_out), .Q(dff20_q), .Qn(dff20_qn), .preset(not_35_out));  // open: reset
  D_Flip_Flop dff23 (.D(undriven_12), .clk(not_36_out), .Qn(dff23_qn), .reset(not_37_out));  // open: Q, preset
  not not_36 (not_36_out, w59_out);
  not not_37 (not_37_out, undriven_12);
  or w126 (o_TIME, undriven_9, as_in);
  or w130 (FDC, as_in, undriven_7);
  nand w65 (w65_out, uds_in, dff13_qn);
  not not_38 (w32, w68_out);
  and w70 (w70_out, w27_out, w71_out);
  or w72 (w72_out, dff15_qn, w43_out);
  not not_39 (not_39_out, not_18_out);
  xor_delay_40x xor_delay_40x_1 (.in_1(undriven_11), .out_2(xor_delay_40x_1_out_2));
  // NOR_Gate w101 has open pins: in0=undriven_13, in1=dff20_qn, out=open
  not w75 (w75_out, w94_out);  // NAND_Gate
  or w83 (w83_out, dff23_qn, va_in[22]);
  // NOT_Gate not_40 has open pins: in=not_39_out, out=open
  // NAND_Gate w96 has open pins: in0=w95_out, in1=undriven_16, in2=undriven_14, out=open
  nand w97 (w97_out, w95_out, undriven_16, undriven_15);
  // NAND_Gate w63 has open pins: in0=not_34_out, out=open
  nand w64 (w64_out, w43_out, xor_delay_40x_1_out_2);
  not not_41 (ZA0_out, w65_out);
  not not_42 (w47, w75_out);
  nand w84 (w84_out, dff23_qn, undriven_18, undriven_17);
  D_Flip_Flop dff26 (.D(vd_in[8]), .clk(w97_out), .reset(not_43_out));  // open: Q, Qn, preset
  not not_43 (not_43_out, undriven_19);
  cnt_bit cnt_bit_6 (
    .cin(cnt_bit_4_q), .val(1'b0), .load(nand_1_out), .clk(MCLK), .res(not_18_out), .q(cnt_bit_6_q),
    .nq(cnt_bit_6_nq));  // open: cout
  cnt_bit cnt_bit_7 (
    .cin(cnt_bit_5_cout), .val(1'b0), .load(d_ff_1_q), .clk(not_49_out), .res(not_10_out), .nq(cnt_bit_7_nq));  // open: cout, q
  nand w102 (w102_out, w70_out, w107_out);
  buf w94 (w94_out, as_in);  // OR_Gate
  not not_44 (not_44_out, cnt_bit_6_q);
  not not_45 (w115, w64_out);
  not not_46 (not_46_out, not_44_out);
  not w103 (w103_out, rw_in);  // NOR_Gate
  not not_47 (not_47_out, w73_out);
  not not_48 (not_48_out, not_46_out);
  not not_49 (not_49_out, not_48_out);
  D_Flip_Flop dff24 (.D(w103_out), .clk(VCLK), .Q(dff24_q), .Qn(w120));  // open: preset, reset
  D_Flip_Flop dff25 (.D(dff12_qn), .clk(not_1_out), .reset(not_47_out));  // open: Q, Qn, preset
endmodule

module cnt_bit (
  input  cin,
  input  val,
  input  load,
  input  clk,
  input  res,
  output cout,
  output q,
  output nq
);

  wire multiplexer_1_out, not_1_out, xor_1_out;

  and and_1 (cout, cin, q);
  xor xor_1 (xor_1_out, cin, q);
  not not_1 (not_1_out, res);
  Multiplexer multiplexer_1 (.in0(val), .in1(xor_1_out), .out(multiplexer_1_out), .sel(load));
  D_Flip_Flop d_ff_1 (.D(multiplexer_1_out), .clk(clk), .Q(q), .Qn(nq), .reset(not_1_out));  // open: preset
endmodule

module xor_delay_6x (
  input  in_1,
  output out_2
);

  wire xor_1_out, xor_2_out, xor_3_out, xor_4_out, xor_5_out;

  xor xor_1 (xor_1_out, in_1, 1'b0);
  xor xor_2 (xor_2_out, xor_1_out, 1'b0);
  xor xor_3 (xor_3_out, xor_2_out, 1'b0);
  xor xor_4 (xor_4_out, xor_3_out, 1'b0);
  xor xor_5 (xor_5_out, xor_4_out, 1'b0);
  xor xor_6 (out_2, xor_5_out, 1'b0);
endmodule

module xor_delay_40x (
  input  in_1,
  output out_2
);

  wire xor_1_out, xor_2_out, xor_3_out, xor_4_out, xor_5_out, xor_6_out, xor_7_out, xor_8_out, xor_9_out,
       xor_10_out, xor_11_out, xor_12_out, xor_13_out, xor_14_out, xor_15_out, xor_16_out, xor_17_out,
       xor_18_out, xor_19_out, xor_20_out, xor_21_out, xor_22_out, xor_23_out, xor_24_out, xor_25_out,
       xor_26_out, xor_27_out, xor_28_out, xor_29_out, xor_30_out, xor_31_out, xor_33_out, xor_34_out,
       xor_35_out, xor_36_out, xor_37_out, xor_38_out, xor_39_out, xor_40_out;

  xor xor_1 (xor_1_out, in_1, 1'b0);
  xor xor_2 (xor_2_out, xor_40_out, 1'b0);
  xor xor_3 (xor_3_out, xor_1_out, 1'b0);
  xor xor_4 (xor_4_out, xor_2_out, 1'b0);
  xor xor_5 (xor_5_out, xor_3_out, 1'b0);
  xor xor_6 (xor_6_out, xor_4_out, 1'b0);
  xor xor_7 (xor_7_out, xor_5_out, 1'b0);
  xor xor_8 (xor_8_out, xor_6_out, 1'b0);
  xor xor_9 (xor_9_out, xor_7_out, 1'b0);
  xor xor_10 (xor_10_out, xor_8_out, 1'b0);
  xor xor_11 (xor_11_out, xor_9_out, 1'b0);
  xor xor_12 (xor_12_out, xor_10_out, 1'b0);
  xor xor_13 (xor_13_out, xor_11_out, 1'b0);
  xor xor_14 (xor_14_out, xor_12_out, 1'b0);
  xor xor_15 (xor_15_out, xor_13_out, 1'b0);
  xor xor_16 (xor_16_out, xor_14_out, 1'b0);
  xor xor_17 (xor_17_out, xor_15_out, 1'b0);
  xor xor_18 (xor_18_out, xor_16_out, 1'b0);
  xor xor_19 (xor_19_out, xor_17_out, 1'b0);
  xor xor_20 (xor_20_out, xor_18_out, 1'b0);
  xor xor_21 (xor_21_out, xor_19_out, 1'b0);
  xor xor_22 (xor_22_out, xor_20_out, 1'b0);
  xor xor_23 (xor_23_out, xor_21_out, 1'b0);
  xor xor_24 (xor_24_out, xor_22_out, 1'b0);
  xor xor_25 (xor_25_out, xor_23_out, 1'b0);
  xor xor_26 (xor_26_out, xor_24_out, 1'b0);
  xor xor_27 (xor_27_out, xor_25_out, 1'b0);
  xor xor_28 (xor_28_out, xor_26_out, 1'b0);
  xor xor_29 (xor_29_out, xor_27_out, 1'b0);
  xor xor_30 (xor_30_out, xor_28_out, 1'b0);
  xor xor_31 (xor_31_out, xor_29_out, 1'b0);
  xor xor_32 (out_2, xor_30_out, 1'b0);
  xor xor_33 (xor_33_out, xor_31_out, 1'b0);
  xor xor_34 (xor_34_out, xor_33_out, 1'b0);
  xor xor_35 (xor_35_out, xor_34_out, 1'b0);
  xor xor_36 (xor_36_out, xor_35_out, 1'b0);
  xor xor_37 (xor_37_out, xor_36_out, 1'b0);
  xor xor_38 (xor_38_out, xor_37_out, 1'b0);
  xor xor_39 (xor_39_out, xor_38_out, 1'b0);
  xor xor_40 (xor_40_out, xor_39_out, 1'b0);
endmodule
