// Logisim project iochip.circ as structural Verilog: 4 circuits, main circuit main
module main (
  input  A6i,
  input  B0i,
  input  B2i,
  input  in_4,
  input  A4i,
  input  w2,
  input  A5i,
  input  in_8,
  input  in_9,
  input  TEST,
  input  SRES,
  input  VCLK,
  input  PAL,
  input  C0i,
  input  C1i,
  input  C2i,
  input  C3i,
  input  C4i,
  input  C5i,
  input  C6i,
  output C4o,
  output out_22,
  output C0d,
  output out_24,
  output out_25,
  output out_26,
  output out_27,
  output out_28,
  output out_29,
  output C0o,
  output C1o,
  output C2o,
  output C3o,
  output C5o,
  output C6o
);

  wire and_1_out, and_2_out, and_3_out, and_4_out, and_5_out, and_6_out, and_7_out, and_8_out, and_9_out,
       and_10_out, and_11_out, and_12_out, and_13_out, and_14_out, and_15_out, and_16_out, and_17_out,
       and_18_out, buffer_9_out, buffer_10_out, clk_div_1_out_4, d_ff_1_q, d_ff_1_qn, d_ff_2_q, d_ff_3_q,
       d_ff_4_q, d_ff_5_q, d_ff_6_q, d_ff_15_q, d_ff_16_q, d_ff_17_q, d_ff_18_q, d_ff_19_q, d_ff_20_q,
       d_ff_21_q, d_ff_23_q, d_ff_23_qn, d_ff_24_q, d_ff_24_qn, d_ff_25_qn, d_ff_26_qn, d_ff_27_qn,
       d_ff_28_qn, d_ff_29_qn, d_ff_30_qn, d_ff_31_qn, d_ff_32_qn, d_ff_33_q, d_ff_33_qn, d_ff_34_q,
       d_ff_34_qn, d_ff_35_q, d_ff_35_qn, d_ff_36_q, d_ff_36_qn, d_ff_37_q, d_ff_38_q, d_ff_39_q, d_ff_40_q,
       d_ff_41_q, d_ff_42_q, d_ff_43_q, d_ff_44_q, d_ff_45_q, d_ff_45_qn, d_ff_46_q, d_ff_46_qn, d_ff_47_q,
       d_ff_47_qn, d_ff_48_qn, d_ff_49_q, d_ff_49_qn, d_ff_50_q, d_ff_51_q, d_ff_51_qn, d_ff_52_q,
       d_ff_52_qn, d_ff_53_q, d_ff_53_qn, d_ff_54_q, d_ff_54_qn, d_ff_55_q, d_ff_55_qn, d_ff_56_q, d_ff_57_q,
       d_ff_58_q, d_ff_58_qn, d_ff_59_q, d_ff_60_q, d_ff_60_qn, d_ff_61_q, d_ff_62_q, d_ff_62_qn, d_ff_63_q,
       d_ff_65_q, d_ff_68_q, d_ff_70_q, d_ff_71_q, d_ff_71_qn, d_ff_73_q, d_ff_74_q, d_ff_74_qn, d_ff_76_q,
       d_ff_78_q, d_ff_79_q, d_ff_79_qn, d_ff_81_q, d_ff_82_q, d_ff_82_qn, d_ff_84_q, multiplexer_6_out,
       multiplexer_7_out, multiplexer_8_out, multiplexer_9_out, multiplexer_10_out, multiplexer_11_out,
       multiplexer_12_out, multiplexer_13_out, multiplexer_14_out, nand_1_out, nand_2_out, nand_3_out,
       nand_4_out, nand_5_out, nand_6_out, nand_7_out, nand_8_out, nand_9_out, nand_10_out, nand_11_out,
       nand_12_out, nand_13_out, nand_14_out, nand_15_out, nand_16_out, nand_17_out, nand_18_out,
       nand_19_out, nand_20_out, nand_21_out, nand_22_out, nand_23_out, nand_24_out, nand_25_out,
       nand_26_out, nand_27_out, nand_28_out, nand_29_out, nand_30_out, nand_31_out, nand_32_out,
       nand_33_out, nand_34_out, nand_35_out, nand_36_out, nand_37_out, nand_38_out, nand_39_out,
       nand_40_out, nand_41_out, nor_1_out, nor_2_out, nor_3_out, nor_4_out, nor_5_out, not_1_out, not_2_out,
       not_3_out, not_4_out, not_5_out, not_6_out, not_7_out, not_8_out, not_9_out, not_10_out, not_11_out,
       not_12_out, not_13_out, not_14_out, not_15_out, not_16_out, not_17_out, not_18_out, not_19_out,
       not_20_out, not_21_out, not_22_out, not_23_out, not_24_out, not_25_out, not_26_out, not_27_out,
       not_28_out, not_29_out, not_30_out, not_31_out, not_32_out, not_33_out, not_34_out, not_35_out,
       not_36_out, not_37_out, not_38_out, not_39_out, not_40_out, not_41_out, not_42_out, not_43_out,
       not_44_out, not_45_out, or_1_out, or_2_out, or_3_out, or_4_out, or_5_out, or_6_out, or_7_out,
       or_8_out, undriven_3, undriven_4, undriven_5, undriven_7, undriven_8, undriven_9, undriven_10,
       undriven_11, xor_delay_6x_1_out_2, xor_delay_6x_2_out_2, xor_delay_6x_3_out_2, xor_delay_6x_4_out_2,
       xor_delay_6x_5_out_2, xor_delay_6x_6_out_2, xor_delay_6x_7_out_2, xor_delay_6x_8_out_2;
  wire [7:0] buffer_1_out, d_ff_7_q, d_ff_83_q, undriven, undriven_2, undriven_6;

  buf buffer_1 (buffer_1_out[0], C0i);
  buf buffer_2 (buffer_1_out[1], C1i);
  buf buffer_3 (buffer_1_out[2], C2i);
  buf buffer_4 (buffer_1_out[3], C3i);
  buf buffer_5 (buffer_1_out[4], C4i);
  buf buffer_6 (buffer_1_out[5], C5i);
  buf buffer_7 (buffer_1_out[6], C6i);
  Multiplexer multiplexer_1 (.in0(B0i), .in1(A6i), .sel(w2));  // open: out
  Multiplexer multiplexer_2 (.in0(A4i), .in1(A4i), .sel(w2));  // open: out
  buf and_1 (and_1_out, A5i);  // AND_Gate
  not not_1 (not_1_out, in_9);
  D_Flip_Flop d_ff_1 (.D(SRES), .clk(VCLK), .Q(d_ff_1_q), .Qn(d_ff_1_qn));  // open: preset, reset
  not not_2 (not_2_out, PAL);
  Multiplexer multiplexer_3 (.in0(B2i), .in1(in_4), .sel(w2));  // open: out
  D_Flip_Flop d_ff_2 (.D(undriven_6[3]), .clk(undriven_3), .Q(d_ff_2_q), .reset(not_3_out));  // open: Qn, preset
  D_Flip_Flop d_ff_3 (.D(undriven_6[4]), .clk(undriven_3), .Q(d_ff_3_q), .reset(not_3_out));  // open: Qn, preset
  D_Flip_Flop d_ff_4 (.D(undriven_6[5]), .clk(undriven_3), .Q(d_ff_4_q), .reset(not_3_out));  // open: Qn, preset
  D_Flip_Flop d_ff_5 (.D(undriven_6[6]), .clk(undriven_3), .Q(d_ff_5_q), .reset(not_3_out));  // open: Qn, preset
  D_Flip_Flop d_ff_6 (.D(undriven_6[7]), .clk(undriven_3), .Q(d_ff_6_q), .reset(not_3_out));  // open: Qn, preset
  not not_3 (not_3_out, in_8);
  not not_4 (not_4_out, multiplexer_14_out);
  not not_5 (not_5_out, d_ff_46_q);
  D_Flip_Flop d_ff_7 (.D(undriven_2[0]), .clk(undriven_5), .Q(d_ff_7_q[0]), .reset(not_7_out));  // open: Qn, preset
  D_Flip_Flop d_ff_8 (.D(undriven_2[1]), .clk(undriven_5), .Q(d_ff_7_q[1]), .reset(not_7_out));  // open: Qn, preset
  D_Flip_Flop d_ff_9 (.D(undriven_2[2]), .clk(undriven_5), .Q(d_ff_7_q[2]), .reset(not_7_out));  // open: Qn, preset
  D_Flip_Flop d_ff_10 (.D(undriven_2[3]), .clk(undriven_5), .Q(d_ff_7_q[3]), .reset(not_7_out));  // open: Qn, preset
  D_Flip_Flop d_ff_11 (.D(undriven_2[4]), .clk(undriven_5), .Q(d_ff_7_q[4]), .reset(not_7_out));  // open: Qn, preset
  D_Flip_Flop d_ff_12 (.D(undriven_2[5]), .clk(undriven_5), .Q(d_ff_7_q[5]), .reset(not_7_out));  // open: Qn, preset
  D_Flip_Flop d_ff_13 (.D(undriven_2[6]), .clk(undriven_5), .Q(d_ff_7_q[6]), .reset(not_7_out));  // open: Qn, preset
  D_Flip_Flop d_ff_14 (.D(undriven_2[7]), .clk(undriven_5), .Q(d_ff_7_q[7]), .reset(not_7_out));  // open: Qn, preset
  D_Flip_Flop d_ff_15 (.D(undriven[0]), .clk(undriven_4), .Q(d_ff_15_q), .reset(not_6_out));  // open: Qn, preset
  D_Flip_Flop d_ff_16 (.D(undriven[1]), .clk(undriven_4), .Q(d_ff_16_q), .reset(not_6_out));  // open: Qn, preset
  D_Flip_Flop d_ff_17 (.D(undriven[2]), .clk(undriven_4), .Q(d_ff_17_q), .reset(not_6_out));  // open: Qn, preset
  D_Flip_Flop d_ff_18 (.D(undriven[3]), .clk(undriven_4), .Q(d_ff_18_q), .reset(not_6_out));  // open: Qn, preset
  D_Flip_Flop d_ff_19 (.D(undriven[4]), .clk(undriven_4), .Q(d_ff_19_q), .reset(not_6_out));  // open: Qn, preset
  D_Flip_Flop d_ff_20 (.D(undriven[5]), .clk(undriven_4), .Q(d_ff_20_q), .reset(not_6_out));  // open: Qn, preset
  D_Flip_Flop d_ff_21 (.D(undriven[6]), .clk(undriven_4), .Q(d_ff_21_q), .reset(not_6_out));  // open: Qn, preset
  D_Flip_Flop d_ff_22 (.D(undriven[7]), .clk(undriven_4), .Q(buffer_1_out[7]), .reset(not_6_out));  // open: Qn, preset
  // NOT_Gate not_6 has open pins: in=open, out=not_6_out
  Multiplexer multiplexer_4 (.in0(and_1_out), .in1(A5i), .sel(w2));  // open: out
  D_Flip_Flop d_ff_23 (
    .D(d_ff_23_qn), .clk(not_4_out), .Q(d_ff_23_q), .Qn(d_ff_23_qn), .reset(not_1_out));  // open: preset
  D_Flip_Flop d_ff_24 (
    .D(d_ff_24_qn), .clk(not_5_out), .Q(d_ff_24_q), .Qn(d_ff_24_qn), .reset(not_1_out));  // open: preset
  buf buffer_8 (out_22, d_ff_1_qn);
  // NOT_Gate not_7 has open pins: in=open, out=not_7_out
  not not_8 (not_8_out, d_ff_5_q);
  buf buffer_9 (buffer_9_out, d_ff_5_q);
  not not_9 (not_9_out, d_ff_6_q);
  buf buffer_10 (buffer_10_out, d_ff_6_q);
  not not_10 (not_10_out, d_ff_23_q);
  not not_11 (not_11_out, d_ff_24_q);
  buf buffer_11 (C0o, d_ff_15_q);
  buf buffer_12 (C1o, d_ff_16_q);
  buf buffer_13 (C2o, d_ff_17_q);
  buf buffer_14 (C3o, d_ff_18_q);
  buf buffer_15 (C5o, d_ff_20_q);
  buf buffer_16 (C6o, d_ff_21_q);
  D_Flip_Flop #(.trigger("high")) d_ff_25 (
    .D(undriven_6[0]), .clk(undriven_7), .Qn(d_ff_25_qn));  // open: Q, preset, reset
  D_Flip_Flop #(.trigger("high")) d_ff_26 (
    .D(undriven_6[1]), .clk(undriven_7), .Qn(d_ff_26_qn));  // open: Q, preset, reset
  D_Flip_Flop #(.trigger("high")) d_ff_27 (
    .D(undriven_6[2]), .clk(undriven_7), .Qn(d_ff_27_qn));  // open: Q, preset, reset
  D_Flip_Flop #(.trigger("high")) d_ff_28 (
    .D(undriven_6[3]), .clk(undriven_7), .Qn(d_ff_28_qn));  // open: Q, preset, reset
  D_Flip_Flop #(.trigger("high")) d_ff_29 (
    .D(undriven_6[4]), .clk(undriven_7), .Qn(d_ff_29_qn));  // open: Q, preset, reset
  D_Flip_Flop #(.trigger("high")) d_ff_30 (
    .D(undriven_6[5]), .clk(undriven_7), .Qn(d_ff_30_qn));  // open: Q, preset, reset
  D_Flip_Flop #(.trigger("high")) d_ff_31 (
    .D(undriven_6[6]), .clk(undriven_7), .Qn(d_ff_31_qn));  // open: Q, preset, reset
  D_Flip_Flop #(.trigger("high")) d_ff_32 (
    .D(undriven_6[7]), .clk(undriven_7), .Qn(d_ff_32_qn));  // open: Q, preset, reset
  D_Flip_Flop d_ff_33 (
    .D(d_ff_33_qn), .clk(not_10_out), .Q(d_ff_33_q), .Qn(d_ff_33_qn), .reset(not_1_out));  // open: preset
  D_Flip_Flop d_ff_34 (
    .D(d_ff_34_qn), .clk(not_11_out), .Q(d_ff_34_q), .Qn(d_ff_34_qn), .reset(not_1_out));  // open: preset
  clk_div clk_div_1 (.VCLK(VCLK), .Reset(d_ff_1_qn), .PAL(not_2_out), .out_4(clk_div_1_out_4));
  not not_12 (not_12_out, d_ff_7_q[7]);
  nor nor_1 (nor_1_out, not_12_out, buffer_1_out[6]);
  and and_2 (and_2_out, multiplexer_14_out, not_8_out, not_9_out);
  and and_3 (and_3_out, d_ff_23_q, buffer_9_out, not_9_out);
  and and_4 (and_4_out, d_ff_33_q, not_8_out, buffer_10_out);
  and and_5 (and_5_out, d_ff_46_q, buffer_9_out, buffer_10_out);
  and and_6 (and_6_out, d_ff_46_q, not_8_out, not_9_out);
  and and_7 (and_7_out, d_ff_24_q, buffer_9_out, not_9_out);
  and and_8 (and_8_out, d_ff_34_q, not_8_out, buffer_10_out);
  and and_9 (and_9_out, d_ff_47_q, buffer_9_out, buffer_10_out);
  not not_13 (not_13_out, d_ff_33_q);
  not not_14 (not_14_out, d_ff_34_q);
  Multiplexer multiplexer_5 (.in0(not_2_out), .in1(clk_div_1_out_4), .sel(TEST));  // open: out
  not not_15 (not_15_out, d_ff_7_q[4]);
  not not_16 (not_16_out, d_ff_7_q[5]);
  Multiplexer multiplexer_6 (.in0(d_ff_25_qn), .in1(d_ff_38_q), .out(multiplexer_6_out), .sel(nand_1_out));
  Multiplexer multiplexer_7 (.in0(d_ff_26_qn), .in1(d_ff_39_q), .out(multiplexer_7_out), .sel(nand_1_out));
  Multiplexer multiplexer_8 (.in0(d_ff_27_qn), .in1(d_ff_40_q), .out(multiplexer_8_out), .sel(nand_1_out));
  Multiplexer multiplexer_9 (.in0(d_ff_28_qn), .in1(d_ff_41_q), .out(multiplexer_9_out), .sel(nand_1_out));
  Multiplexer multiplexer_10 (.in0(d_ff_29_qn), .in1(d_ff_42_q), .out(multiplexer_10_out), .sel(nand_1_out));
  Multiplexer multiplexer_11 (.in0(d_ff_30_qn), .in1(d_ff_43_q), .out(multiplexer_11_out), .sel(nand_1_out));
  Multiplexer multiplexer_12 (.in0(d_ff_31_qn), .in1(d_ff_44_q), .out(multiplexer_12_out), .sel(nand_1_out));
  Multiplexer multiplexer_13 (.in0(d_ff_32_qn), .in1(1'b0), .out(multiplexer_13_out), .sel(nand_1_out));
  D_Flip_Flop d_ff_35 (
    .D(d_ff_35_qn), .clk(not_13_out), .Q(d_ff_35_q), .Qn(d_ff_35_qn), .reset(not_1_out));  // open: preset
  D_Flip_Flop d_ff_36 (
    .D(d_ff_36_qn), .clk(not_14_out), .Q(d_ff_36_q), .Qn(d_ff_36_qn), .reset(not_1_out));  // open: preset
  Multiplexer multiplexer_14 (.in0(clk_div_1_out_4), .in1(VCLK), .out(multiplexer_14_out), .sel(TEST));
  not not_17 (not_17_out, d_ff_7_q[0]);
  not not_18 (not_18_out, d_ff_7_q[1]);
  not not_19 (not_19_out, d_ff_7_q[2]);
  not not_20 (not_20_out, d_ff_7_q[3]);
  and and_10 (and_10_out, not_15_out, not_31_out);
  or or_1 (or_1_out, not_16_out, d_ff_4_q);
  not not_21 (not_21_out, d_ff_7_q[6]);
  D_Flip_Flop d_ff_37 (.D(multiplexer_6_out), .clk(or_2_out), .Q(d_ff_37_q), .reset(not_24_out));  // open: Qn, preset
  D_Flip_Flop d_ff_38 (.D(multiplexer_7_out), .clk(or_2_out), .Q(d_ff_38_q), .reset(not_24_out));  // open: Qn, preset
  D_Flip_Flop d_ff_39 (.D(multiplexer_8_out), .clk(or_2_out), .Q(d_ff_39_q), .reset(not_24_out));  // open: Qn, preset
  D_Flip_Flop d_ff_40 (.D(multiplexer_9_out), .clk(or_2_out), .Q(d_ff_40_q), .reset(not_24_out));  // open: Qn, preset
  D_Flip_Flop d_ff_41 (.D(multiplexer_10_out), .clk(or_2_out), .Q(d_ff_41_q), .reset(not_24_out));  // open: Qn, preset
  D_Flip_Flop d_ff_42 (.D(multiplexer_11_out), .clk(or_2_out), .Q(d_ff_42_q), .reset(not_24_out));  // open: Qn, preset
  D_Flip_Flop d_ff_43 (.D(multiplexer_12_out), .clk(or_2_out), .Q(d_ff_43_q), .reset(not_24_out));  // open: Qn, preset
  D_Flip_Flop d_ff_44 (.D(multiplexer_13_out), .clk(or_2_out), .Q(d_ff_44_q), .reset(not_24_out));  // open: Qn, preset
  buf or_2 (or_2_out, or_4_out);  // OR_Gate
  or or_3 (or_3_out, and_2_out, and_3_out, and_4_out, and_5_out);
  or or_4 (or_4_out, and_6_out, and_7_out, and_8_out, and_9_out);
  buf buffer_17 (C0d, not_17_out);
  buf buffer_18 (out_24, not_18_out);
  buf buffer_19 (out_25, not_19_out);
  buf buffer_20 (out_26, not_20_out);
  buf buffer_21 (out_27, and_10_out);
  buf buffer_22 (out_28, or_1_out);
  buf buffer_23 (out_29, not_21_out);
  not not_22 (not_22_out, d_ff_35_q);
  not not_23 (not_23_out, d_ff_36_q);
  not not_24 (not_24_out, d_ff_3_q);
  not not_25 (not_25_out, d_ff_37_q);
  D_Flip_Flop d_ff_45 (
    .D(nand_16_out), .clk(or_4_out), .Q(d_ff_45_q), .Qn(d_ff_45_qn), .reset(not_26_out));  // open: preset
  not not_26 (not_26_out, d_ff_1_q);
  or or_5 (or_5_out, d_ff_52_q, nor_5_out);
  or or_6 (or_6_out, nor_5_out, d_ff_48_qn);
  D_Flip_Flop d_ff_46 (
    .D(d_ff_46_qn), .clk(not_22_out), .Q(d_ff_46_q), .Qn(d_ff_46_qn), .reset(not_1_out));  // open: preset
  D_Flip_Flop d_ff_47 (
    .D(d_ff_47_qn), .clk(not_23_out), .Q(d_ff_47_q), .Qn(d_ff_47_qn), .reset(not_1_out));  // open: preset
  nand nand_1 (nand_1_out, d_ff_59_q, 1'b1, d_ff_54_qn, d_ff_49_qn, d_ff_51_qn, d_ff_45_qn);
  nand nand_2 (nand_2_out, d_ff_54_q, d_ff_45_qn);
  nand nand_3 (nand_3_out, d_ff_54_qn, d_ff_59_q, d_ff_45_qn);
  nand nand_4 (nand_4_out, d_ff_54_q, d_ff_49_q, d_ff_45_q);
  nand nand_5 (nand_5_out, d_ff_45_q, d_ff_49_q);
  nand nand_6 (nand_6_out, d_ff_49_q, d_ff_54_q, d_ff_51_q);
  nand nand_7 (nand_7_out, d_ff_54_q, d_ff_51_q, d_ff_45_q);
  nand nand_8 (nand_8_out, d_ff_54_q, d_ff_45_q);
  nand nand_9 (nand_9_out, d_ff_54_q, d_ff_49_q);
  D_Flip_Flop d_ff_48 (.D(nand_10_out), .clk(or_3_out), .Qn(d_ff_48_qn), .reset(not_29_out));  // open: Q, preset
  nand nand_10 (nand_10_out, or_5_out, or_6_out);
  not not_27 (not_27_out, nand_1_out);
  and and_11 (and_11_out, not_25_out, nand_1_out);
  D_Flip_Flop d_ff_49 (
    .D(nand_17_out), .clk(or_4_out), .Q(d_ff_49_q), .Qn(d_ff_49_qn), .reset(not_26_out));  // open: preset
  nand nand_11 (nand_11_out, d_ff_49_qn, d_ff_45_qn, d_ff_51_q, d_ff_54_q);
  not not_28 (not_28_out, d_ff_52_q);
  and and_12 (and_12_out, not_27_out, d_ff_53_q);
  nor nor_2 (nor_2_out, d_ff_53_q, undriven_10);
  D_Flip_Flop d_ff_50 (.D(and_11_out), .clk(or_4_out), .Q(d_ff_50_q), .preset(not_24_out));  // open: Qn, reset
  not not_29 (not_29_out, d_ff_1_q);
  not not_30 (not_30_out, and_17_out);
  nor nor_3 (nor_3_out, and_18_out, nor_1_out);
  nor nor_4 (nor_4_out, and_12_out, nor_2_out);
  not not_31 (not_31_out, d_ff_3_q);
  D_Flip_Flop d_ff_51 (
    .D(nand_18_out), .clk(or_4_out), .Q(d_ff_51_q), .Qn(d_ff_51_qn), .reset(not_26_out));  // open: preset
  D_Flip_Flop d_ff_52 (
    .D(nand_29_out), .clk(or_3_out), .Q(d_ff_52_q), .Qn(d_ff_52_qn), .preset(not_29_out));  // open: reset
  nor nor_5 (nor_5_out, d_ff_48_qn, not_30_out, d_ff_62_q);
  nand nand_12 (nand_12_out, d_ff_55_q, d_ff_58_q);
  not not_32 (not_32_out, or_4_out);
  and and_13 (and_13_out, d_ff_50_q, d_ff_3_q);
  and and_14 (and_14_out, not_31_out, d_ff_19_q);
  not not_33 (not_33_out, nor_5_out);
  nand nand_13 (nand_13_out, d_ff_55_q, d_ff_60_qn);
  nand nand_14 (nand_14_out, d_ff_60_qn, d_ff_58_q);
  nand nand_15 (nand_15_out, d_ff_58_qn, d_ff_60_q, d_ff_55_qn);
  not not_34 (not_34_out, undriven_8);
  D_Flip_Flop d_ff_53 (
    .D(nor_4_out), .clk(not_35_out), .Q(d_ff_53_q), .Qn(d_ff_53_qn), .preset(not_34_out), .reset(not_36_out));
  not not_35 (not_35_out, not_32_out);
  not not_36 (not_36_out, undriven_9);
  or or_7 (or_7_out, and_13_out, and_14_out);
  D_Flip_Flop d_ff_54 (
    .D(nand_19_out), .clk(or_4_out), .Q(d_ff_54_q), .Qn(d_ff_54_qn), .reset(not_26_out));  // open: preset
  nand nand_16 (nand_16_out, nand_2_out, nand_3_out, nand_4_out);
  nand nand_17 (nand_17_out, nand_3_out, nand_5_out, nand_11_out);
  nand nand_18 (nand_18_out, nand_3_out, nand_4_out, nand_6_out, nand_7_out);
  nand nand_19 (nand_19_out, nand_5_out, nand_11_out, nand_8_out, nand_9_out);
  nand nand_20 (nand_20_out, d_ff_54_q, d_ff_51_qn, d_ff_49_qn, d_ff_45_qn);
  D_Flip_Flop d_ff_55 (
    .D(nand_21_out), .clk(or_3_out), .Q(d_ff_55_q), .Qn(d_ff_55_qn), .preset(not_29_out));  // open: reset
  nand nand_21 (nand_21_out, not_33_out, nand_12_out, nand_15_out, nand_13_out);
  nand nand_22 (nand_22_out, nand_14_out, not_33_out, nand_24_out);
  nand nand_23 (nand_23_out, d_ff_60_q, nor_5_out);
  nand nand_24 (nand_24_out, d_ff_60_q, d_ff_58_qn);
  nand nand_25 (nand_25_out, d_ff_58_qn, d_ff_60_q, d_ff_55_qn, not_28_out);
  nand nand_26 (nand_26_out, d_ff_52_q, d_ff_55_q);
  nand nand_27 (nand_27_out, d_ff_52_q, d_ff_60_qn);
  nand nand_28 (nand_28_out, d_ff_52_q, d_ff_58_q);
  not not_37 (not_37_out, d_ff_53_qn);
  D_Flip_Flop d_ff_56 (
    .D(undriven_10), .clk(d_ff_57_q), .Q(d_ff_56_q), .preset(not_37_out), .reset(not_38_out));  // open: Qn
  not not_38 (not_38_out, undriven_11);
  buf buffer_24 (C4o, or_7_out);
  D_Flip_Flop d_ff_57 (.D(nand_20_out), .clk(or_4_out), .Q(d_ff_57_q), .preset(not_26_out));  // open: Qn, reset
  D_Flip_Flop d_ff_58 (
    .D(nand_23_out), .clk(or_3_out), .Q(d_ff_58_q), .Qn(d_ff_58_qn), .preset(not_29_out));  // open: reset
  nand nand_29 (nand_29_out, nand_25_out, 1'b1, not_33_out, nand_26_out, nand_27_out, nand_28_out);
  // AND_Gate and_15 has open pins: out=and_15_out
  D_Flip_Flop d_ff_59 (.D(d_ff_56_q), .clk(or_3_out), .Q(d_ff_59_q));  // open: Qn, preset, reset
  D_Flip_Flop d_ff_60 (
    .D(nand_22_out), .clk(or_3_out), .Q(d_ff_60_q), .Qn(d_ff_60_qn), .reset(not_29_out));  // open: preset
  not not_39 (not_39_out, d_ff_4_q);
  not not_40 (not_40_out, and_15_out);
  not not_41 (not_41_out, 1'b1);
  and and_16 (and_16_out, d_ff_62_q, 1'b1);
  D_Flip_Flop d_ff_61 (.D(and_16_out), .clk(d_ff_52_qn), .Q(d_ff_61_q), .reset(not_42_out));  // open: Qn, preset
  D_Flip_Flop d_ff_62 (
    .D(buffer_1_out[5]), .clk(or_3_out), .Q(d_ff_62_q), .Qn(d_ff_62_qn), .preset(not_39_out));  // open: reset
  D_Flip_Flop d_ff_63 (.D(1'b1), .clk(or_8_out), .Q(d_ff_63_q), .reset(not_40_out));  // open: Qn, preset
  D_Flip_Flop d_ff_64 (
    .D(xor_delay_6x_1_out_2), .clk(or_8_out), .Q(d_ff_83_q[7]), .reset(not_41_out));  // open: Qn, preset
  D_Flip_Flop d_ff_65 (.D(d_ff_61_q), .clk(d_ff_52_qn), .Q(d_ff_65_q), .reset(not_42_out));  // open: Qn, preset
  not not_42 (not_42_out, d_ff_4_q);
  nand nand_30 (nand_30_out, d_ff_71_q, d_ff_82_q);
  D_Flip_Flop d_ff_66 (.D(d_ff_62_qn), .clk(or_8_out), .reset(not_40_out));  // open: Q, Qn, preset
  xor_delay_6x xor_delay_6x_1 (.in_1(d_ff_61_q), .out_2(xor_delay_6x_1_out_2));
  nand nand_31 (nand_31_out, d_ff_71_qn, d_ff_82_qn, d_ff_48_qn, not_43_out);
  nand nand_32 (nand_32_out, d_ff_71_q, d_ff_74_q, d_ff_79_qn, d_ff_82_qn);
  not not_43 (not_43_out, d_ff_62_q);
  D_Flip_Flop d_ff_67 (
    .D(xor_delay_6x_2_out_2), .clk(or_8_out), .Q(d_ff_83_q[6]), .reset(not_41_out));  // open: Qn, preset
  xor_delay_6x xor_delay_6x_2 (.in_1(d_ff_65_q), .out_2(xor_delay_6x_2_out_2));
  D_Flip_Flop d_ff_68 (.D(d_ff_65_q), .clk(d_ff_52_qn), .Q(d_ff_68_q), .reset(not_42_out));  // open: Qn, preset
  not not_44 (not_44_out, d_ff_1_q);
  nand nand_33 (nand_33_out, nand_31_out, nand_32_out, nand_34_out, nand_30_out);
  and and_17 (and_17_out, d_ff_71_qn, d_ff_82_qn);
  nand nand_34 (nand_34_out, d_ff_79_q, d_ff_82_qn, d_ff_71_q);
  nand nand_35 (nand_35_out, d_ff_71_q, d_ff_82_qn, d_ff_74_qn);
  nand nand_36 (nand_36_out, d_ff_71_q, d_ff_79_q, d_ff_82_q);
  nand nand_37 (nand_37_out, d_ff_79_q, d_ff_71_q, d_ff_74_q);
  nand nand_38 (nand_38_out, d_ff_82_q, d_ff_71_q, d_ff_74_q);
  and and_18 (and_18_out, d_ff_63_q, d_ff_2_q);
  D_Flip_Flop d_ff_69 (
    .D(xor_delay_6x_3_out_2), .clk(or_8_out), .Q(d_ff_83_q[5]), .reset(not_41_out));  // open: Qn, preset
  xor_delay_6x xor_delay_6x_3 (.in_1(d_ff_68_q), .out_2(xor_delay_6x_3_out_2));
  D_Flip_Flop d_ff_70 (.D(d_ff_68_q), .clk(d_ff_52_qn), .Q(d_ff_70_q), .reset(not_42_out));  // open: Qn, preset
  D_Flip_Flop d_ff_71 (
    .D(nand_33_out), .clk(d_ff_52_qn), .Q(d_ff_71_q), .Qn(d_ff_71_qn), .reset(not_44_out));  // open: preset
  nand nand_39 (nand_39_out, nand_32_out, nand_31_out, nand_34_out, nand_35_out);
  nand nand_40 (nand_40_out, nand_35_out, nand_31_out, nand_32_out, nand_36_out);
  nand nand_41 (nand_41_out, nand_35_out, nand_31_out, nand_37_out, nand_38_out);
  D_Flip_Flop d_ff_72 (
    .D(xor_delay_6x_4_out_2), .clk(or_8_out), .Q(d_ff_83_q[4]), .reset(not_41_out));  // open: Qn, preset
  xor_delay_6x xor_delay_6x_4 (.in_1(d_ff_70_q), .out_2(xor_delay_6x_4_out_2));
  D_Flip_Flop d_ff_73 (.D(d_ff_70_q), .clk(d_ff_52_qn), .Q(d_ff_73_q), .reset(not_45_out));  // open: Qn, preset
  D_Flip_Flop d_ff_74 (
    .D(nand_41_out), .clk(d_ff_52_qn), .Q(d_ff_74_q), .Qn(d_ff_74_qn), .reset(not_44_out));  // open: preset
  D_Flip_Flop d_ff_75 (
    .D(xor_delay_6x_5_out_2), .clk(or_8_out), .Q(d_ff_83_q[3]), .reset(not_41_out));  // open: Qn, preset
  D_Flip_Flop d_ff_76 (.D(d_ff_73_q), .clk(d_ff_52_qn), .Q(d_ff_76_q), .reset(not_45_out));  // open: Qn, preset
  not not_45 (not_45_out, d_ff_4_q);
  D_Flip_Flop d_ff_77 (
    .D(xor_delay_6x_6_out_2), .clk(or_8_out), .Q(d_ff_83_q[2]), .reset(not_41_out));  // open: Qn, preset
  xor_delay_6x xor_delay_6x_5 (.in_1(d_ff_73_q), .out_2(xor_delay_6x_5_out_2));
  D_Flip_Flop d_ff_78 (.D(d_ff_76_q), .clk(d_ff_52_qn), .Q(d_ff_78_q), .reset(not_45_out));  // open: Qn, preset
  D_Flip_Flop d_ff_79 (
    .D(nand_40_out), .clk(d_ff_52_qn), .Q(d_ff_79_q), .Qn(d_ff_79_qn), .reset(not_44_out));  // open: preset
  xor_delay_6x xor_delay_6x_6 (.in_1(d_ff_76_q), .out_2(xor_delay_6x_6_out_2));
  D_Flip_Flop d_ff_80 (
    .D(xor_delay_6x_7_out_2), .clk(or_8_out), .Q(d_ff_83_q[1]), .reset(not_41_out));  // open: Qn, preset
  xor_delay_6x xor_delay_6x_7 (.in_1(d_ff_78_q), .out_2(xor_delay_6x_7_out_2));
  D_Flip_Flop d_ff_81 (.D(d_ff_78_q), .clk(d_ff_52_qn), .Q(d_ff_81_q), .reset(not_45_out));  // open: Qn, preset
  D_Flip_Flop d_ff_82 (
    .D(nand_39_out), .clk(d_ff_52_qn), .Q(d_ff_82_q), .Qn(d_ff_82_qn), .reset(not_44_out));  // open: preset
  D_Flip_Flop d_ff_83 (
    .D(xor_delay_6x_8_out_2), .clk(or_8_out), .Q(d_ff_83_q[0]), .reset(not_41_out));  // open: Qn, preset
  xor_delay_6x xor_delay_6x_8 (.in_1(d_ff_81_q), .out_2(xor_delay_6x_8_out_2));
  D_Flip_Flop d_ff_84 (.D(nand_35_out), .clk(d_ff_52_qn), .Q(d_ff_84_q), .preset(not_44_out));  // open: Qn, reset
  or or_8 (or_8_out, d_ff_84_q, d_ff_52_qn);

  // Notes on the sheet:
  //   w5
endmodule

module cnt_bit (
  input  cin,
  input  val,
  input  load,
  input  clk,
  input  res,
  output cout,
  output q,
  output nq
);

  wire multiplexer_1_out, not_1_out, xor_1_out;

  and and_1 (cout, cin, q);
  xor xor_1 (xor_1_out, cin, q);
  not not_1 (not_1_out, res);
  Multiplexer multiplexer_1 (.in0(val), .in1(xor_1_out), .out(multiplexer_1_out), .sel(load));
  D_Flip_Flop d_ff_1 (.D(multiplexer_1_out), .clk(clk), .Q(q), .Qn(nq), .reset(not_1_out));  // open: preset
endmodule

module clk_div (
  input  VCLK,
  input  Reset,
  input  PAL,
  output out_4
);

  wire and_1_out, and_2_out, and_3_out, and_4_out, cnt_bit_1_cout, cnt_bit_1_nq, cnt_bit_2_cout,
       cnt_bit_2_nq, cnt_bit_3_cout, cnt_bit_3_nq, cnt_bit_4_cout, cnt_bit_4_nq, cnt_bit_5_cout,
       cnt_bit_5_nq, cnt_bit_6_cout, cnt_bit_6_nq, cnt_bit_7_nq, cnt_bit_8_nq, nor_1_out, nor_2_out,
       nor_3_out;

  and and_1 (and_1_out, nor_3_out, 1'b1, and_4_out);
  and and_2 (and_2_out, nor_3_out, 1'b1, 1'b1);
  cnt_bit cnt_bit_1 (
    .cin(and_1_out), .val(1'b1), .load(nor_3_out), .clk(VCLK), .res(1'b1), .cout(cnt_bit_1_cout),
    .nq(cnt_bit_1_nq));  // open: q
  cnt_bit cnt_bit_2 (
    .cin(and_2_out), .val(PAL), .load(nor_3_out), .clk(VCLK), .res(1'b1), .cout(cnt_bit_2_cout),
    .nq(cnt_bit_2_nq));  // open: q
  nor nor_1 (nor_1_out, cnt_bit_1_nq, cnt_bit_3_nq, cnt_bit_5_nq, cnt_bit_7_nq);
  nor nor_2 (nor_2_out, cnt_bit_2_nq, cnt_bit_8_nq, cnt_bit_6_nq, cnt_bit_4_nq);
  cnt_bit cnt_bit_3 (
    .cin(cnt_bit_1_cout), .val(1'b0), .load(nor_3_out), .clk(VCLK), .res(1'b1), .cout(cnt_bit_3_cout),
    .nq(cnt_bit_3_nq));  // open: q
  and and_3 (and_3_out, nor_1_out, and_4_out);
  cnt_bit cnt_bit_4 (
    .cin(cnt_bit_2_cout), .val(1'b0), .load(nor_3_out), .clk(VCLK), .res(1'b1), .cout(cnt_bit_4_cout),
    .nq(cnt_bit_4_nq));  // open: q
  and and_4 (and_4_out, nor_2_out, 1'b1);
  nor nor_3 (nor_3_out, Reset, and_3_out);
  cnt_bit cnt_bit_5 (
    .cin(cnt_bit_3_cout), .val(1'b0), .load(nor_3_out), .clk(VCLK), .res(1'b1), .cout(cnt_bit_5_cout),
    .q(out_4), .nq(cnt_bit_5_nq));
  cnt_bit cnt_bit_6 (
    .cin(cnt_bit_4_cout), .val(1'b1), .load(nor_3_out), .clk(VCLK), .res(1'b1), .cout(cnt_bit_6_cout),
    .nq(cnt_bit_6_nq));  // open: q
  cnt_bit cnt_bit_7 (
    .cin(cnt_bit_5_cout), .val(1'b1), .load(nor_3_out), .clk(VCLK), .res(1'b1), .nq(cnt_bit_7_nq));  // open: cout, q
  cnt_bit cnt_bit_8 (
    .cin(cnt_bit_6_cout), .val(1'b1), .load(nor_3_out), .clk(VCLK), .res(1'b1), .nq(cnt_bit_8_nq));  // open: cout, q
endmodule

module xor_delay_6x (
  input  in_1,
  output out_2
);

  wire xor_1_out, xor_2_out, xor_3_out, xor_4_out, xor_5_out;

  xor xor_1 (xor_1_out, in_1, 1'b0);
  xor xor_2 (xor_2_out, xor_1_out, 1'b0);
  xor xor_3 (xor_3_out, xor_2_out, 1'b0);
  xor xor_4 (xor_4_out, xor_3_out, 1'b0);
  xor xor_5 (xor_5_out, xor_4_out, 1'b0);
  xor xor_6 (out_2, xor_5_out, 1'b0);
endmodule
