// Logisim project YM3438.circ as structural Verilog: 9 circuits, main circuit main
module main (
  input  M,
  input  in_2,
  input  in_3,
  input  in_4,
  input  in_5,
  input  in_6
);

  wire C1, C2, clock_1_out, clock_2_g_15, FCLK1, FCLK2, fsm_1_g_66, fsm_1_g_67, fsm_1_g_68, fsm_1_g_69,
       fsm_1_g_74, fsm_1_g_75, fsm_1_g_77, fsm_1_g_79, fsm_1_g_100, fsm_1_g_109, fsm_1_g_114, fsm_1_g_118,
       fsm_1_g_122, fsm_1_g_123, fsm_1_g_124, fsm_1_g_125, fsm_1_g_127, nFCLK1, nFCLK2;

  Clock clock_1 (.out(clock_1_out));
  CLOCK clock_2 (
    .M(clock_1_out), .g_932(in_2), .g_15(clock_2_g_15), .FCLK1(FCLK1), .nFCLK1(nFCLK1), .FCLK2(FCLK2),
    .nFCLK2(nFCLK2), .C2(C2), .C1(C1));
  FSM fsm_1 (
    .C2(C2), .C1(C1), .FCLK2(FCLK2), .FCLK1(FCLK1), .g_15(clock_2_g_15), .g_77(fsm_1_g_77),
    .g_118(fsm_1_g_118), .g_123(fsm_1_g_123), .g_114(fsm_1_g_114), .g_127(fsm_1_g_127), .g_122(fsm_1_g_122),
    .g_124(fsm_1_g_124), .g_75(fsm_1_g_75), .g_79(fsm_1_g_79), .g_109(fsm_1_g_109), .g_74(fsm_1_g_74),
    .g_3080(in_3), .g_3079(in_4), .g_3078(in_5), .g_345(in_6), .g_125(fsm_1_g_125), .g_69(fsm_1_g_69),
    .g_66(fsm_1_g_66), .g_67(fsm_1_g_67), .g_68(fsm_1_g_68), .g_100(fsm_1_g_100));
endmodule

module CLOCK (
  input  M,
  input  g_932,
  output C2,
  output C1,
  output g_15,
  output FCLK1,
  output nFCLK1,
  output FCLK2,
  output nFCLK2
);

  wire _1_out, _3_out, _16_out, _20_out, _24_out, _25_out, not_1_out, not_2_out, not_3_out, not_4_out,
       not_5_out, not_6_out, not_7_out, not_8_out, not_10_out, not_11_out, not_12_out, not_13_out,
       not_15_out, not_16_out, not_17_out, not_18_out, not_19_out, not_20_out, not_22_out, not_24_out,
       not_27_out, sdelay12_1_q, sr_bit_1_q, sr_bit_2_q, sr_bit_3_q, sr_bit_4_q, sr_bit_5_q, sr_bit_6_q,
       sr_bit_7_q, sr_bit_8_q;

  not not_1 (not_1_out, M);
  not not_2 (not_2_out, g_932);
  SR_BIT sr_bit_1 (.C2(C2), .C1(C1), .D(_16_out), .Q(sr_bit_1_q));  // open: nQ
  nor _1 (_1_out, not_1_out, not_12_out);
  nor _3 (_3_out, not_11_out, M);
  not not_3 (not_3_out, _1_out);
  not not_4 (not_4_out, not_5_out);
  not not_5 (not_5_out, _1_out);
  not not_6 (not_6_out, _3_out);
  not not_7 (not_7_out, not_6_out);
  not not_8 (not_8_out, _3_out);
  not not_9 (C2, not_3_out);
  not not_10 (not_10_out, not_4_out);
  not not_11 (not_11_out, not_10_out);
  not not_12 (not_12_out, not_13_out);
  not not_13 (not_13_out, not_7_out);
  not not_14 (C1, not_8_out);
  SDELAY12 sdelay12_1 (.C2(C2), .C1(C1), .D(not_2_out), .Q(sdelay12_1_q));
  SR_BIT sr_bit_2 (.C2(C2), .C1(C1), .D(sr_bit_1_q), .Q(sr_bit_2_q));  // open: nQ
  SR_BIT sr_bit_3 (.C2(C2), .C1(C1), .D(sr_bit_2_q), .Q(sr_bit_3_q));  // open: nQ
  not not_15 (not_15_out, sdelay12_1_q);
  and _15 (g_15, not_15_out, not_2_out);
  SR_BIT sr_bit_4 (.C2(C2), .C1(C1), .D(sr_bit_3_q), .Q(sr_bit_4_q));  // open: nQ
  SR_BIT sr_bit_5 (.C2(C2), .C1(C1), .D(sr_bit_4_q), .Q(sr_bit_5_q));  // open: nQ
  or _25 (_25_out, sr_bit_6_q, sr_bit_1_q);
  or _24 (_24_out, sr_bit_4_q, sr_bit_3_q);
  or _20 (_20_out, sr_bit_1_q, sr_bit_2_q, sr_bit_3_q, sr_bit_4_q, sr_bit_5_q);
  SR_BIT sr_bit_6 (.C2(C2), .C1(C1), .D(sr_bit_5_q), .Q(sr_bit_6_q));  // open: nQ
  SR_BIT sr_bit_7 (.C2(C2), .C1(C1), .D(_25_out), .Q(sr_bit_7_q));  // open: nQ
  SR_BIT sr_bit_8 (.C2(C2), .C1(C1), .D(_24_out), .Q(sr_bit_8_q));  // open: nQ
  nor _16 (_16_out, g_15, _20_out);
  not not_16 (not_16_out, sr_bit_7_q);
  not not_17 (not_17_out, sr_bit_8_q);
  not not_18 (not_18_out, not_16_out);
  not not_19 (not_19_out, not_17_out);
  not not_20 (not_20_out, not_18_out);
  not not_21 (FCLK1, not_20_out);
  not not_22 (not_22_out, not_16_out);
  not not_23 (nFCLK1, not_22_out);
  not not_24 (not_24_out, not_19_out);
  not not_25 (FCLK2, not_24_out);
  not not_26 (nFCLK2, not_27_out);
  not not_27 (not_27_out, not_17_out);

  // Notes on the sheet:
  //   9
  //   38
  //   17
  //   7A
  //   2
  //   39
  //   7B
  //   /C2
  //   7A
  //   C2
  //   /C1
  //   7B
  //   C1
  //   18
  //   10
  //   19
  //   14
  //   21
  //   22
  //   23
  //   27
  //   26
  //   35
  //   30
  //   35
  //   30
  //   34
  //   33
  //   37
  //   36
  //   29
  //   28
  //   31
  //   32
endmodule

module D_LATCH (
  input  EN,
  input  D,
  output Q,
  output nQ
);

  D_Flip_Flop #(.trigger("high")) d_ff_1 (.clk(EN), .D(D), .Q(Q), .Qn(nQ));  // open: preset, en, reset
endmodule

// SR BIT
module SR_BIT (
  input  C2,
  input  C1,
  input  D,
  output Q,
  output nQ
);

  wire d_latch_1_q;

  D_LATCH d_latch_1 (.EN(C1), .D(D), .Q(d_latch_1_q));  // open: nQ
  D_LATCH d_latch_2 (.EN(C2), .D(d_latch_1_q), .Q(Q), .nQ(nQ));
endmodule

module SDELAY12 (
  input  C2,
  input  C1,
  input  D,
  output Q
);

  wire d_ff_1_q, d_ff_2_q, d_ff_3_q, d_ff_4_q, d_ff_5_q, d_ff_6_q, d_ff_7_q, d_ff_8_q, d_ff_9_q, d_ff_10_q,
       d_ff_11_q, d_ff_12_q, d_ff_13_q, d_ff_14_q, d_ff_15_q, d_ff_16_q, d_ff_17_q, d_ff_18_q, d_ff_19_q,
       d_ff_20_q, d_ff_21_q, d_ff_22_q, d_ff_23_q;

  D_Flip_Flop #(.trigger("high")) d_ff_1 (.clk(C1), .D(D), .Q(d_ff_1_q));  // open: Qn, preset, en, reset
  D_Flip_Flop #(.trigger("high")) d_ff_2 (.clk(C1), .D(d_ff_22_q), .Q(d_ff_2_q));  // open: Qn, preset, en, reset
  D_Flip_Flop #(.trigger("high")) d_ff_3 (.clk(C1), .D(d_ff_23_q), .Q(d_ff_3_q));  // open: Qn, preset, en, reset
  D_Flip_Flop #(.trigger("high")) d_ff_4 (.clk(C2), .D(d_ff_1_q), .Q(d_ff_4_q));  // open: Qn, preset, en, reset
  D_Flip_Flop #(.trigger("high")) d_ff_5 (.clk(C2), .D(d_ff_2_q), .Q(d_ff_5_q));  // open: Qn, preset, en, reset
  D_Flip_Flop #(.trigger("high")) d_ff_6 (.clk(C2), .D(d_ff_3_q), .Q(d_ff_6_q));  // open: Qn, preset, en, reset
  D_Flip_Flop #(.trigger("high")) d_ff_7 (.clk(C1), .D(d_ff_4_q), .Q(d_ff_7_q));  // open: Qn, preset, en, reset
  D_Flip_Flop #(.trigger("high")) d_ff_8 (.clk(C1), .D(d_ff_5_q), .Q(d_ff_8_q));  // open: Qn, preset, en, reset
  D_Flip_Flop #(.trigger("high")) d_ff_9 (.clk(C1), .D(d_ff_6_q), .Q(d_ff_9_q));  // open: Qn, preset, en, reset
  D_Flip_Flop #(.trigger("high")) d_ff_10 (.clk(C2), .D(d_ff_7_q), .Q(d_ff_10_q));  // open: Qn, preset, en, reset
  D_Flip_Flop #(.trigger("high")) d_ff_11 (.clk(C2), .D(d_ff_8_q), .Q(d_ff_11_q));  // open: Qn, preset, en, reset
  D_Flip_Flop #(.trigger("high")) d_ff_12 (.clk(C2), .D(d_ff_9_q), .Q(d_ff_12_q));  // open: Qn, preset, en, reset
  D_Flip_Flop #(.trigger("high")) d_ff_13 (.clk(C1), .D(d_ff_10_q), .Q(d_ff_13_q));  // open: Qn, preset, en, reset
  D_Flip_Flop #(.trigger("high")) d_ff_14 (.clk(C1), .D(d_ff_11_q), .Q(d_ff_14_q));  // open: Qn, preset, en, reset
  D_Flip_Flop #(.trigger("high")) d_ff_15 (.clk(C1), .D(d_ff_12_q), .Q(d_ff_15_q));  // open: Qn, preset, en, reset
  D_Flip_Flop #(.trigger("high")) d_ff_16 (.clk(C2), .D(d_ff_13_q), .Q(d_ff_16_q));  // open: Qn, preset, en, reset
  D_Flip_Flop #(.trigger("high")) d_ff_17 (.clk(C2), .D(d_ff_14_q), .Q(d_ff_17_q));  // open: Qn, preset, en, reset
  D_Flip_Flop #(.trigger("high")) d_ff_18 (.clk(C2), .D(d_ff_15_q), .Q(d_ff_18_q));  // open: Qn, preset, en, reset
  D_Flip_Flop #(.trigger("high")) d_ff_19 (.clk(C1), .D(d_ff_16_q), .Q(d_ff_19_q));  // open: Qn, preset, en, reset
  D_Flip_Flop #(.trigger("high")) d_ff_20 (.clk(C1), .D(d_ff_17_q), .Q(d_ff_20_q));  // open: Qn, preset, en, reset
  D_Flip_Flop #(.trigger("high")) d_ff_21 (.clk(C1), .D(d_ff_18_q), .Q(d_ff_21_q));  // open: Qn, preset, en, reset
  D_Flip_Flop #(.trigger("high")) d_ff_22 (.clk(C2), .D(d_ff_19_q), .Q(d_ff_22_q));  // open: Qn, preset, en, reset
  D_Flip_Flop #(.trigger("high")) d_ff_23 (.clk(C2), .D(d_ff_20_q), .Q(d_ff_23_q));  // open: Qn, preset, en, reset
  D_Flip_Flop #(.trigger("high")) d_ff_24 (.clk(C2), .D(d_ff_21_q), .Q(Q));  // open: Qn, preset, en, reset
endmodule

// CNT BIT
module CNT_BIT (
  input  C2,
  input  C1,
  input  CIN,
  input  RES,
  output Q,
  output nQ,
  output CO
);

  wire and_1_out, d_ff_1_q, not_1_out, xor_1_out;

  not not_1 (not_1_out, RES);
  and and_1 (and_1_out, not_1_out, xor_1_out);
  xor xor_1 (xor_1_out, Q, CIN);
  and and_2 (CO, Q, CIN);
  D_Flip_Flop #(.trigger("high")) d_ff_1 (.clk(C1), .D(and_1_out), .Q(d_ff_1_q));  // open: Qn, preset, en, reset
  D_Flip_Flop #(.trigger("high")) d_ff_2 (.clk(C2), .D(d_ff_1_q), .Q(Q), .Qn(nQ));  // open: preset, en, reset
endmodule

module FSM (
  input  C2,
  input  C1,
  input  FCLK2,
  input  FCLK1,
  input  g_345,
  input  g_3080,
  input  g_3079,
  input  g_3078,
  input  g_15,
  output g_125,
  output g_122,
  output g_123,
  output g_114,
  output g_109,
  output g_77,
  output g_127,
  output g_124,
  output g_118,
  output g_74,
  output g_79,
  output g_100,
  output g_75,
  output g_66,
  output g_69,
  output g_67,
  output g_68
);

  wire _6_out, _47_out, _48_out, _49_out, _50_out, _51_out, _52_out, _53_out, _54_out, _55_out, _56_out,
       _57_out, _58_out, _59_out, _60_out, _61_out, _62_out, _63_out, _64_out, _72_out, _73_out, _76_out,
       _80_out, _81_out, _82_out, _83_out, _84_out, _85_out, _86_out, _87_out, _88_out, _89_out, _90_out,
       _110_out, _113_2_out, _113_3_out, _113_4_out, _113_5_out, _113_out, _115_out, _116_out, _117_out,
       _119_out, _120_out, _121_2_out, _121_3_out, _121_out, _126_2_out, _126_3_out, _126_out, _134_out,
       _135_out, _136_out, _137_out, _138_out, _139_out, _143_out, _144_out, _145_out, _146_out, _147_out,
       _148_out, _149_out, _150_out, _151_out, cnt_bit_1_co, cnt_bit_1_q, cnt_bit_2_q, cnt_bit_3_co,
       cnt_bit_3_q, cnt_bit_4_co, cnt_bit_4_q, cnt_bit_5_q, d_latch_1_nq, d_latch_2_nq, nor_2_out, not_1_out,
       not_2_out, not_3_out, not_4_out, not_5_out, not_6_out, not_7_out, not_8_out, not_9_out, not_10_out,
       not_11_out, not_12_out, not_13_out, not_14_out, not_15_out, not_16_out, not_17_out, not_20_out,
       not_21_out, not_24_out, not_31_out, sr_bit_1_q, sr_bit_2_q, sr_bit_3_q, sr_bit_4_q, sr_bit_5_q;

  not not_1 (not_1_out, g_345);
  or _6 (_6_out, sr_bit_1_q, cnt_bit_2_q);
  SR_BIT sr_bit_1 (.C2(C2), .C1(C1), .D(sr_bit_2_q), .Q(sr_bit_1_q));  // open: nQ
  SR_BIT sr_bit_2 (.C2(C2), .C1(C1), .D(sr_bit_3_q), .Q(sr_bit_2_q));  // open: nQ
  SR_BIT sr_bit_3 (.C2(C2), .C1(C1), .D(sr_bit_4_q), .Q(sr_bit_3_q));  // open: nQ
  SR_BIT sr_bit_4 (.C2(C2), .C1(C1), .D(g_15), .Q(sr_bit_4_q));  // open: nQ
  CNT_BIT cnt_bit_1 (.C2(FCLK2), .C1(FCLK1), .CIN(1'b1), .RES(_6_out), .Q(cnt_bit_1_q), .CO(cnt_bit_1_co));  // open: nQ
  CNT_BIT cnt_bit_2 (.C2(FCLK2), .C1(FCLK1), .CIN(cnt_bit_1_co), .RES(_6_out), .Q(cnt_bit_2_q));  // open: nQ, CO
  CNT_BIT cnt_bit_3 (
    .C2(FCLK2), .C1(FCLK1), .CIN(cnt_bit_2_q), .RES(sr_bit_1_q), .Q(cnt_bit_3_q), .CO(cnt_bit_3_co));  // open: nQ
  CNT_BIT cnt_bit_4 (
    .C2(FCLK2), .C1(FCLK1), .CIN(cnt_bit_3_co), .RES(sr_bit_1_q), .Q(cnt_bit_4_q), .CO(cnt_bit_4_co));  // open: nQ
  CNT_BIT cnt_bit_5 (.C2(FCLK2), .C1(FCLK1), .CIN(cnt_bit_4_co), .RES(sr_bit_1_q), .Q(cnt_bit_5_q));  // open: nQ, CO
  not not_2 (not_2_out, cnt_bit_1_q);
  not not_3 (not_3_out, cnt_bit_2_q);
  not not_4 (not_4_out, cnt_bit_3_q);
  not not_5 (not_5_out, cnt_bit_4_q);
  not not_6 (not_6_out, cnt_bit_5_q);
  not not_7 (not_7_out, not_2_out);
  not not_8 (not_8_out, not_3_out);
  not not_9 (not_9_out, not_4_out);
  not not_10 (not_10_out, not_5_out);
  not not_11 (not_11_out, not_6_out);
  not not_12 (not_12_out, g_3080);
  not not_13 (not_13_out, g_3079);
  not not_14 (not_14_out, g_3078);
  not not_15 (not_15_out, not_12_out);
  not not_16 (not_16_out, not_13_out);
  not not_17 (not_17_out, not_14_out);
  and _88 (_88_out, not_2_out, not_8_out, not_11_out, not_9_out, not_10_out);
  and _87 (_87_out, not_7_out, not_3_out, not_11_out, not_9_out, not_10_out);
  and _86 (_86_out, not_2_out, not_3_out, not_11_out, not_10_out, not_9_out);
  and _85 (_85_out, not_2_out, not_8_out, not_11_out, not_4_out, not_10_out);
  and _84 (_84_out, not_7_out, not_3_out, not_11_out, not_4_out, not_10_out);
  and _83 (_83_out, not_2_out, not_3_out, not_11_out, not_4_out, not_10_out);
  and _47 (_47_out, not_2_out, not_8_out, not_9_out, not_5_out, not_11_out);
  and _48 (_48_out, not_7_out, not_3_out, not_9_out, not_5_out, not_11_out);
  and _49 (_49_out, not_2_out, not_3_out, not_9_out, not_5_out, not_11_out);
  and _50 (_50_out, not_2_out, not_8_out, not_4_out, not_5_out, not_11_out);
  and _51 (_51_out, not_7_out, not_3_out, not_4_out, not_5_out, not_11_out);
  and _52 (_52_out, not_2_out, not_3_out, not_4_out, not_5_out, not_11_out);
  and _53 (_53_out, not_2_out, not_8_out, not_9_out, not_10_out, not_6_out);
  and _54 (_54_out, not_7_out, not_3_out, not_9_out, not_10_out, not_6_out);
  and _55 (_55_out, not_2_out, not_3_out, not_9_out, not_10_out, not_6_out);
  and _56 (_56_out, not_2_out, not_8_out, not_4_out, not_10_out, not_6_out);
  and _57 (_57_out, not_7_out, not_3_out, not_4_out, not_10_out, not_6_out);
  and _58 (_58_out, not_2_out, not_3_out, not_4_out, not_10_out, not_6_out);
  and _59 (_59_out, not_2_out, not_8_out, not_9_out, not_5_out, not_6_out);
  and _60 (_60_out, not_7_out, not_3_out, not_9_out, not_5_out, not_6_out);
  and _61 (_61_out, not_2_out, not_3_out, not_9_out, not_5_out, not_6_out);
  and _62 (_62_out, not_2_out, not_8_out, not_4_out, not_5_out, not_6_out);
  and _63 (_63_out, not_7_out, not_3_out, not_4_out, not_5_out, not_6_out);
  and _64 (_64_out, not_2_out, not_3_out, not_4_out, not_5_out, not_6_out);
  and _143 (_143_out, not_12_out, not_13_out, not_14_out);
  and _144 (_144_out, not_15_out, not_13_out, not_14_out);
  and _145 (_145_out, not_12_out, not_16_out, not_14_out);
  and _146 (_146_out, not_15_out, not_16_out, not_14_out);
  and _147 (_147_out, not_12_out, not_13_out, not_17_out);
  and _148 (_148_out, not_15_out, not_13_out, not_17_out);
  and _149 (_149_out, not_12_out, not_16_out, not_17_out);
  and _150 (_150_out, not_15_out, not_16_out, not_17_out);
  or _89 (_89_out, _88_out, _87_out, _86_out, _85_out, _84_out, _83_out);
  nor _90 (_90_out, _88_out, _87_out, _86_out, _85_out, _84_out, _83_out);
  or _82 (_82_out, _47_out, _48_out, _49_out, _50_out, _51_out, _52_out);
  nor _81 (_81_out, _47_out, _48_out, _49_out, _50_out, _51_out, _52_out);
  nor _80 (_80_out, _53_out, _54_out, _55_out, _56_out, _57_out, _58_out);
  or _72 (_72_out, _59_out, _60_out, _61_out, _62_out, _63_out, _64_out);
  nor _76 (_76_out, _59_out, _60_out, _61_out, _62_out, _63_out, _64_out);
  not not_18 (g_79, _80_out);
  not not_19 (g_75, _76_out);
  or _134 (_134_out, _143_out, _144_out, _145_out);
  or _135 (_135_out, _143_out, _144_out, _146_out, _147_out);
  or _138 (_138_out, _145_out, _148_out);
  or _139 (_139_out, _144_out, _148_out);
  or _136 (_136_out, _143_out, _144_out, _147_out, _148_out, _149_out);
  or _151 (_151_out, _148_out, _149_out, _150_out);
  or _137 (_137_out, _150_out, _147_out, _148_out, _149_out);
  nor _73 (_73_out, _85_out, _50_out, _56_out, _62_out);
  D_LATCH d_latch_1 (.EN(FCLK1), .D(g_75), .nQ(d_latch_1_nq));  // open: Q
  D_LATCH d_latch_2 (.EN(FCLK1), .D(_62_out), .nQ(d_latch_2_nq));  // open: Q
  not not_20 (not_20_out, g_75);
  not not_21 (not_21_out, _62_out);
  and _126 (_126_out, _146_out, _82_out);
  and _126_2 (_126_2_out, _134_out, _72_out);
  nand _120 (_120_out, _145_out, _82_out);
  and _121 (_121_out, _82_out, _135_out);
  and _121_2 (_121_2_out, _136_out, g_79);
  and _116 (_116_out, _138_out, _82_out);
  and _117 (_117_out, _139_out, _72_out);
  and _113 (_113_out, _151_out, _82_out);
  and _113_2 (_113_2_out, _150_out, g_79);
  and _113_3 (_113_3_out, 1'b1, _72_out);
  and _113_4 (_113_4_out, _137_out, _89_out);
  and _119 (_119_out, _90_out, _81_out);
  nor nor_1 (g_100, d_latch_1_nq, not_20_out);
  nor nor_2 (nor_2_out, d_latch_2_nq, not_21_out);
  not not_22 (g_118, _119_out);
  not not_23 (g_74, _73_out);
  buf buffer_1 (g_66, nor_2_out);
  buf buffer_2 (g_69, _62_out);
  buf buffer_3 (g_67, _64_out);
  buf buffer_4 (g_68, _63_out);
  nor _126_3 (_126_3_out, _126_out, _126_2_out);
  nor _121_3 (_121_3_out, _121_out, _121_2_out);
  nor _115 (_115_out, _116_out, _117_out, _89_out);
  nor _113_5 (_113_5_out, _113_out, _113_2_out, _113_3_out, _113_4_out);
  SR_BIT sr_bit_5 (.C2(FCLK2), .C1(FCLK1), .D(_89_out), .Q(sr_bit_5_q));  // open: nQ
  not not_24 (not_24_out, _113_5_out);
  not not_25 (g_125, _126_3_out);
  not not_26 (g_122, _120_out);
  not not_27 (g_123, _121_3_out);
  not not_28 (g_114, _115_out);
  nand _110 (_110_out, not_1_out, not_24_out);
  not not_29 (g_109, _110_out);
  not not_30 (g_77, not_31_out);
  not not_31 (not_31_out, _88_out);
  not not_32 (g_127, sr_bit_5_q);
  buf buffer_5 (g_124, _89_out);

  // Notes on the sheet:
  //   111
  //   43
  //   42
  //   40
  //   4
  //   5
  //   11
  //   8
  //   13
  //   12
  //   97
  //   98
  //   99
  //   41
  //   44
  //   97
  //   98
  //   99
  //   41
  //   44
  //   140
  //   141
  //   142
  //   140
  //   141
  //   142
  //   79
  //   75
  //   100
  //   65
  //   118
  //   74
  //   66
  //   69
  //   67
  //   68
  //   112
  //   78
  //   128
  //   127
  //   125
  //   122
  //   123
  //   114
  //   109
  //   77
  //   124
endmodule

module SDELAY24 (
  input  C2,
  input  C1,
  input  D,
  output Q40,
  output Q
);

  wire d_ff_1_q, d_ff_2_q, d_ff_3_q, d_ff_4_q, d_ff_5_q, d_ff_6_q, d_ff_7_q, d_ff_8_q, d_ff_9_q, d_ff_10_q,
       d_ff_11_q, d_ff_12_q, d_ff_13_q, d_ff_14_q, d_ff_15_q, d_ff_16_q, d_ff_17_q, d_ff_18_q, d_ff_19_q,
       d_ff_20_q, d_ff_21_q, d_ff_22_q, d_ff_23_q, d_ff_24_q, d_ff_25_q, d_ff_26_q, d_ff_27_q, d_ff_28_q,
       d_ff_29_q, d_ff_30_q, d_ff_31_q, d_ff_32_q, d_ff_33_q, d_ff_34_q, d_ff_35_q, d_ff_36_q, d_ff_37_q,
       d_ff_38_q, d_ff_39_q, d_ff_40_q, d_ff_41_q, d_ff_42_q, d_ff_43_q, d_ff_44_q, d_ff_45_q, d_ff_46_q;

  D_Flip_Flop #(.trigger("high")) d_ff_1 (.clk(C1), .D(D), .Q(d_ff_1_q));  // open: Qn, preset, en, reset
  D_Flip_Flop #(.trigger("high")) d_ff_2 (.clk(C1), .D(d_ff_43_q), .Q(d_ff_2_q));  // open: Qn, preset, en, reset
  D_Flip_Flop #(.trigger("high")) d_ff_3 (.clk(C1), .D(d_ff_44_q), .Q(d_ff_3_q));  // open: Qn, preset, en, reset
  D_Flip_Flop #(.trigger("high")) d_ff_4 (.clk(C1), .D(d_ff_45_q), .Q(d_ff_4_q));  // open: Qn, preset, en, reset
  D_Flip_Flop #(.trigger("high")) d_ff_5 (.clk(C1), .D(d_ff_46_q), .Q(d_ff_5_q));  // open: Qn, preset, en, reset
  D_Flip_Flop #(.trigger("high")) d_ff_6 (.clk(C1), .D(Q40), .Q(d_ff_6_q));  // open: Qn, preset, en, reset
  D_Flip_Flop #(.trigger("high")) d_ff_7 (.clk(C2), .D(d_ff_1_q), .Q(d_ff_7_q));  // open: Qn, preset, en, reset
  D_Flip_Flop #(.trigger("high")) d_ff_8 (.clk(C2), .D(d_ff_2_q), .Q(d_ff_8_q));  // open: Qn, preset, en, reset
  D_Flip_Flop #(.trigger("high")) d_ff_9 (.clk(C2), .D(d_ff_3_q), .Q(d_ff_9_q));  // open: Qn, preset, en, reset
  D_Flip_Flop #(.trigger("high")) d_ff_10 (.clk(C2), .D(d_ff_4_q), .Q(d_ff_10_q));  // open: Qn, preset, en, reset
  D_Flip_Flop #(.trigger("high")) d_ff_11 (.clk(C2), .D(d_ff_5_q), .Q(d_ff_11_q));  // open: Qn, preset, en, reset
  D_Flip_Flop #(.trigger("high")) d_ff_12 (.clk(C2), .D(d_ff_6_q), .Q(d_ff_12_q));  // open: Qn, preset, en, reset
  D_Flip_Flop #(.trigger("high")) d_ff_13 (.clk(C1), .D(d_ff_7_q), .Q(d_ff_13_q));  // open: Qn, preset, en, reset
  D_Flip_Flop #(.trigger("high")) d_ff_14 (.clk(C1), .D(d_ff_8_q), .Q(d_ff_14_q));  // open: Qn, preset, en, reset
  D_Flip_Flop #(.trigger("high")) d_ff_15 (.clk(C1), .D(d_ff_9_q), .Q(d_ff_15_q));  // open: Qn, preset, en, reset
  D_Flip_Flop #(.trigger("high")) d_ff_16 (.clk(C1), .D(d_ff_10_q), .Q(d_ff_16_q));  // open: Qn, preset, en, reset
  D_Flip_Flop #(.trigger("high")) d_ff_17 (.clk(C1), .D(d_ff_11_q), .Q(d_ff_17_q));  // open: Qn, preset, en, reset
  D_Flip_Flop #(.trigger("high")) d_ff_18 (.clk(C1), .D(d_ff_12_q), .Q(d_ff_18_q));  // open: Qn, preset, en, reset
  D_Flip_Flop #(.trigger("high")) d_ff_19 (.clk(C2), .D(d_ff_13_q), .Q(d_ff_19_q));  // open: Qn, preset, en, reset
  D_Flip_Flop #(.trigger("high")) d_ff_20 (.clk(C2), .D(d_ff_14_q), .Q(d_ff_20_q));  // open: Qn, preset, en, reset
  D_Flip_Flop #(.trigger("high")) d_ff_21 (.clk(C2), .D(d_ff_15_q), .Q(d_ff_21_q));  // open: Qn, preset, en, reset
  D_Flip_Flop #(.trigger("high")) d_ff_22 (.clk(C2), .D(d_ff_16_q), .Q(d_ff_22_q));  // open: Qn, preset, en, reset
  D_Flip_Flop #(.trigger("high")) d_ff_23 (.clk(C2), .D(d_ff_17_q), .Q(d_ff_23_q));  // open: Qn, preset, en, reset
  D_Flip_Flop #(.trigger("high")) d_ff_24 (.clk(C2), .D(d_ff_18_q), .Q(d_ff_24_q));  // open: Qn, preset, en, reset
  D_Flip_Flop #(.trigger("high")) d_ff_25 (.clk(C1), .D(d_ff_19_q), .Q(d_ff_25_q));  // open: Qn, preset, en, reset
  D_Flip_Flop #(.trigger("high")) d_ff_26 (.clk(C1), .D(d_ff_20_q), .Q(d_ff_26_q));  // open: Qn, preset, en, reset
  D_Flip_Flop #(.trigger("high")) d_ff_27 (.clk(C1), .D(d_ff_21_q), .Q(d_ff_27_q));  // open: Qn, preset, en, reset
  D_Flip_Flop #(.trigger("high")) d_ff_28 (.clk(C1), .D(d_ff_22_q), .Q(d_ff_28_q));  // open: Qn, preset, en, reset
  D_Flip_Flop #(.trigger("high")) d_ff_29 (.clk(C1), .D(d_ff_23_q), .Q(d_ff_29_q));  // open: Qn, preset, en, reset
  D_Flip_Flop #(.trigger("high")) d_ff_30 (.clk(C1), .D(d_ff_24_q), .Q(d_ff_30_q));  // open: Qn, preset, en, reset
  D_Flip_Flop #(.trigger("high")) d_ff_31 (.clk(C2), .D(d_ff_25_q), .Q(d_ff_31_q));  // open: Qn, preset, en, reset
  D_Flip_Flop #(.trigger("high")) d_ff_32 (.clk(C2), .D(d_ff_26_q), .Q(d_ff_32_q));  // open: Qn, preset, en, reset
  D_Flip_Flop #(.trigger("high")) d_ff_33 (.clk(C2), .D(d_ff_27_q), .Q(d_ff_33_q));  // open: Qn, preset, en, reset
  D_Flip_Flop #(.trigger("high")) d_ff_34 (.clk(C2), .D(d_ff_28_q), .Q(d_ff_34_q));  // open: Qn, preset, en, reset
  D_Flip_Flop #(.trigger("high")) d_ff_35 (.clk(C2), .D(d_ff_29_q), .Q(d_ff_35_q));  // open: Qn, preset, en, reset
  D_Flip_Flop #(.trigger("high")) d_ff_36 (.clk(C2), .D(d_ff_30_q), .Q(d_ff_36_q));  // open: Qn, preset, en, reset
  D_Flip_Flop #(.trigger("high")) d_ff_37 (.clk(C1), .D(d_ff_31_q), .Q(d_ff_37_q));  // open: Qn, preset, en, reset
  D_Flip_Flop #(.trigger("high")) d_ff_38 (.clk(C1), .D(d_ff_32_q), .Q(d_ff_38_q));  // open: Qn, preset, en, reset
  D_Flip_Flop #(.trigger("high")) d_ff_39 (.clk(C1), .D(d_ff_33_q), .Q(d_ff_39_q));  // open: Qn, preset, en, reset
  D_Flip_Flop #(.trigger("high")) d_ff_40 (.clk(C1), .D(d_ff_34_q), .Q(d_ff_40_q));  // open: Qn, preset, en, reset
  D_Flip_Flop #(.trigger("high")) d_ff_41 (.clk(C1), .D(d_ff_35_q), .Q(d_ff_41_q));  // open: Qn, preset, en, reset
  D_Flip_Flop #(.trigger("high")) d_ff_42 (.clk(C1), .D(d_ff_36_q), .Q(d_ff_42_q));  // open: Qn, preset, en, reset
  D_Flip_Flop #(.trigger("high")) d_ff_43 (.clk(C2), .D(d_ff_37_q), .Q(d_ff_43_q));  // open: Qn, preset, en, reset
  D_Flip_Flop #(.trigger("high")) d_ff_44 (.clk(C2), .D(d_ff_38_q), .Q(d_ff_44_q));  // open: Qn, preset, en, reset
  D_Flip_Flop #(.trigger("high")) d_ff_45 (.clk(C2), .D(d_ff_39_q), .Q(d_ff_45_q));  // open: Qn, preset, en, reset
  D_Flip_Flop #(.trigger("high")) d_ff_46 (.clk(C2), .D(d_ff_40_q), .Q(d_ff_46_q));  // open: Qn, preset, en, reset
  D_Flip_Flop #(.trigger("high")) d_ff_47 (.clk(C2), .D(d_ff_41_q), .Q(Q40));  // open: Qn, preset, en, reset
  D_Flip_Flop #(.trigger("high")) d_ff_48 (.clk(C2), .D(d_ff_42_q), .Q(Q));  // open: Qn, preset, en, reset
endmodule

module PHASE_GEN (
  input  FCLK2,
  input  FCLK1,
  output g_3391
);

  wire _3123_out, _3172_out, _3178_out, _3180_out, _3188_out, _3195_out, _3196_out, _3203_out, _3209_out,
       _3211_out, _3218_out, _3224_out, _3226_out, _3233_out, _3238_out, _3241_out, _3248_out, _3255_out,
       _3256_out, _3263_out, _3269_out, _3271_out, _3278_out, _3284_out, _3286_out, _3293_out, _3299_out,
       _3301_out, _3308_out, _3314_out, _3316_out, _3322_out, _3328_out, _3330_out, _3465_2_out, _3465_3_out,
       _3465_4_out, _3465_5_out, _3465_6_out, _3465_7_out, _3465_out, _3528_2_out, _3528_3_out, _3528_4_out,
       _3528_5_out, _3528_6_out, _3528_7_out, _3528_out, _3529_2_out, _3529_3_out, _3529_4_out, _3529_5_out,
       _3529_6_out, _3529_7_out, _3529_out, _3535_2_out, _3535_3_out, _3535_4_out, _3535_5_out, _3535_6_out,
       _3535_7_out, _3535_out, _3540_2_out, _3540_3_out, _3540_4_out, _3540_5_out, _3540_6_out, _3540_7_out,
       _3540_out, _3545_2_out, _3545_3_out, _3545_4_out, _3545_5_out, _3545_6_out, _3545_7_out, _3545_out,
       _3550_2_out, _3550_3_out, _3550_4_out, _3550_5_out, _3550_6_out, _3550_7_out, _3550_out, _3555_2_out,
       _3555_3_out, _3555_4_out, _3555_5_out, _3555_6_out, _3555_7_out, _3555_out, _3560_2_out, _3560_3_out,
       _3560_4_out, _3560_5_out, _3560_6_out, _3560_7_out, _3560_out, _3565_2_out, _3565_3_out, _3565_4_out,
       _3565_5_out, _3565_6_out, _3565_7_out, _3565_out, _3570_2_out, _3570_3_out, _3570_4_out, _3570_5_out,
       _3570_6_out, _3570_7_out, _3570_out, adder_1_cout, adder_1_out, adder_2_cout, adder_2_out,
       adder_3_cout, adder_3_out, adder_4_cout, adder_4_out, adder_5_cout, adder_5_out, adder_6_cout,
       adder_6_out, adder_7_cout, adder_7_out, adder_8_cout, adder_8_out, adder_9_cout, adder_9_out,
       adder_10_cout, adder_10_out, adder_11_cout, adder_11_out, adder_12_cout, adder_12_out, adder_13_cout,
       adder_13_out, adder_14_cout, adder_14_out, adder_15_cout, adder_15_out, adder_16_cout, adder_16_out,
       adder_17_cout, adder_17_out, adder_18_cout, adder_18_out, adder_19_cout, adder_19_out, adder_20_cout,
       adder_20_out, adder_21_cout, adder_21_out, adder_22_out, adder_23_cout, adder_23_out, adder_24_cout,
       adder_24_out, adder_25_cout, adder_25_out, adder_26_cout, adder_26_out, adder_27_cout, adder_27_out,
       adder_28_cout, adder_28_out, adder_29_cout, adder_29_out, adder_30_cout, adder_30_out, adder_31_cout,
       adder_31_out, adder_32_cout, adder_32_out, adder_33_cout, adder_33_out, and_1_out, and_2_out,
       and_3_out, and_4_out, and_5_out, and_6_out, and_7_out, and_8_out, and_9_out, and_10_out, d_latch_1_nq,
       d_latch_2_nq, d_latch_3_nq, d_latch_4_nq, d_latch_5_nq, d_latch_6_nq, d_latch_7_nq, d_latch_8_nq,
       d_latch_9_nq, d_latch_10_nq, d_latch_11_nq, d_latch_12_nq, d_latch_13_nq, d_latch_14_nq,
       d_latch_15_nq, d_latch_16_nq, d_latch_17_nq, d_latch_18_nq, d_latch_19_nq, d_latch_20_nq,
       d_latch_21_nq, d_latch_22_nq, d_latch_23_nq, d_latch_24_nq, d_latch_25_nq, d_latch_26_nq,
       d_latch_27_nq, d_latch_28_nq, d_latch_29_nq, d_latch_30_nq, d_latch_31_nq, d_latch_32_nq,
       d_latch_33_nq, d_latch_34_nq, d_latch_35_nq, d_latch_36_nq, d_latch_37_nq, d_latch_38_nq,
       d_latch_39_nq, d_latch_40_nq, d_latch_41_nq, d_latch_42_nq, d_latch_43_nq, d_latch_44_nq,
       d_latch_45_nq, d_latch_46_nq, d_latch_47_nq, d_latch_48_nq, d_latch_49_nq, d_latch_50_nq,
       d_latch_51_nq, d_latch_52_nq, d_latch_53_nq, d_latch_54_nq, d_latch_55_nq, d_latch_56_nq,
       d_latch_57_nq, d_latch_58_nq, d_latch_59_nq, d_latch_60_nq, d_latch_61_nq, d_latch_62_nq,
       d_latch_63_nq, d_latch_64_nq, d_latch_65_nq, d_latch_66_nq, not_1_out, not_2_out, not_3_out,
       not_4_out, not_5_out, not_6_out, not_7_out, not_8_out, not_9_out, not_10_out, not_11_out, not_12_out,
       not_13_out, not_14_out, not_15_out, not_16_out, not_17_out, not_18_out, not_19_out, not_20_out,
       not_21_out, not_22_out, not_23_out, not_24_out, not_25_out, not_26_out, not_27_out, not_28_out,
       or_1_out, or_2_out, or_3_out, or_4_out, or_5_out, or_6_out, or_7_out, or_8_out, or_9_out, or_10_out,
       sdelay24_1_q, sdelay24_2_q, sdelay24_3_q, sdelay24_4_q, sdelay24_5_q, sdelay24_6_q, sdelay24_7_q,
       sdelay24_8_q, sdelay24_9_q, sdelay24_10_q, sdelay24_11_q, sdelay24_11_q40, sr_bit_1_q, sr_bit_2_q,
       sr_bit_3_q, sr_bit_4_q, sr_bit_5_q, sr_bit_6_q, sr_bit_7_q, sr_bit_8_q, sr_bit_9_q, sr_bit_10_q,
       sr_bit_11_q, sr_bit_12_q, sr_bit_13_q, sr_bit_14_q, sr_bit_15_q, sr_bit_16_q, sr_bit_17_q,
       sr_bit_18_q, sr_bit_19_q, sr_bit_20_q, sr_bit_21_q, sr_bit_22_q, sr_bit_23_q, sr_bit_24_q,
       sr_bit_25_q, sr_bit_26_q, sr_bit_27_q, sr_bit_28_q, sr_bit_29_q, sr_bit_30_q, sr_bit_31_q,
       sr_bit_32_q, undriven, undriven_2, undriven_3, undriven_4, undriven_5, undriven_6, undriven_7,
       undriven_8, undriven_9, undriven_10, undriven_11, undriven_12, undriven_13, undriven_14, undriven_15,
       undriven_16, undriven_17, undriven_18, undriven_19, undriven_20, undriven_21, undriven_22;

  not not_1 (not_1_out, undriven);
  not not_2 (not_2_out, undriven_2);
  D_LATCH d_latch_1 (.EN(FCLK2), .D(_3123_out), .nQ(d_latch_1_nq));  // open: Q
  nor _3123 (_3123_out, not_1_out, not_2_out);
  and _3465 (_3465_out, 1'b0, 1'b0);
  // AND_Gate _3465_2 has open pins: out=_3465_2_out
  // AND_Gate _3465_3 has open pins: out=_3465_3_out
  // AND_Gate _3465_4 has open pins: out=_3465_4_out
  // AND_Gate _3465_5 has open pins: out=_3465_5_out
  // AND_Gate _3465_6 has open pins: out=_3465_6_out
  and _3528 (_3528_out, 1'b0, 1'b0);
  // AND_Gate _3528_2 has open pins: out=_3528_2_out
  // AND_Gate _3528_3 has open pins: out=_3528_3_out
  // AND_Gate _3528_4 has open pins: out=_3528_4_out
  // AND_Gate _3528_5 has open pins: out=_3528_5_out
  // AND_Gate _3528_6 has open pins: out=_3528_6_out
  and _3529 (_3529_out, 1'b0, 1'b0);
  // AND_Gate _3529_2 has open pins: out=_3529_2_out
  // AND_Gate _3529_3 has open pins: out=_3529_3_out
  // AND_Gate _3529_4 has open pins: out=_3529_4_out
  // AND_Gate _3529_5 has open pins: out=_3529_5_out
  // AND_Gate _3529_6 has open pins: out=_3529_6_out
  and _3535 (_3535_out, 1'b0, 1'b0);
  // AND_Gate _3535_2 has open pins: out=_3535_2_out
  // AND_Gate _3535_3 has open pins: out=_3535_3_out
  // AND_Gate _3535_4 has open pins: out=_3535_4_out
  // AND_Gate _3535_5 has open pins: out=_3535_5_out
  // AND_Gate _3535_6 has open pins: out=_3535_6_out
  and _3540 (_3540_out, 1'b0, 1'b0);
  // AND_Gate _3540_2 has open pins: out=_3540_2_out
  // AND_Gate _3540_3 has open pins: out=_3540_3_out
  // AND_Gate _3540_4 has open pins: out=_3540_4_out
  // AND_Gate _3540_5 has open pins: out=_3540_5_out
  // AND_Gate _3540_6 has open pins: out=_3540_6_out
  and _3545 (_3545_out, 1'b0, 1'b0);
  // AND_Gate _3545_2 has open pins: out=_3545_2_out
  // AND_Gate _3545_3 has open pins: out=_3545_3_out
  // AND_Gate _3545_4 has open pins: out=_3545_4_out
  // AND_Gate _3545_5 has open pins: out=_3545_5_out
  // AND_Gate _3545_6 has open pins: out=_3545_6_out
  and _3550 (_3550_out, 1'b0, 1'b0);
  // AND_Gate _3550_2 has open pins: out=_3550_2_out
  // AND_Gate _3550_3 has open pins: out=_3550_3_out
  // AND_Gate _3550_4 has open pins: out=_3550_4_out
  // AND_Gate _3550_5 has open pins: out=_3550_5_out
  // AND_Gate _3550_6 has open pins: out=_3550_6_out
  and _3555 (_3555_out, 1'b0, 1'b0);
  // AND_Gate _3555_2 has open pins: out=_3555_2_out
  // AND_Gate _3555_3 has open pins: out=_3555_3_out
  // AND_Gate _3555_4 has open pins: out=_3555_4_out
  // AND_Gate _3555_5 has open pins: out=_3555_5_out
  // AND_Gate _3555_6 has open pins: out=_3555_6_out
  and _3560 (_3560_out, 1'b0, 1'b0);
  // AND_Gate _3560_2 has open pins: out=_3560_2_out
  // AND_Gate _3560_3 has open pins: out=_3560_3_out
  // AND_Gate _3560_4 has open pins: out=_3560_4_out
  // AND_Gate _3560_5 has open pins: out=_3560_5_out
  // AND_Gate _3560_6 has open pins: out=_3560_6_out
  and _3565 (_3565_out, 1'b0, 1'b0);
  // AND_Gate _3565_2 has open pins: out=_3565_2_out
  // AND_Gate _3565_3 has open pins: out=_3565_3_out
  // AND_Gate _3565_4 has open pins: out=_3565_4_out
  // AND_Gate _3565_5 has open pins: out=_3565_5_out
  // AND_Gate _3565_6 has open pins: out=_3565_6_out
  and _3570 (_3570_out, 1'b0, 1'b0);
  // AND_Gate _3570_2 has open pins: out=_3570_2_out
  // AND_Gate _3570_3 has open pins: out=_3570_3_out
  // AND_Gate _3570_4 has open pins: out=_3570_4_out
  // AND_Gate _3570_5 has open pins: out=_3570_5_out
  // AND_Gate _3570_6 has open pins: out=_3570_6_out
  nor _3465_7 (_3465_7_out, _3465_out, _3465_2_out, _3465_3_out, _3465_4_out, _3465_5_out, _3465_6_out);
  nor _3528_7 (_3528_7_out, _3528_out, _3528_2_out, _3528_3_out, _3528_4_out, _3528_5_out, _3528_6_out);
  nor _3529_7 (_3529_7_out, _3529_out, _3529_2_out, _3529_3_out, _3529_4_out, _3529_5_out, _3529_6_out);
  nor _3535_7 (_3535_7_out, _3535_out, _3535_2_out, _3535_3_out, _3535_4_out, _3535_5_out, _3535_6_out);
  nor _3540_7 (_3540_7_out, _3540_out, _3540_2_out, _3540_3_out, _3540_4_out, _3540_5_out, _3540_6_out);
  nor _3545_7 (_3545_7_out, _3545_out, _3545_2_out, _3545_3_out, _3545_4_out, _3545_5_out, _3545_6_out);
  nor _3550_7 (_3550_7_out, _3550_out, _3550_2_out, _3550_3_out, _3550_4_out, _3550_5_out, _3550_6_out);
  nor _3555_7 (_3555_7_out, _3555_out, _3555_2_out, _3555_3_out, _3555_4_out, _3555_5_out, _3555_6_out);
  nor _3560_7 (_3560_7_out, _3560_out, _3560_2_out, _3560_3_out, _3560_4_out, _3560_5_out, _3560_6_out);
  nor _3565_7 (_3565_7_out, _3565_out, _3565_2_out, _3565_3_out, _3565_4_out, _3565_5_out, _3565_6_out);
  nor _3570_7 (_3570_7_out, _3570_out, _3570_2_out, _3570_3_out, _3570_4_out, _3570_5_out, _3570_6_out);
  D_LATCH d_latch_2 (.EN(FCLK2), .D(_3465_7_out), .nQ(d_latch_2_nq));  // open: Q
  D_LATCH d_latch_3 (.EN(FCLK2), .D(undriven_3), .nQ(d_latch_3_nq));  // open: Q
  D_LATCH d_latch_4 (.EN(FCLK2), .D(_3528_7_out), .nQ(d_latch_4_nq));  // open: Q
  D_LATCH d_latch_5 (.EN(FCLK2), .D(undriven_4), .nQ(d_latch_5_nq));  // open: Q
  D_LATCH d_latch_6 (.EN(FCLK2), .D(undriven_5), .nQ(d_latch_6_nq));  // open: Q
  D_LATCH d_latch_7 (.EN(FCLK2), .D(_3529_7_out), .nQ(d_latch_7_nq));  // open: Q
  D_LATCH d_latch_8 (.EN(FCLK2), .D(undriven_6), .nQ(d_latch_8_nq));  // open: Q
  D_LATCH d_latch_9 (.EN(FCLK2), .D(undriven_7), .nQ(d_latch_9_nq));  // open: Q
  D_LATCH d_latch_10 (.EN(FCLK2), .D(_3535_7_out), .nQ(d_latch_10_nq));  // open: Q
  D_LATCH d_latch_11 (.EN(FCLK2), .D(undriven_8), .nQ(d_latch_11_nq));  // open: Q
  D_LATCH d_latch_12 (.EN(FCLK2), .D(undriven_9), .nQ(d_latch_12_nq));  // open: Q
  D_LATCH d_latch_13 (.EN(FCLK2), .D(_3540_7_out), .nQ(d_latch_13_nq));  // open: Q
  D_LATCH d_latch_14 (.EN(FCLK2), .D(undriven_10), .nQ(d_latch_14_nq));  // open: Q
  D_LATCH d_latch_15 (.EN(FCLK2), .D(undriven_11), .nQ(d_latch_15_nq));  // open: Q
  D_LATCH d_latch_16 (.EN(FCLK2), .D(_3545_7_out), .nQ(d_latch_16_nq));  // open: Q
  D_LATCH d_latch_17 (.EN(FCLK2), .D(undriven_12), .nQ(d_latch_17_nq));  // open: Q
  D_LATCH d_latch_18 (.EN(FCLK2), .D(undriven_13), .nQ(d_latch_18_nq));  // open: Q
  D_LATCH d_latch_19 (.EN(FCLK2), .D(_3550_7_out), .nQ(d_latch_19_nq));  // open: Q
  D_LATCH d_latch_20 (.EN(FCLK2), .D(undriven_14), .nQ(d_latch_20_nq));  // open: Q
  D_LATCH d_latch_21 (.EN(FCLK2), .D(undriven_15), .nQ(d_latch_21_nq));  // open: Q
  D_LATCH d_latch_22 (.EN(FCLK2), .D(_3555_7_out), .nQ(d_latch_22_nq));  // open: Q
  D_LATCH d_latch_23 (.EN(FCLK2), .D(undriven_16), .nQ(d_latch_23_nq));  // open: Q
  D_LATCH d_latch_24 (.EN(FCLK2), .D(undriven_17), .nQ(d_latch_24_nq));  // open: Q
  D_LATCH d_latch_25 (.EN(FCLK2), .D(_3560_7_out), .nQ(d_latch_25_nq));  // open: Q
  D_LATCH d_latch_26 (.EN(FCLK2), .D(undriven_18), .nQ(d_latch_26_nq));  // open: Q
  D_LATCH d_latch_27 (.EN(FCLK2), .D(undriven_19), .nQ(d_latch_27_nq));  // open: Q
  D_LATCH d_latch_28 (.EN(FCLK2), .D(_3565_7_out), .nQ(d_latch_28_nq));  // open: Q
  D_LATCH d_latch_29 (.EN(FCLK2), .D(undriven_20), .nQ(d_latch_29_nq));  // open: Q
  D_LATCH d_latch_30 (.EN(FCLK2), .D(undriven_21), .nQ(d_latch_30_nq));  // open: Q
  D_LATCH d_latch_31 (.EN(FCLK2), .D(_3570_7_out), .nQ(d_latch_31_nq));  // open: Q
  D_LATCH d_latch_32 (.EN(FCLK2), .D(undriven_22), .nQ(d_latch_32_nq));  // open: Q
  // NOT_Gate not_3 has open pins: in=open, out=not_3_out
  // NOT_Gate not_4 has open pins: in=open, out=not_4_out
  // NOT_Gate not_5 has open pins: in=open, out=not_5_out
  // NOT_Gate not_6 has open pins: in=open, out=not_6_out
  not not_7 (not_7_out, d_latch_3_nq);
  not not_8 (not_8_out, d_latch_5_nq);
  not not_9 (not_9_out, d_latch_8_nq);
  not not_10 (not_10_out, d_latch_11_nq);
  not not_11 (not_11_out, d_latch_14_nq);
  not not_12 (not_12_out, d_latch_17_nq);
  not not_13 (not_13_out, d_latch_20_nq);
  not not_14 (not_14_out, d_latch_23_nq);
  not not_15 (not_15_out, d_latch_26_nq);
  not not_16 (not_16_out, d_latch_29_nq);
  not not_17 (not_17_out, d_latch_32_nq);
  Adder #(.width(1)) adder_1 (.a(1'b0), .b(d_latch_2_nq), .out(adder_1_out), .cin(d_latch_1_nq), .cout(adder_1_cout));
  Adder #(.width(1)) adder_2 (.a(1'b0), .b(d_latch_4_nq), .out(adder_2_out), .cin(adder_1_cout), .cout(adder_2_cout));
  Adder #(.width(1)) adder_3 (
    .a(d_latch_6_nq), .b(d_latch_7_nq), .out(adder_3_out), .cin(adder_2_cout), .cout(adder_3_cout));
  Adder #(.width(1)) adder_4 (
    .a(d_latch_9_nq), .b(d_latch_10_nq), .out(adder_4_out), .cin(adder_3_cout), .cout(adder_4_cout));
  Adder #(.width(1)) adder_5 (
    .a(d_latch_12_nq), .b(d_latch_13_nq), .out(adder_5_out), .cin(adder_4_cout), .cout(adder_5_cout));
  Adder #(.width(1)) adder_6 (
    .a(d_latch_15_nq), .b(d_latch_16_nq), .out(adder_6_out), .cin(adder_5_cout), .cout(adder_6_cout));
  Adder #(.width(1)) adder_7 (
    .a(d_latch_18_nq), .b(d_latch_19_nq), .out(adder_7_out), .cin(adder_6_cout), .cout(adder_7_cout));
  Adder #(.width(1)) adder_8 (
    .a(d_latch_21_nq), .b(d_latch_22_nq), .out(adder_8_out), .cin(adder_7_cout), .cout(adder_8_cout));
  Adder #(.width(1)) adder_9 (
    .a(d_latch_24_nq), .b(d_latch_25_nq), .out(adder_9_out), .cin(adder_8_cout), .cout(adder_9_cout));
  Adder #(.width(1)) adder_10 (
    .a(d_latch_27_nq), .b(d_latch_28_nq), .out(adder_10_out), .cin(adder_9_cout), .cout(adder_10_cout));
  Adder #(.width(1)) adder_11 (
    .a(d_latch_30_nq), .b(d_latch_31_nq), .out(adder_11_out), .cin(adder_10_cout), .cout(adder_11_cout));
  SR_BIT sr_bit_1 (.C2(FCLK2), .C1(FCLK1), .D(adder_1_out), .Q(sr_bit_1_q));  // open: nQ
  SR_BIT sr_bit_2 (.C2(FCLK2), .C1(FCLK1), .D(not_7_out), .Q(sr_bit_2_q));  // open: nQ
  SR_BIT sr_bit_3 (.C2(FCLK2), .C1(FCLK1), .D(adder_2_out), .Q(sr_bit_3_q));  // open: nQ
  SR_BIT sr_bit_4 (.C2(FCLK2), .C1(FCLK1), .D(not_8_out), .Q(sr_bit_4_q));  // open: nQ
  SR_BIT sr_bit_5 (.C2(FCLK2), .C1(FCLK1), .D(adder_3_out), .Q(sr_bit_5_q));  // open: nQ
  SR_BIT sr_bit_6 (.C2(FCLK2), .C1(FCLK1), .D(not_9_out), .Q(sr_bit_6_q));  // open: nQ
  SR_BIT sr_bit_7 (.C2(FCLK2), .C1(FCLK1), .D(adder_4_out), .Q(sr_bit_7_q));  // open: nQ
  SR_BIT sr_bit_8 (.C2(FCLK2), .C1(FCLK1), .D(not_10_out), .Q(sr_bit_8_q));  // open: nQ
  SR_BIT sr_bit_9 (.C2(FCLK2), .C1(FCLK1), .D(adder_5_out), .Q(sr_bit_9_q));  // open: nQ
  SR_BIT sr_bit_10 (.C2(FCLK2), .C1(FCLK1), .D(not_11_out), .Q(sr_bit_10_q));  // open: nQ
  SR_BIT sr_bit_11 (.C2(FCLK2), .C1(FCLK1), .D(adder_6_out), .Q(sr_bit_11_q));  // open: nQ
  SR_BIT sr_bit_12 (.C2(FCLK2), .C1(FCLK1), .D(not_12_out), .Q(sr_bit_12_q));  // open: nQ
  SR_BIT sr_bit_13 (.C2(FCLK2), .C1(FCLK1), .D(adder_7_out), .Q(sr_bit_13_q));  // open: nQ
  SR_BIT sr_bit_14 (.C2(FCLK2), .C1(FCLK1), .D(not_13_out), .Q(sr_bit_14_q));  // open: nQ
  SR_BIT sr_bit_15 (.C2(FCLK2), .C1(FCLK1), .D(adder_8_out), .Q(sr_bit_15_q));  // open: nQ
  SR_BIT sr_bit_16 (.C2(FCLK2), .C1(FCLK1), .D(not_14_out), .Q(sr_bit_16_q));  // open: nQ
  SR_BIT sr_bit_17 (.C2(FCLK2), .C1(FCLK1), .D(adder_9_out), .Q(sr_bit_17_q));  // open: nQ
  SR_BIT sr_bit_18 (.C2(FCLK2), .C1(FCLK1), .D(not_15_out), .Q(sr_bit_18_q));  // open: nQ
  SR_BIT sr_bit_19 (.C2(FCLK2), .C1(FCLK1), .D(adder_10_out), .Q(sr_bit_19_q));  // open: nQ
  SR_BIT sr_bit_20 (.C2(FCLK2), .C1(FCLK1), .D(not_16_out), .Q(sr_bit_20_q));  // open: nQ
  SR_BIT sr_bit_21 (.C2(FCLK2), .C1(FCLK1), .D(adder_11_out), .Q(sr_bit_21_q));  // open: nQ
  SR_BIT sr_bit_22 (.C2(FCLK2), .C1(FCLK1), .D(not_17_out), .Q(sr_bit_22_q));  // open: nQ
  D_LATCH d_latch_33 (.EN(FCLK2), .D(_3178_out), .nQ(d_latch_33_nq));  // open: Q
  nand _3178 (_3178_out, sr_bit_1_q, not_6_out);
  D_LATCH d_latch_34 (.EN(FCLK2), .D(_3180_out), .nQ(d_latch_34_nq));  // open: Q
  nand _3180 (_3180_out, sr_bit_2_q, not_5_out);
  D_LATCH d_latch_35 (.EN(FCLK2), .D(_3195_out), .nQ(d_latch_35_nq));  // open: Q
  nand _3195 (_3195_out, sr_bit_3_q, not_6_out);
  D_LATCH d_latch_36 (.EN(FCLK2), .D(_3196_out), .nQ(d_latch_36_nq));  // open: Q
  nand _3196 (_3196_out, sr_bit_4_q, not_5_out);
  D_LATCH d_latch_37 (.EN(FCLK2), .D(_3209_out), .nQ(d_latch_37_nq));  // open: Q
  nand _3209 (_3209_out, sr_bit_5_q, not_6_out);
  D_LATCH d_latch_38 (.EN(FCLK2), .D(_3211_out), .nQ(d_latch_38_nq));  // open: Q
  nand _3211 (_3211_out, sr_bit_6_q, not_5_out);
  D_LATCH d_latch_39 (.EN(FCLK2), .D(_3224_out), .nQ(d_latch_39_nq));  // open: Q
  nand _3224 (_3224_out, sr_bit_7_q, not_6_out);
  D_LATCH d_latch_40 (.EN(FCLK2), .D(_3226_out), .nQ(d_latch_40_nq));  // open: Q
  nand _3226 (_3226_out, sr_bit_8_q, not_5_out);
  D_LATCH d_latch_41 (.EN(FCLK2), .D(_3238_out), .nQ(d_latch_41_nq));  // open: Q
  nand _3238 (_3238_out, sr_bit_9_q, not_6_out);
  D_LATCH d_latch_42 (.EN(FCLK2), .D(_3241_out), .nQ(d_latch_42_nq));  // open: Q
  nand _3241 (_3241_out, sr_bit_10_q, not_5_out);
  D_LATCH d_latch_43 (.EN(FCLK2), .D(_3255_out), .nQ(d_latch_43_nq));  // open: Q
  nand _3255 (_3255_out, sr_bit_11_q, not_6_out);
  D_LATCH d_latch_44 (.EN(FCLK2), .D(_3256_out), .nQ(d_latch_44_nq));  // open: Q
  nand _3256 (_3256_out, sr_bit_12_q, not_5_out);
  D_LATCH d_latch_45 (.EN(FCLK2), .D(_3269_out), .nQ(d_latch_45_nq));  // open: Q
  nand _3269 (_3269_out, sr_bit_13_q, not_6_out);
  D_LATCH d_latch_46 (.EN(FCLK2), .D(_3271_out), .nQ(d_latch_46_nq));  // open: Q
  nand _3271 (_3271_out, sr_bit_14_q, not_5_out);
  D_LATCH d_latch_47 (.EN(FCLK2), .D(_3284_out), .nQ(d_latch_47_nq));  // open: Q
  nand _3284 (_3284_out, sr_bit_15_q, not_6_out);
  D_LATCH d_latch_48 (.EN(FCLK2), .D(_3286_out), .nQ(d_latch_48_nq));  // open: Q
  nand _3286 (_3286_out, sr_bit_16_q, not_5_out);
  D_LATCH d_latch_49 (.EN(FCLK2), .D(_3299_out), .nQ(d_latch_49_nq));  // open: Q
  nand _3299 (_3299_out, sr_bit_17_q, not_6_out);
  D_LATCH d_latch_50 (.EN(FCLK2), .D(_3301_out), .nQ(d_latch_50_nq));  // open: Q
  nand _3301 (_3301_out, sr_bit_18_q, not_5_out);
  D_LATCH d_latch_51 (.EN(FCLK2), .D(_3314_out), .nQ(d_latch_51_nq));  // open: Q
  nand _3314 (_3314_out, sr_bit_19_q, not_6_out);
  D_LATCH d_latch_52 (.EN(FCLK2), .D(_3316_out), .nQ(d_latch_52_nq));  // open: Q
  nand _3316 (_3316_out, sr_bit_20_q, not_5_out);
  D_LATCH d_latch_53 (.EN(FCLK2), .D(_3328_out), .nQ(d_latch_53_nq));  // open: Q
  nand _3328 (_3328_out, sr_bit_21_q, not_6_out);
  D_LATCH d_latch_54 (.EN(FCLK2), .D(_3330_out), .nQ(d_latch_54_nq));  // open: Q
  nand _3330 (_3330_out, sr_bit_22_q, not_5_out);
  Adder #(.width(1)) adder_12 (
    .a(d_latch_33_nq), .b(d_latch_34_nq), .out(adder_12_out), .cin(1'b0), .cout(adder_12_cout));
  Adder #(.width(1)) adder_13 (
    .a(d_latch_35_nq), .b(d_latch_36_nq), .out(adder_13_out), .cin(adder_12_cout), .cout(adder_13_cout));
  Adder #(.width(1)) adder_14 (
    .a(d_latch_37_nq), .b(d_latch_38_nq), .out(adder_14_out), .cin(adder_13_cout), .cout(adder_14_cout));
  Adder #(.width(1)) adder_15 (
    .a(d_latch_39_nq), .b(d_latch_40_nq), .out(adder_15_out), .cin(adder_14_cout), .cout(adder_15_cout));
  Adder #(.width(1)) adder_16 (
    .a(d_latch_41_nq), .b(d_latch_42_nq), .out(adder_16_out), .cin(adder_15_cout), .cout(adder_16_cout));
  Adder #(.width(1)) adder_17 (
    .a(d_latch_43_nq), .b(d_latch_44_nq), .out(adder_17_out), .cin(adder_16_cout), .cout(adder_17_cout));
  Adder #(.width(1)) adder_18 (
    .a(d_latch_45_nq), .b(d_latch_46_nq), .out(adder_18_out), .cin(adder_17_cout), .cout(adder_18_cout));
  Adder #(.width(1)) adder_19 (
    .a(d_latch_47_nq), .b(d_latch_48_nq), .out(adder_19_out), .cin(adder_18_cout), .cout(adder_19_cout));
  Adder #(.width(1)) adder_20 (
    .a(d_latch_49_nq), .b(d_latch_50_nq), .out(adder_20_out), .cin(adder_19_cout), .cout(adder_20_cout));
  Adder #(.width(1)) adder_21 (
    .a(d_latch_51_nq), .b(d_latch_52_nq), .out(adder_21_out), .cin(adder_20_cout), .cout(adder_21_cout));
  Adder #(.width(1)) adder_22 (
    .a(d_latch_53_nq), .b(d_latch_54_nq), .out(adder_22_out), .cin(adder_21_cout));  // open: cout
  SDELAY24 sdelay24_1 (.C2(FCLK2), .C1(FCLK1), .D(adder_23_out), .Q(sdelay24_1_q));  // open: Q40
  D_LATCH d_latch_55 (.EN(FCLK2), .D(adder_12_out), .nQ(d_latch_55_nq));  // open: Q
  SDELAY24 sdelay24_2 (.C2(FCLK2), .C1(FCLK1), .D(adder_24_out), .Q(sdelay24_2_q));  // open: Q40
  D_LATCH d_latch_56 (.EN(FCLK2), .D(adder_13_out), .nQ(d_latch_56_nq));  // open: Q
  SDELAY24 sdelay24_3 (.C2(FCLK2), .C1(FCLK1), .D(adder_25_out), .Q(sdelay24_3_q));  // open: Q40
  D_LATCH d_latch_57 (.EN(FCLK2), .D(adder_14_out), .nQ(d_latch_57_nq));  // open: Q
  SDELAY24 sdelay24_4 (.C2(FCLK2), .C1(FCLK1), .D(adder_26_out), .Q(sdelay24_4_q));  // open: Q40
  D_LATCH d_latch_58 (.EN(FCLK2), .D(adder_15_out), .nQ(d_latch_58_nq));  // open: Q
  SDELAY24 sdelay24_5 (.C2(FCLK2), .C1(FCLK1), .D(adder_27_out), .Q(sdelay24_5_q));  // open: Q40
  D_LATCH d_latch_59 (.EN(FCLK2), .D(adder_16_out), .nQ(d_latch_59_nq));  // open: Q
  SDELAY24 sdelay24_6 (.C2(FCLK2), .C1(FCLK1), .D(adder_28_out), .Q(sdelay24_6_q));  // open: Q40
  D_LATCH d_latch_60 (.EN(FCLK2), .D(adder_17_out), .nQ(d_latch_60_nq));  // open: Q
  SDELAY24 sdelay24_7 (.C2(FCLK2), .C1(FCLK1), .D(adder_29_out), .Q(sdelay24_7_q));  // open: Q40
  D_LATCH d_latch_61 (.EN(FCLK2), .D(adder_18_out), .nQ(d_latch_61_nq));  // open: Q
  SDELAY24 sdelay24_8 (.C2(FCLK2), .C1(FCLK1), .D(adder_30_out), .Q(sdelay24_8_q));  // open: Q40
  D_LATCH d_latch_62 (.EN(FCLK2), .D(adder_19_out), .nQ(d_latch_62_nq));  // open: Q
  SDELAY24 sdelay24_9 (.C2(FCLK2), .C1(FCLK1), .D(adder_31_out), .Q(sdelay24_9_q));  // open: Q40
  D_LATCH d_latch_63 (.EN(FCLK2), .D(adder_20_out), .nQ(d_latch_63_nq));  // open: Q
  SDELAY24 sdelay24_10 (.C2(FCLK2), .C1(FCLK1), .D(adder_32_out), .Q(sdelay24_10_q));  // open: Q40
  D_LATCH d_latch_64 (.EN(FCLK2), .D(adder_21_out), .nQ(d_latch_64_nq));  // open: Q
  SDELAY24 sdelay24_11 (.C2(FCLK2), .C1(FCLK1), .D(adder_33_out), .Q(sdelay24_11_q), .Q40(sdelay24_11_q40));
  D_LATCH d_latch_65 (.EN(FCLK2), .D(adder_22_out), .nQ(d_latch_65_nq));  // open: Q
  not not_18 (not_18_out, d_latch_55_nq);
  not not_19 (not_19_out, d_latch_56_nq);
  not not_20 (not_20_out, d_latch_57_nq);
  not not_21 (not_21_out, d_latch_58_nq);
  not not_22 (not_22_out, d_latch_59_nq);
  not not_23 (not_23_out, d_latch_60_nq);
  not not_24 (not_24_out, d_latch_61_nq);
  not not_25 (not_25_out, d_latch_62_nq);
  not not_26 (not_26_out, d_latch_63_nq);
  not not_27 (not_27_out, d_latch_64_nq);
  not not_28 (not_28_out, d_latch_65_nq);
  and _3172 (_3172_out, sdelay24_1_q, not_4_out);
  and _3188 (_3188_out, sdelay24_2_q, not_4_out);
  and _3203 (_3203_out, sdelay24_3_q, not_4_out);
  and _3218 (_3218_out, sdelay24_4_q, not_4_out);
  and _3233 (_3233_out, sdelay24_5_q, not_4_out);
  and _3248 (_3248_out, sdelay24_6_q, not_4_out);
  and _3263 (_3263_out, sdelay24_7_q, not_4_out);
  and _3278 (_3278_out, sdelay24_8_q, not_4_out);
  and _3293 (_3293_out, sdelay24_9_q, not_4_out);
  and _3308 (_3308_out, sdelay24_10_q, not_4_out);
  not not_29 (g_3391, sdelay24_11_q40);
  and _3322 (_3322_out, sdelay24_11_q, not_4_out);
  Adder #(.width(1)) adder_23 (.a(_3172_out), .b(not_18_out), .out(adder_23_out), .cin(1'b0), .cout(adder_23_cout));
  Adder #(.width(1)) adder_24 (
    .a(_3188_out), .b(not_19_out), .out(adder_24_out), .cin(adder_23_cout), .cout(adder_24_cout));
  Adder #(.width(1)) adder_25 (
    .a(_3203_out), .b(not_20_out), .out(adder_25_out), .cin(adder_24_cout), .cout(adder_25_cout));
  Adder #(.width(1)) adder_26 (
    .a(_3218_out), .b(not_21_out), .out(adder_26_out), .cin(adder_25_cout), .cout(adder_26_cout));
  Adder #(.width(1)) adder_27 (
    .a(_3233_out), .b(not_22_out), .out(adder_27_out), .cin(adder_26_cout), .cout(adder_27_cout));
  Adder #(.width(1)) adder_28 (
    .a(_3248_out), .b(not_23_out), .out(adder_28_out), .cin(adder_27_cout), .cout(adder_28_cout));
  Adder #(.width(1)) adder_29 (
    .a(_3263_out), .b(not_24_out), .out(adder_29_out), .cin(adder_28_cout), .cout(adder_29_cout));
  Adder #(.width(1)) adder_30 (
    .a(_3278_out), .b(not_25_out), .out(adder_30_out), .cin(adder_29_cout), .cout(adder_30_cout));
  Adder #(.width(1)) adder_31 (
    .a(_3293_out), .b(not_26_out), .out(adder_31_out), .cin(adder_30_cout), .cout(adder_31_cout));
  Adder #(.width(1)) adder_32 (
    .a(_3308_out), .b(not_27_out), .out(adder_32_out), .cin(adder_31_cout), .cout(adder_32_cout));
  Adder #(.width(1)) adder_33 (
    .a(_3322_out), .b(not_28_out), .out(adder_33_out), .cin(adder_32_cout), .cout(adder_33_cout));
  and and_1 (and_1_out, not_3_out, sdelay24_1_q);
  and and_2 (and_2_out, not_3_out, sdelay24_2_q);
  and and_3 (and_3_out, not_3_out, sdelay24_3_q);
  and and_4 (and_4_out, not_3_out, sdelay24_4_q);
  and and_5 (and_5_out, not_3_out, sdelay24_5_q);
  and and_6 (and_6_out, not_3_out, sdelay24_6_q);
  and and_7 (and_7_out, not_3_out, sdelay24_7_q);
  and and_8 (and_8_out, not_3_out, sdelay24_8_q);
  and and_9 (and_9_out, not_3_out, sdelay24_9_q);
  and and_10 (and_10_out, not_3_out, sdelay24_10_q);
  or or_1 (or_1_out, and_1_out, sr_bit_24_q);
  or or_2 (or_2_out, and_2_out, sr_bit_25_q);
  or or_3 (or_3_out, and_3_out, sr_bit_26_q);
  or or_4 (or_4_out, and_4_out, sr_bit_27_q);
  or or_5 (or_5_out, and_5_out, sr_bit_28_q);
  or or_6 (or_6_out, and_6_out, sr_bit_29_q);
  or or_7 (or_7_out, and_7_out, sr_bit_30_q);
  or or_8 (or_8_out, and_8_out, sr_bit_31_q);
  or or_9 (or_9_out, and_9_out, sr_bit_32_q);
  or or_10 (or_10_out, and_10_out, d_latch_66_nq);
  SR_BIT sr_bit_23 (.C2(FCLK2), .C1(FCLK1), .D(or_1_out), .Q(sr_bit_23_q));  // open: nQ
  SR_BIT sr_bit_24 (.C2(FCLK2), .C1(FCLK1), .D(or_2_out), .Q(sr_bit_24_q));  // open: nQ
  SR_BIT sr_bit_25 (.C2(FCLK2), .C1(FCLK1), .D(or_3_out), .Q(sr_bit_25_q));  // open: nQ
  SR_BIT sr_bit_26 (.C2(FCLK2), .C1(FCLK1), .D(or_4_out), .Q(sr_bit_26_q));  // open: nQ
  SR_BIT sr_bit_27 (.C2(FCLK2), .C1(FCLK1), .D(or_5_out), .Q(sr_bit_27_q));  // open: nQ
  SR_BIT sr_bit_28 (.C2(FCLK2), .C1(FCLK1), .D(or_6_out), .Q(sr_bit_28_q));  // open: nQ
  SR_BIT sr_bit_29 (.C2(FCLK2), .C1(FCLK1), .D(or_7_out), .Q(sr_bit_29_q));  // open: nQ
  SR_BIT sr_bit_30 (.C2(FCLK2), .C1(FCLK1), .D(or_8_out), .Q(sr_bit_30_q));  // open: nQ
  SR_BIT sr_bit_31 (.C2(FCLK2), .C1(FCLK1), .D(or_9_out), .Q(sr_bit_31_q));  // open: nQ
  SR_BIT sr_bit_32 (.C2(FCLK2), .C1(FCLK1), .D(or_10_out), .Q(sr_bit_32_q));  // open: nQ
  D_LATCH d_latch_66 (.EN(FCLK2), .D(1'b1), .nQ(d_latch_66_nq));  // open: Q
  // NOT_Gate not_30 is placed but not wired

  // Notes on the sheet:
  //   3114
  //   3108
  //   3124
  //   3091
  //   3093
  //   3097
  //   3099
  //   3185
  //   3182
  //   3527
  //   3198
  //   3533
  //   3534
  //   3213
  //   3538
  //   3539
  //   3228
  //   3543
  //   3544
  //   3243
  //   3548
  //   3549
  //   3258
  //   3553
  //   3554
  //   3274
  //   3558
  //   3559
  //   3288
  //   3563
  //   3564
  //   3303
  //   3568
  //   3569
  //   3318
  //   3573
  //   3574
  //   3332
  //   3183
  //   3199
  //   3214
  //   3229
  //   3244
  //   3259
  //   3273
  //   3289
  //   3304
  //   3319
  //   3333
  //   3184
  //   3181
  //   3200
  //   3197
  //   3215
  //   3212
  //   3230
  //   3227
  //   3245
  //   3242
  //   3260
  //   3257
  //   3275
  //   3272
  //   3290
  //   3287
  //   3305
  //   3302
  //   3320
  //   3317
  //   3334
  //   3331
  //   FA_SEQ
  //   FA_SEQ
  //   FA_SEQ
  //   FA_SEQ
  //   FA_SEQ
  //   FA_SEQ
  //   FA_SEQ
  //   FA_SEQ
  //   FA_SEQ
  //   FA_SEQ
  //   FA_SEQ
  //   3177
  //   3179
  //   3193
  //   3194
  //   3208
  //   3210
  //   3223
  //   3225
  //   3239
  //   3240
  //   3253
  //   3254
  //   3268
  //   3270
  //   3283
  //   3285
  //   3298
  //   3300
  //   3313
  //   3315
  //   3327
  //   3329
  //   3176
  //   3192
  //   3207
  //   3222
  //   3237
  //   3252
  //   3267
  //   3282
  //   3297
  //   3312
  //   3326
  //   3175
  //   3191
  //   3206
  //   3221
  //   3236
  //   3251
  //   3266
  //   3281
  //   3296
  //   3311
  //   3325
  //   3171
  //   3174
  //   3187
  //   3190
  //   3202
  //   3205
  //   3217
  //   3220
  //   3232
  //   3235
  //   3246
  //   3250
  //   3262
  //   3265
  //   3277
  //   3280
  //   3292
  //   3295
  //   3307
  //   3310
  //   3321
  //   3324
  //   3391
  //   3173
  //   3189
  //   3204
  //   3219
  //   3234
  //   3249
  //   3264
  //   3279
  //   3294
  //   3309
  //   3323
  //   3170
  //   A2
  //   A1
  //   3186
  //   A2
  //   A1
  //   3201
  //   A2
  //   A1
  //   3216
  //   A2
  //   A1
  //   3231
  //   A2
  //   A1
  //   3247
  //   A2
  //   A1
  //   3261
  //   A2
  //   A1
  //   3276
  //   A2
  //   A1
  //   3291
  //   A2
  //   A1
  //   3306
  //   A2
  //   A1
  //   B
  //   B
  //   B
  //   B
  //   B
  //   B
  //   B
  //   B
  //   B
  //   B
  //   3110
  //   AON21SR
  //   AON21SR
  //   AON21SR
  //   AON21SR
  //   AON21SR
  //   AON21SR
  //   AON21SR
  //   AON21SR
  //   AON21SR
  //   AON21SR
endmodule
