// Logisim project SEGA 315-5309.circ as structural Verilog: 5 circuits, main circuit main
module main (
  input  VCLK,
  input  nM3,
  input  TEST,
  input  nSRES,
  input  NTSC,
  input  nVTOZ,
  input  nZTOV,
  input  nLWR,
  input  nIO,
  input  nCAS0,
  input  VA1,
  input  VA2,
  input  VA3,
  input  VA4,
  input  VA5,
  input  VA6,
  input  VA7,
  input  ZA0,
  input  ZA1,
  input  ZA2,
  input  ZA3,
  input  ZA4,
  input  ZA5,
  input  ZA6,
  input  ZA7,
  input  VD0_i,
  input  VD1_i,
  input  VD2_i,
  input  VD3_i,
  input  VD4_i,
  input  VD5_i,
  input  VD6_i,
  input  VD7_i,
  input  VD8_i,
  input  VD9_i,
  input  VD10_i,
  input  VD11_i,
  input  VD12_i,
  input  VD13_i,
  input  VD14_i,
  input  VD15_i,
  input  ZD0_i,
  input  ZD1_i,
  input  ZD2_i,
  input  ZD3_i,
  input  ZD4_i,
  input  ZD5_i,
  input  ZD6_i,
  input  ZD7_i,
  input  EM31,
  input  EM32,
  input  EM33,
  input  EM34,
  input  EM36,
  input  EM38,
  input  EM37,
  input  EM11,
  input  EM12,
  input  EM13,
  input  EM14,
  input  EM16,
  input  EM18,
  input  EM17,
  input  EM21,
  input  EM22,
  input  EM23,
  input  EM24,
  input  EM26,
  input  EM28,
  input  EM27,
  input  FREQ,
  input  LANG,
  input  nDISK,
  input  nFRES,
  output FRES_o,
  output ZD7_o,
  output ZD6_o,
  output ZD5_o,
  output ZD4_o,
  output ZD3_o,
  output ZD2_o,
  output ZD1_o,
  output ZD0_o,
  output VD0_o,
  output VD1_o,
  output VD2_o,
  output VD3_o,
  output VD4_o,
  output VD5_o,
  output VD6_o,
  output VD7_o,
  output VD8_o,
  output VD9_o,
  output VD10_o,
  output VD11_o,
  output VD12_o,
  output VD13_o,
  output VD14_o,
  output VD15_o,
  output VA7_2,
  output VA6_2,
  output VA5_2,
  output VA4_2,
  output VA3_2,
  output VA2_2,
  output VA1_2,
  output ZA1_o,
  output ZA2_o,
  output ZA3_o,
  output ZA4_o,
  output ZA5_o,
  output ZA6_o,
  output ZA7_o,
  output EM31_2,
  output EM32_2,
  output EM33_2,
  output EM34_2,
  output nHL,
  output EM36_2,
  output EM38_2,
  output EM37_2,
  output EM11_2,
  output EM12_2,
  output EM13_2,
  output EM14_2,
  output EM16_2,
  output EM18_2,
  output EM17_2,
  output EM21_2,
  output EM22_2,
  output EM23_2,
  output EM24_2,
  output EM26_2,
  output EM28_2,
  output EM27_2
);

  wire _1_out, _2_out, _3_out, _4_out, _6_out, _7_out, _8_out, _9_out, _10_out, _11_out, _12_out, _13_out,
       _14_out, _15_out, _16_out, _17_q, _46_out, _47_q, _54_out, _56_out, _57_out, _58_out, _59_out,
       _60_out, _61_out, _63_out, _64_out, _65_out, _67_out, _68_out, _69_out, _70_out, _71_out, _72_out,
       _73_out, _78_nq, _79_out, _80_co, _80_nq, _81_co, _81_nq, _81_q, _107_out, _108_out, _109_out,
       _110_out, _111_out, _112_out, _113_q, _114_out, _116_out, _117_out, _120_out, _121_out, _122_out,
       _125_out, _126_out, _128_out, _129_co, _129_nq, _130_co, _130_nq, _131_out, _132_out, _133_co,
       _133_nq, _134_nq, _156_q, _165_q, _167_out, _168_out, _169_out, _170_out, _171_out, _174_out,
       _175_out, _176_out, _177_q, _179_q, _182_q, _188_co, _188_nq, _198_out, _203_out, _205_out, _206_out,
       _207_2_out, _207_out, _211_q, _212_q, _212_qn, _215_q, _217_out, _218_out, _219_out, _220_qn,
       _221_out, _222_out, _223_out, _224_out, _225_out, _226_out, _227_out, _229_q, _231_q, _234_q, _236_q,
       _237_out, _242_out, _244_q, _246_nq, _249_nq, _250_nq, _251_nq, _252_nq, _255_q, _262_out, _264_out,
       _288_out, _297_nq, _301_out, _304_nq, _319_nq, _324_out, _325_out, _326_out, _327_out, _328_out,
       _330_out, _332_out, _333_out, _334_out, _336_out, _337_out, _338_out, _341_out, _342_out, _344_q,
       _346_q, _348_out, _349_out, _354_q, _354_qn, _393_out, _394_out, _395_out, _398_out, _399_out,
       _401_out, _402_out, _405_out, _406_out, _407_out, _408_q, _409_out, _410_q, _410_qn, _411_q, _411_qn,
       _412_out, _413_out, _414_q, _414_qn, _415_out, _416_q, _416_qn, _417_out, _418_q, _418_qn, _419_q,
       _420_out, _426_q, _429_q, _432_out, _463_q, _463_qn, _464_q, _464_qn, _465_out, _466_q, _466_qn,
       _468_q, _468_qn, _469_out, _470_out, _471_out, _472_out, _473_out, _474_out, _475_out, _476_out,
       _477_out, _478_out, _479_out, _480_out, _481_out, _482_out, _483_out, _484_out, _485_out, _547_out,
       _548_out, _549_out, _550_out, _551_out, _552_out, _553_out, _554_out, _555_out, _556_out, _557_q,
       _557_qn, _558_out, _559_q, _559_qn, _560_out, _561_out, _562_out, _563_out, _616_q, _616_qn, _617_out,
       _618_out, _619_out, _620_out, _642_out, _643_out, _644_out, _645_out, _666_out, _676_out, _677_out,
       _681_out, _682_out, _684_out, _694_out, _695_out, _697_out, ADR0, ADR1, ADR2, ADR3, ADR4, ADR5, ADR6,
       ADR7, d_ff_1_q, d_ff_2_q, d_ff_3_q, d_ff_4_q, d_ff_5_q, d_ff_6_q, d_ff_7_q, d_ff_8_q, DB0, DB1, DB2,
       DB3, DB4, DB5, DB6, DB7, DEC0_1, DEC0_2, DEC0_4, DEC0_5, DEC0_7, DEC0_SEL, DEC1_0, DEC1_3, DEC1_6,
       DEC1_SEL, DEC2_1, DEC2_2, DEC2_3, DEC2_4, DEC2_5, DEC2_6, DEC2_7, DEC2_SEL, DIV0, DIV1, DIV2, DIV3,
       DIV4, DIV5, DIV6, FRES, FRES0, g_340, multiplexer_4_out, multiplexer_5_out, multiplexer_6_out,
       multiplexer_7_out, multiplexer_8_out, multiplexer_9_out, multiplexer_10_out, multiplexer_11_out,
       multiplexer_42_out, MUX_CTRL, nM3_0, not_1_out, not_2_out, not_3_out, not_4_out, not_5_out, not_6_out,
       not_7_out, not_8_out, not_9_out, not_10_out, not_11_out, not_12_out, not_13_out, not_14_out,
       not_15_out, not_16_out, PB4_o, PB5_i, PB6_i, UCLK1, UCLK2, undriven, VCLK_t, VD0_o_t, VD1_o_t,
       VD2_o_t, VD3_o_t, VD4_o_t, VD5_o_t, VD6_o_t, VD7_o_t;
  wire [0:0] controlled_buffer_11_out;
  wire [1:0] _321_q;
  wire [2:0] _322_out, undriven_2;
  wire [3:0] multiplexer_14_out, multiplexer_18_out, multiplexer_22_out, multiplexer_26_out,
       multiplexer_30_out, multiplexer_31_out, multiplexer_36_out, multiplexer_37_out, multiplexer_38_out,
       multiplexer_39_out, multiplexer_40_out, multiplexer_41_out;
  wire [7:0] _249_q, _390_q;

  Clock clock_1 (.out(VCLK_t));
  buf _124 (nM3_0, nM3);
  and _645 (_645_out, _132_out, 1'b1);
  and _642 (_642_out, _645_out, _79_out);
  not _666 (_666_out, NTSC);
  and _128 (_128_out, 1'b1, _644_out, 1'b1);
  and _242 (_242_out, 1'b1, _645_out, _644_out);
  nor _643 (_643_out, FRES_o, _642_out);
  buf _644 (_644_out, _643_out);
  not _12 (_12_out, ADR6);
  not _11 (_11_out, ADR7);
  D_Flip_Flop _595 (.clk(VCLK_t), .D(nSRES), .Q(FRES0), .Qn(FRES_o));  // open: preset, en, reset
  _1_bit_cnt _129 (
    .C(VCLK_t), .CIN(_128_out), .VAL(_666_out), .nLD(_644_out), .nRES(1'b1), .nQ(_129_nq), .CO(_129_co));  // open: Q
  _1_bit_cnt _130 (
    .C(VCLK_t), .CIN(_129_co), .VAL(1'b0), .nLD(_644_out), .nRES(1'b1), .nQ(_130_nq), .CO(_130_co));  // open: Q
  _1_bit_cnt _133 (
    .C(VCLK_t), .CIN(_130_co), .VAL(1'b1), .nLD(_644_out), .nRES(1'b1), .nQ(_133_nq), .CO(_133_co));  // open: Q
  _1_bit_cnt _134 (.C(VCLK_t), .CIN(_133_co), .VAL(1'b1), .nLD(_644_out), .nRES(1'b1), .nQ(_134_nq));  // open: Q, CO
  _1_bit_cnt _188 (
    .C(VCLK_t), .CIN(_242_out), .VAL(1'b1), .nLD(_644_out), .nRES(1'b1), .nQ(_188_nq), .CO(_188_co));  // open: Q
  _1_bit_cnt _80 (
    .C(VCLK_t), .CIN(_188_co), .VAL(1'b0), .nLD(_644_out), .nRES(1'b1), .nQ(_80_nq), .CO(_80_co));  // open: Q
  _1_bit_cnt _81 (
    .C(VCLK_t), .CIN(_80_co), .VAL(1'b0), .nLD(_644_out), .nRES(1'b1), .Q(_81_q), .nQ(_81_nq), .CO(_81_co));
  _1_bit_cnt _78 (.C(VCLK_t), .CIN(_81_co), .VAL(1'b1), .nLD(_644_out), .nRES(1'b1), .nQ(_78_nq));  // open: Q, CO
  Multiplexer #(.width(4), .disabled(0), .enable("false")) multiplexer_1 (
    .in0({ZA0, ZA1, ZA2, ZA3}), .in1({VA1, VA2, VA3, VA4}), .out({ADR0, ADR1, ADR2, ADR3}), .sel(nM3));
  Multiplexer #(.width(4), .disabled(0), .enable("false")) multiplexer_2 (
    .in0({ZA4, ZA5, ZA6, ZA7}), .in1({VA5, VA6, VA7, 1'b0}), .out({ADR4, ADR5, ADR6, ADR7}), .sel(nM3));
  nor _46 (_46_out, ADR4, ADR5, ADR6, ADR7);
  nor _16 (_16_out, ADR4, ADR3, ADR2);
  and _14 (_14_out, ADR4, ADR2, ADR3);
  nand _10 (_10_out, ADR7, ADR6);
  or _8 (_8_out, ADR5, ADR1);
  or _620 (_620_out, nLWR, nIO);
  buf _376 (FRES, FRES0);
  nor _15 (_15_out, _16_out, _14_out);
  nand _13 (_13_out, 1'b1, ADR5, _12_out, _11_out, ADR1, ADR4, ADR2, ADR3);
  nor _132 (_132_out, _134_nq, _133_nq, _130_nq, _129_nq);
  nor _79 (_79_out, _78_nq, _81_nq, _80_nq, _188_nq);
  or _7 (_7_out, _15_out, _10_out, _8_out, nM3);
  or _9 (_9_out, nM3, _13_out, _620_out);
  nand _169 (_169_out, _46_out, nM3);
  and _6 (_6_out, _7_out, _9_out);
  Multiplexer #(.disabled(0), .enable("false")) multiplexer_3 (.in0(_81_q), .in1(VCLK_t), .out(DIV0), .sel(TEST));
  buf _237 (_237_out, FRES0);
  not _107 (_107_out, ADR3);
  T_Flip_Flop _239 (.clk(DIV0), .T(_237_out), .Q(DIV1));  // open: Qn, preset, reset, en
  T_Flip_Flop _240 (.clk(DIV1), .T(_237_out), .Q(DIV2));  // open: Qn, preset, reset, en
  T_Flip_Flop _244 (.clk(DIV2), .T(_237_out), .Q(_244_q));  // open: Qn, preset, reset, en
  T_Flip_Flop _243 (.clk(_244_q), .T(_237_out), .Q(DIV3));  // open: Qn, preset, reset, en
  T_Flip_Flop _238 (.clk(DIV3), .T(_237_out), .Q(DIV4));  // open: Qn, preset, reset, en
  T_Flip_Flop _347 (.clk(DIV4), .T(_237_out), .Q(DIV5));  // open: Qn, preset, reset, en
  T_Flip_Flop _346 (.clk(DIV5), .T(_237_out), .Q(_346_q));  // open: Qn, preset, reset, en
  T_Flip_Flop _345 (.clk(_346_q), .T(_237_out), .Q(DIV6));  // open: Qn, preset, reset, en
  and _170 (_170_out, _169_out, _6_out);
  or _341 (_341_out, _6_out, ADR0);
  not _337 (_337_out, ADR3);
  not _174 (_174_out, ADR3);
  or _108 (_108_out, nIO, nCAS0);
  not _227 (_227_out, _107_out);
  nor _96 (MUX_CTRL, nIO, _170_out, nCAS0);
  D_Flip_Flop _340 (.clk(_341_out), .D(VD4_i), .Q(g_340));  // open: Qn, preset, en, reset
  nor _335 (DEC0_SEL, _169_out, _337_out, _620_out);
  nor _173 (DEC1_SEL, _169_out, _174_out, _108_out);
  nor _282 (DEC2_SEL, _169_out, _227_out, _620_out);
  S_latch _249 (.EN(not_1_out), .D(DB0), .Q(_249_q[0]), .nQ(_249_nq));
  S_latch _304 (.EN(not_1_out), .D(DB1), .Q(_249_q[1]), .nQ(_304_nq));
  S_latch _250 (.EN(not_1_out), .D(DB2), .Q(_249_q[2]), .nQ(_250_nq));
  S_latch _246 (.EN(not_1_out), .D(DB3), .Q(_249_q[3]), .nQ(_246_nq));
  S_latch _252 (.EN(not_1_out), .D(DB4), .Q(_249_q[4]), .nQ(_252_nq));
  S_latch _319 (.EN(not_1_out), .D(DB5), .Q(_249_q[5]), .nQ(_319_nq));
  S_latch _251 (.EN(not_1_out), .D(DB6), .Q(_249_q[6]), .nQ(_251_nq));
  S_latch _297 (.EN(not_1_out), .D(DB7), .Q(_249_q[7]), .nQ(_297_nq));
  not not_1 (not_1_out, DEC0_2);
  D_Flip_Flop _156 (.clk(DEC0_4), .Q(_156_q), .en(not_2_out));  // open: D, Qn, preset, reset
  D_Flip_Flop _47 (.clk(DEC0_4), .Q(_47_q), .en(not_2_out));  // open: D, Qn, preset, reset
  D_Flip_Flop _165 (.clk(DEC0_4), .Q(_165_q), .en(not_2_out));  // open: D, Qn, preset, reset
  D_Flip_Flop _321 (.clk(DEC0_4), .Q(_321_q[0]), .en(not_2_out));  // open: D, Qn, preset, reset
  D_Flip_Flop _277 (.clk(DEC0_4), .Q(_321_q[1]), .en(not_2_out));  // open: D, Qn, preset, reset
  and _131 (_131_out, FRES0, nM3);
  not not_2 (not_2_out, _131_out);
  not not_3 (not_3_out, _412_out);
  not not_4 (not_4_out, not_3_out);
  Multiplexer #(.disabled(0), .enable("false")) multiplexer_4 (
    .in0(_249_nq), .in1(_179_q), .out(multiplexer_4_out), .sel(not_4_out));
  Multiplexer #(.disabled(0), .enable("false")) multiplexer_5 (
    .in0(_304_nq), .in1(_182_q), .out(multiplexer_5_out), .sel(not_4_out));
  Multiplexer #(.disabled(0), .enable("false")) multiplexer_6 (
    .in0(_250_nq), .in1(_229_q), .out(multiplexer_6_out), .sel(not_4_out));
  Multiplexer #(.disabled(0), .enable("false")) multiplexer_7 (
    .in0(_246_nq), .in1(_231_q), .out(multiplexer_7_out), .sel(not_4_out));
  Multiplexer #(.disabled(0), .enable("false")) multiplexer_8 (
    .in0(_252_nq), .in1(_234_q), .out(multiplexer_8_out), .sel(not_4_out));
  Multiplexer #(.disabled(0), .enable("false")) multiplexer_9 (
    .in0(_319_nq), .in1(_236_q), .out(multiplexer_9_out), .sel(not_4_out));
  Multiplexer #(.disabled(0), .enable("false")) multiplexer_10 (
    .in0(_251_nq), .in1(_344_q), .out(multiplexer_10_out), .sel(not_4_out));
  Multiplexer #(.disabled(0), .enable("false")) multiplexer_11 (
    .in0(_297_nq), .in1(1'b0), .out(multiplexer_11_out), .sel(not_4_out));
  or _342 (_342_out, UCLK1, 1'b0);
  Multiplexer #(.select(2), .disabled(0), .enable("false")) multiplexer_12 (
    .in0(DIV0), .in1(DIV2), .in2(DIV1), .in3(DIV3), .out(UCLK2), .sel(_321_q));
  Multiplexer #(.select(2), .disabled(0), .enable("false")) multiplexer_13 (
    .in0(DIV3), .in1(DIV5), .in2(DIV4), .in3(DIV6), .out(UCLK1), .sel(_321_q));
  D_Flip_Flop _177 (.clk(_342_out), .D(multiplexer_4_out), .Q(_177_q), .reset(not_5_out));  // open: Qn, preset, en
  D_Flip_Flop _179 (.clk(_342_out), .D(multiplexer_5_out), .Q(_179_q), .reset(not_5_out));  // open: Qn, preset, en
  D_Flip_Flop _182 (.clk(_342_out), .D(multiplexer_6_out), .Q(_182_q), .reset(not_5_out));  // open: Qn, preset, en
  D_Flip_Flop _229 (.clk(_342_out), .D(multiplexer_7_out), .Q(_229_q), .reset(not_5_out));  // open: Qn, preset, en
  D_Flip_Flop _231 (.clk(_342_out), .D(multiplexer_8_out), .Q(_231_q), .reset(not_5_out));  // open: Qn, preset, en
  D_Flip_Flop _234 (.clk(_342_out), .D(multiplexer_9_out), .Q(_234_q), .reset(not_5_out));  // open: Qn, preset, en
  D_Flip_Flop _236 (.clk(_342_out), .D(multiplexer_10_out), .Q(_236_q), .reset(not_5_out));  // open: Qn, preset, en
  D_Flip_Flop _344 (.clk(_342_out), .D(multiplexer_11_out), .Q(_344_q), .reset(not_5_out));  // open: Qn, preset, en
  not _176 (_176_out, _177_q);
  not not_5 (not_5_out, _47_q);
  and _175 (_175_out, _412_out, _176_out);
  or _223 (_223_out, _410_q, _224_out);
  not _470 (_470_out, _224_out);
  or _222 (_222_out, _224_out, _220_qn);
  D_Flip_Flop _113 (.clk(UCLK1), .D(_175_out), .Q(_113_q), .preset(not_5_out));  // open: Qn, en, reset
  not _117 (_117_out, _47_q);
  D_Flip_Flop _17 (.Q(_17_q));  // open: clk, D, Qn, preset, en, reset
  not not_6 (not_6_out, _395_out);
  buf _395 (_395_out, FRES);
  nand _472 (_472_out, _410_q, _464_q);
  nand _473 (_473_out, _410_q, _463_q);
  nand _474 (_474_out, _410_q, _468_qn);
  nand _465 (_465_out, _464_qn, _410_qn, _463_qn, _468_q);
  nand _551 (_551_out, _468_q, _463_qn);
  nand _552 (_552_out, _463_q, _468_qn);
  nand _548 (_548_out, _463_q, _464_q);
  nand _550 (_550_out, _468_q, _463_qn, _464_qn);
  nand _549 (_549_out, _468_qn, _464_q);
  nor _469 (_469_out, _468_q, _224_out);
  and _114 (_114_out, _113_q, _47_q);
  and _120 (_120_out, _117_out, _17_q);
  D_Flip_Flop _410 (.clk(UCLK2), .D(_471_out), .Q(_410_q), .Qn(_410_qn), .preset(not_6_out));  // open: en, reset
  nand _553 (_553_out, _470_out, _551_out, _552_out);
  nand _221 (_221_out, _223_out, _222_out);
  or _119 (PB4_o, _114_out, _120_out);
  nand _471 (_471_out, _472_out, _473_out, _474_out, _465_out, _470_out, 1'b1);
  nand _547 (_547_out, _470_out, _548_out, _550_out, _549_out);
  D_Flip_Flop _463 (.clk(UCLK2), .D(_553_out), .Q(_463_q), .Qn(_463_qn), .preset(not_6_out));  // open: en, reset
  buf _420 (_420_out, FRES);
  nand _415 (_415_out, _414_qn, _411_q, _418_qn, _416_q);
  nand _478 (_478_out, _414_q, _411_q);
  nand _477 (_477_out, _418_q, _411_q);
  nand _479 (_479_out, _418_q, _414_q);
  nand _413 (_413_out, _429_q, _418_qn, _411_qn);
  nand _485 (_485_out, _411_q, _416_q, _414_q);
  nand _480 (_480_out, _418_q, _414_q, _411_qn);
  nand _484 (_484_out, _416_q, _418_q, _411_q);
  nand _481 (_481_out, _418_qn, _411_q);
  nand _417 (_417_out, _416_qn, _414_qn, _411_q, _418_qn);
  nand _412 (_412_out, 1'b1, _414_qn, _416_qn, _429_q, _418_qn, _411_qn);
  D_Flip_Flop _464 (.clk(UCLK2), .D(_547_out), .Q(_464_q), .Qn(_464_qn), .preset(not_6_out));  // open: en, reset
  not not_7 (not_7_out, _420_out);
  not _348 (_348_out, _412_out);
  not _349 (_349_out, UCLK1);
  buf _432 (_432_out, FRES0);
  not not_8 (not_8_out, _432_out);
  not not_9 (not_9_out, DEC0_2);
  D_Flip_Flop _411 (.clk(UCLK1), .D(_476_out), .Q(_411_q), .Qn(_411_qn), .preset(not_7_out));  // open: en, reset
  nand _476 (_476_out, _415_out, _478_out, _477_out, _479_out);
  nand _475 (_475_out, _479_out, _415_out, _413_out);
  nand _483 (_483_out, _485_out, _413_out, _480_out, _484_out);
  nand _482 (_482_out, _413_out, _480_out, _481_out);
  D_Flip_Flop _468 (.clk(UCLK2), .D(_469_out), .Q(_468_q), .Qn(_468_qn), .reset(not_6_out));  // open: preset, en
  D_Flip_Flop _220 (.clk(UCLK2), .D(_221_out), .Qn(_220_qn), .reset(not_6_out));  // open: Q, preset, en
  nor _224 (_224_out, _220_qn, _212_q, _225_out);
  J_K_Flip_Flop #(.trigger("falling")) _354 (
    .J(_348_out), .clk(_349_out), .K(1'b0), .Q(_354_q), .Qn(_354_qn), .preset(not_9_out), .reset(not_8_out));  // open: en
  not not_10 (not_10_out, _354_qn);
  D_Flip_Flop _414 (.clk(UCLK1), .D(_475_out), .Q(_414_q), .Qn(_414_qn), .preset(not_7_out));  // open: en, reset
  D_Flip_Flop _426 (.clk(_419_q), .D(1'b0), .Q(_426_q), .preset(not_10_out), .reset(not_8_out));  // open: Qn, en
  D_Flip_Flop _416 (.clk(UCLK1), .D(_483_out), .Q(_416_q), .Qn(_416_qn), .preset(not_7_out));  // open: en, reset
  not not_11 (not_11_out, _165_q);
  D_Flip_Flop _212 (.clk(UCLK2), .D(PB5_i), .Q(_212_q), .Qn(_212_qn), .preset(not_11_out));  // open: en, reset
  not _226 (_226_out, _212_q);
  D_Flip_Flop _418 (.clk(UCLK1), .D(_482_out), .Q(_418_q), .Qn(_418_qn), .reset(not_7_out));  // open: preset, en
  D_Flip_Flop _429 (.clk(UCLK2), .D(_426_q), .Q(_429_q));  // open: Qn, preset, en, reset
  D_Flip_Flop _419 (.clk(UCLK1), .D(_417_out), .Q(_419_q), .reset(not_7_out));  // open: Qn, preset, en
  not not_12 (not_12_out, _393_out);
  buf _393 (_393_out, FRES);
  nand _618 (_618_out, _466_q, _559_q, _616_q);
  nand _619 (_619_out, _557_q, _616_q, _466_q);
  nand _218 (_218_out, _226_out, _220_qn, _557_qn, _466_qn);
  nand _555 (_555_out, _466_q, _557_qn, _616_q, _559_qn);
  nand _556 (_556_out, _466_q, _559_q, _557_qn);
  nand _562 (_562_out, _466_q, _557_q, _559_q);
  nand _563 (_563_out, _557_q, _466_q);
  nand _554 (_554_out, _466_q, _557_qn, _616_qn, _559_qn);
  and _219 (_219_out, _557_qn, _466_qn);
  not _225 (_225_out, _219_out);
  D_Flip_Flop _616 (.clk(_410_qn), .D(_617_out), .Q(_616_q), .Qn(_616_qn), .reset(not_12_out));  // open: preset, en
  and _394 (_394_out, 1'b1, _212_q);
  nand _617 (_617_out, _618_out, _619_out, _218_out, _554_out);
  nand _558 (_558_out, _554_out, _555_out, _218_out, _556_out);
  nand _560 (_560_out, _554_out, _555_out, _562_out, _218_out);
  nand _561 (_561_out, _555_out, _218_out, _563_out, _556_out);
  D_Flip_Flop _557 (.clk(_410_qn), .D(_558_out), .Q(_557_q), .Qn(_557_qn), .reset(not_12_out));  // open: preset, en
  D_Flip_Flop _559 (.clk(_410_qn), .D(_560_out), .Q(_559_q), .Qn(_559_qn), .reset(not_12_out));  // open: preset, en
  D_Flip_Flop d_ff_1 (.clk(_410_qn), .D(_394_out), .Q(d_ff_1_q), .reset(not_11_out));  // open: Qn, preset, en
  D_Flip_Flop d_ff_2 (.clk(_410_qn), .D(d_ff_1_q), .Q(d_ff_2_q), .reset(not_11_out));  // open: Qn, preset, en
  D_Flip_Flop d_ff_3 (.clk(_410_qn), .D(d_ff_2_q), .Q(d_ff_3_q), .reset(not_11_out));  // open: Qn, preset, en
  D_Flip_Flop d_ff_4 (.clk(_410_qn), .D(d_ff_3_q), .Q(d_ff_4_q), .reset(not_11_out));  // open: Qn, preset, en
  D_Flip_Flop d_ff_5 (.clk(_410_qn), .D(d_ff_4_q), .Q(d_ff_5_q), .reset(not_11_out));  // open: Qn, preset, en
  D_Flip_Flop d_ff_6 (.clk(_410_qn), .D(d_ff_5_q), .Q(d_ff_6_q), .reset(not_11_out));  // open: Qn, preset, en
  D_Flip_Flop d_ff_7 (.clk(_410_qn), .D(d_ff_6_q), .Q(d_ff_7_q), .reset(not_11_out));  // open: Qn, preset, en
  D_Flip_Flop d_ff_8 (.clk(_410_qn), .D(d_ff_7_q), .Q(d_ff_8_q), .reset(not_11_out));  // open: Qn, preset, en
  D_Flip_Flop _466 (.clk(_410_qn), .D(_561_out), .Q(_466_q), .Qn(_466_qn), .reset(not_12_out));  // open: preset, en
  RC_DELAY _677 (.IN(d_ff_1_q), .OUT(_677_out));
  RC_DELAY _684 (.IN(d_ff_2_q), .OUT(_684_out));
  RC_DELAY _676 (.IN(d_ff_3_q), .OUT(_676_out));
  RC_DELAY _681 (.IN(d_ff_4_q), .OUT(_681_out));
  RC_DELAY _694 (.IN(d_ff_5_q), .OUT(_694_out));
  RC_DELAY _697 (.IN(d_ff_6_q), .OUT(_697_out));
  RC_DELAY _682 (.IN(d_ff_7_q), .OUT(_682_out));
  RC_DELAY _695 (.IN(d_ff_8_q), .OUT(_695_out));
  buf _262 (_262_out, FRES0);
  and _217 (_217_out, undriven, _262_out);
  D_Flip_Flop _408 (.clk(_410_qn), .D(_554_out), .Q(_408_q), .preset(not_12_out));  // open: Qn, en, reset
  not not_13 (not_13_out, _217_out);
  or _409 (_409_out, _410_qn, _408_q);
  D_Flip_Flop _390 (.clk(_409_out), .D(_677_out), .Q(_390_q[0]), .reset(not_14_out));  // open: Qn, preset, en
  D_Flip_Flop _274 (.clk(_409_out), .D(_684_out), .Q(_390_q[1]), .reset(not_14_out));  // open: Qn, preset, en
  D_Flip_Flop _391 (.clk(_409_out), .D(_676_out), .Q(_390_q[2]), .reset(not_14_out));  // open: Qn, preset, en
  D_Flip_Flop _318 (.clk(_409_out), .D(_681_out), .Q(_390_q[3]), .reset(not_14_out));  // open: Qn, preset, en
  D_Flip_Flop _216 (.clk(_409_out), .D(_694_out), .Q(_390_q[4]), .reset(not_14_out));  // open: Qn, preset, en
  D_Flip_Flop _202 (.clk(_409_out), .D(_697_out), .Q(_390_q[5]), .reset(not_14_out));  // open: Qn, preset, en
  D_Flip_Flop _315 (.clk(_409_out), .D(_682_out), .Q(_390_q[6]), .reset(not_14_out));  // open: Qn, preset, en
  D_Flip_Flop _208 (.clk(_409_out), .D(_695_out), .Q(_390_q[7]), .reset(not_14_out));  // open: Qn, preset, en
  not not_14 (not_14_out, 1'b1);
  D_Flip_Flop _211 (.clk(_409_out), .D(_212_qn), .Q(_211_q), .reset(not_13_out));  // open: Qn, preset, en
  D_Flip_Flop _215 (.clk(_409_out), .D(1'b1), .Q(_215_q), .reset(not_13_out));  // open: Qn, preset, en
  and _207 (_207_out, _156_q, _215_q);
  Multiplexer #(.select(3), .disabled(0), .enable("false")) multiplexer_14 (
    .out(multiplexer_14_out[0]), .sel(undriven_2));  // open: in0, in1, in2, in3, in4, in5, in6, in7
  Multiplexer #(.select(3), .disabled(0), .enable("false")) multiplexer_15 (
    .out(multiplexer_14_out[1]), .sel(undriven_2));  // open: in0, in1, in2, in3, in4, in5, in6, in7
  Multiplexer #(.select(3), .disabled(0), .enable("false")) multiplexer_16 (
    .out(multiplexer_14_out[2]), .sel(undriven_2));  // open: in0, in1, in2, in3, in4, in5, in6, in7
  Multiplexer #(.select(3), .disabled(0), .enable("false")) multiplexer_17 (
    .out(multiplexer_14_out[3]), .sel(undriven_2));  // open: in0, in1, in2, in3, in4, in5, in6, in7
  Multiplexer #(.select(3), .disabled(0), .enable("false")) multiplexer_18 (
    .in2(_249_q[7]), .out(multiplexer_18_out[0]), .sel(undriven_2));  // open: in0, in1, in3, in4, in5, in6, in7
  Multiplexer #(.select(3), .disabled(0), .enable("false")) multiplexer_19 (
    .out(multiplexer_18_out[1]), .sel(undriven_2));  // open: in0, in1, in2, in3, in4, in5, in6, in7
  Multiplexer #(.select(3), .disabled(0), .enable("false")) multiplexer_20 (
    .out(multiplexer_18_out[2]), .sel(undriven_2));  // open: in0, in1, in2, in3, in4, in5, in6, in7
  Multiplexer #(.select(3), .disabled(0), .enable("false")) multiplexer_21 (
    .out(multiplexer_18_out[3]), .sel(undriven_2));  // open: in0, in1, in2, in3, in4, in5, in6, in7
  Multiplexer #(.select(3), .disabled(0), .enable("false")) multiplexer_22 (
    .out(multiplexer_22_out[0]), .sel(undriven_2));  // open: in0, in1, in2, in3, in4, in5, in6, in7
  Multiplexer #(.select(3), .disabled(0), .enable("false")) multiplexer_23 (
    .out(multiplexer_22_out[1]), .sel(undriven_2));  // open: in0, in1, in2, in3, in4, in5, in6, in7
  Multiplexer #(.select(3), .disabled(0), .enable("false")) multiplexer_24 (
    .out(multiplexer_22_out[2]), .sel(undriven_2));  // open: in0, in1, in2, in3, in4, in5, in6, in7
  Multiplexer #(.select(3), .disabled(0), .enable("false")) multiplexer_25 (
    .out(multiplexer_22_out[3]), .sel(undriven_2));  // open: in0, in1, in2, in3, in4, in5, in6, in7
  Multiplexer #(.select(3), .disabled(0), .enable("false")) multiplexer_26 (
    .out(multiplexer_26_out[0]), .sel(_322_out));  // open: in0, in1, in2, in3, in4, in5, in6, in7
  Multiplexer #(.select(3), .disabled(0), .enable("false")) multiplexer_27 (
    .out(multiplexer_26_out[1]), .sel(_322_out));  // open: in0, in1, in2, in3, in4, in5, in6, in7
  Multiplexer #(.select(3), .disabled(0), .enable("false")) multiplexer_28 (
    .out(multiplexer_26_out[2]), .sel(_322_out));  // open: in0, in1, in2, in3, in4, in5, in6, in7
  Multiplexer #(.select(3), .disabled(0), .enable("false")) multiplexer_29 (
    .in3(_390_q[7]), .out(multiplexer_26_out[3]), .sel(_322_out));  // open: in0, in1, in2, in4, in5, in6, in7
  Multiplexer #(.width(4), .disabled(0), .enable("false")) multiplexer_30 (
    .in0(multiplexer_14_out), .in1(multiplexer_18_out), .out(multiplexer_30_out), .sel(_198_out));
  and _198 (_198_out, nM3, ADR3);
  Multiplexer #(.width(4), .disabled(0), .enable("false")) multiplexer_31 (
    .in0(multiplexer_22_out), .in1(multiplexer_26_out), .out(multiplexer_31_out), .sel(_198_out));
  buf _322 (_322_out[0], _324_out);
  xnor _324 (_324_out, ADR0, nM3);
  or _2 (_2_out, _1_out, _3_out);
  buf _135 (_322_out[1], _2_out);
  buf _163 (_322_out[2], _167_out);
  and _1 (_1_out, nM3, ADR1);
  nor _3 (_3_out, nM3, _4_out);
  and _167 (_167_out, nM3, ADR2);
  Multiplexer #(.width(4), .disabled(0), .enable("false")) multiplexer_32 (
    .in0({ZD4_i, ZD5_i, ZD6_i, ZD7_i}), .in1(multiplexer_30_out), .out({VD4_o_t, VD5_o_t, VD6_o_t, VD7_o_t}),
    .sel(MUX_CTRL));
  Multiplexer #(.width(4), .disabled(0), .enable("false")) multiplexer_33 (
    .in0({ZD0_i, ZD1_i, ZD2_i, ZD3_i}), .in1(multiplexer_31_out), .out({VD0_o_t, VD1_o_t, VD2_o_t, VD3_o_t}),
    .sel(MUX_CTRL));
  not _4 (_4_out, ADR0);
  D_Flip_Flop _255 (.Q(_255_q));  // open: clk, D, Qn, preset, en, reset
  buf _206 (_206_out, _255_q);  // AND_Gate
  // AND_Gate _207_2 has open pins: out=_207_2_out
  // AND_Gate _205 has open pins: out=_205_out
  // NOR_Gate _264 has open pins: out=_264_out
  // NOR_Gate _116 has open pins: out=_116_out
  // NOR_Gate _301 has open pins: out=_301_out
  not _126 (_126_out, ZA0);
  // NOT_Gate _65 has open pins: in=open, out=_65_out
  Multiplexer #(.width(4), .disabled(0), .enable("false")) multiplexer_34 (
    .in0({VD4_i, VD5_i, VD6_i, VD7_i}), .in1({ZD4_i, ZD5_i, ZD6_i, ZD7_i}), .out({DB4, DB5, DB6, DB7}),
    .sel(_288_out));
  Multiplexer #(.width(4), .disabled(0), .enable("false")) multiplexer_35 (
    .in0({VD0_i, VD1_i, VD2_i, VD3_i}), .in1({ZD0_i, ZD1_i, ZD2_i, ZD3_i}), .out({DB0, DB1, DB2, DB3}),
    .sel(_288_out));
  not _288 (_288_out, nM3_0);
  and _125 (_125_out, nM3_0, _126_out);
  Multiplexer #(.width(4), .disabled(0), .enable("false")) multiplexer_36 (
    .in0({VD4_i, VD5_i, VD6_i, VD7_i}), .in1({VD12_i, VD13_i, VD14_i, VD15_i}), .out(multiplexer_36_out),
    .sel(_125_out));
  Multiplexer #(.width(4), .disabled(0), .enable("false")) multiplexer_37 (
    .in0({VD0_i, VD1_i, VD2_i, VD3_i}), .in1({VD8_i, VD9_i, VD10_i, VD11_i}), .out(multiplexer_37_out),
    .sel(_125_out));
  not _69 (_69_out, nCAS0);
  nor _203 (_203_out, _206_out, _207_2_out, _205_out, _264_out, _116_out, _301_out);
  nor _109 (_109_out, PB6_i, _65_out);
  Multiplexer #(.width(4), .disabled(0), .enable("false")) multiplexer_38 (
    .in0(multiplexer_36_out), .in1(multiplexer_30_out), .out(multiplexer_38_out), .sel(MUX_CTRL));
  Multiplexer #(.width(4), .disabled(0), .enable("false")) multiplexer_39 (
    .in0(multiplexer_37_out), .in1(multiplexer_31_out), .out(multiplexer_39_out), .sel(MUX_CTRL));
  or _73 (_73_out, nZTOV, nCAS0);
  and _72 (_72_out, _73_out, _71_out);
  or _71 (_71_out, nVTOZ, _69_out);
  or _68 (_68_out, nZTOV, _69_out);
  or _70 (_70_out, nCAS0, nVTOZ);
  nand _111 (_111_out, MUX_CTRL, nM3_0);
  Multiplexer #(.width(4), .disabled(0), .enable("false")) multiplexer_40 (
    .in0({ZA4, ZA5, ZA6, 1'b0}), .in1({ZA5, ZA6, ZA7, 1'b0}), .out(multiplexer_40_out), .sel(nM3));
  Multiplexer #(.width(4), .disabled(0), .enable("false")) multiplexer_41 (
    .in0({ZA0, ZA1, ZA2, ZA3}), .in1({ZA1, ZA2, ZA3, ZA4}), .out(multiplexer_41_out), .sel(nM3));
  not _121 (_121_out, nM3);
  not _110 (_110_out, _109_out);  // NOR_Gate
  assign {ZD4_o, ZD5_o, ZD6_o, ZD7_o} = _72_out ? multiplexer_38_out : 4'bz;  // Controlled_Buffer controlled_buffer_1
  assign {ZD0_o, ZD1_o, ZD2_o, ZD3_o} = _72_out ? multiplexer_39_out : 4'bz;  // Controlled_Buffer controlled_buffer_2
  and _338 (_338_out, nM3_0, _67_out);
  and _67 (_67_out, _68_out, _70_out, _111_out);
  assign VD0_o = _67_out ? VD0_o_t : 1'bz;  // Controlled_Buffer controlled_buffer_3
  assign VD1_o = _67_out ? VD1_o_t : 1'bz;  // Controlled_Buffer controlled_buffer_4
  assign VD2_o = _67_out ? VD2_o_t : 1'bz;  // Controlled_Buffer controlled_buffer_5
  assign VD3_o = _67_out ? VD3_o_t : 1'bz;  // Controlled_Buffer controlled_buffer_6
  assign VD4_o = _67_out ? VD4_o_t : 1'bz;  // Controlled_Buffer controlled_buffer_7
  assign VD5_o = _67_out ? VD5_o_t : 1'bz;  // Controlled_Buffer controlled_buffer_8
  assign VD6_o = _67_out ? VD6_o_t : 1'bz;  // Controlled_Buffer controlled_buffer_9
  assign VD7_o = _67_out ? VD7_o_t : 1'bz;  // Controlled_Buffer controlled_buffer_10
  Multiplexer #(.disabled(0), .enable("false")) multiplexer_42 (
    .in0(g_340), .in1(VD0_o_t), .out(multiplexer_42_out), .sel(nM3_0));
  assign {VA5_2, VA6_2, VA7_2, controlled_buffer_11_out[0]} = not_15_out ? multiplexer_40_out : 4'bz;  // Controlled_Buffer controlled_buffer_11
  not not_15 (not_15_out, nZTOV);
  assign {VA1_2, VA2_2, VA3_2, VA4_2} = not_15_out ? multiplexer_41_out : 4'bz;  // Controlled_Buffer controlled_buffer_12
  not not_16 (not_16_out, nVTOZ);
  nor _122 (_122_out, _121_out, _203_out);
  nor _112 (_112_out, nM3, _110_out);
  assign VD8_o = _338_out ? multiplexer_42_out : 1'bz;  // Controlled_Buffer controlled_buffer_13
  assign VD9_o = _338_out ? VD1_o_t : 1'bz;  // Controlled_Buffer controlled_buffer_14
  assign VD10_o = _338_out ? VD2_o_t : 1'bz;  // Controlled_Buffer controlled_buffer_15
  assign VD11_o = _338_out ? VD3_o_t : 1'bz;  // Controlled_Buffer controlled_buffer_16
  assign VD12_o = _338_out ? VD4_o_t : 1'bz;  // Controlled_Buffer controlled_buffer_17
  assign VD13_o = _338_out ? VD5_o_t : 1'bz;  // Controlled_Buffer controlled_buffer_18
  assign VD14_o = _338_out ? VD6_o_t : 1'bz;  // Controlled_Buffer controlled_buffer_19
  assign VD15_o = _338_out ? VD7_o_t : 1'bz;  // Controlled_Buffer controlled_buffer_20
  assign ZA1_o = not_16_out ? VA1 : 1'bz;  // Controlled_Buffer controlled_buffer_21
  assign ZA2_o = not_16_out ? VA2 : 1'bz;  // Controlled_Buffer controlled_buffer_22
  assign ZA3_o = not_16_out ? VA3 : 1'bz;  // Controlled_Buffer controlled_buffer_23
  assign ZA4_o = not_16_out ? VA4 : 1'bz;  // Controlled_Buffer controlled_buffer_24
  assign ZA5_o = not_16_out ? VA5 : 1'bz;  // Controlled_Buffer controlled_buffer_25
  assign ZA6_o = not_16_out ? VA6 : 1'bz;  // Controlled_Buffer controlled_buffer_26
  assign ZA7_o = not_16_out ? VA7 : 1'bz;  // Controlled_Buffer controlled_buffer_27
  nor _123 (nHL, _122_out, _112_out);
  not _407 (_407_out, ADR0);
  not _401 (_401_out, _407_out);
  not _325 (_325_out, ADR1);
  not _398 (_398_out, _325_out);
  not _326 (_326_out, ADR2);
  not _406 (_406_out, _326_out);
  not _171 (_171_out, ADR0);
  not _60 (_60_out, _171_out);
  not _56 (_56_out, ADR1);
  not _64 (_64_out, _56_out);
  not _168 (_168_out, ADR2);
  not _58 (_58_out, _168_out);
  not _328 (_328_out, ADR0);
  not _336 (_336_out, _328_out);
  not _330 (_330_out, ADR1);
  not _332 (_332_out, _330_out);
  not _327 (_327_out, ADR2);
  not _334 (_334_out, _327_out);
  nand _405 (_405_out, _406_out, _407_out, _398_out, DEC0_SEL);
  nand _404 (DEC0_2, _326_out, _407_out, _398_out, DEC0_SEL);
  nand _403 (DEC0_4, _406_out, _407_out, _325_out, DEC0_SEL);
  nand _402 (_402_out, _326_out, _407_out, _325_out, DEC0_SEL);
  nand _400 (DEC0_1, _326_out, _401_out, _325_out, DEC0_SEL);
  nand _399 (_399_out, _326_out, _401_out, _398_out, DEC0_SEL);
  nand _397 (DEC0_7, _406_out, _401_out, _398_out, DEC0_SEL);
  nand _396 (DEC0_5, _406_out, _401_out, _325_out, DEC0_SEL);
  nand _63 (_63_out, _58_out, _171_out, _56_out, DEC1_SEL);
  nand _172 (DEC1_0, _168_out, _171_out, _56_out, DEC1_SEL);
  nand _62 (DEC1_6, _58_out, _171_out, _64_out, DEC1_SEL);
  nand _54 (_54_out, _168_out, _171_out, _64_out, DEC1_SEL);
  nand _61 (_61_out, _58_out, _60_out, _64_out, DEC1_SEL);
  nand _59 (_59_out, _58_out, _60_out, _56_out, DEC1_SEL);
  nand _57 (_57_out, _168_out, _60_out, _56_out, DEC1_SEL);
  nand _55 (DEC1_3, _168_out, _60_out, _64_out, DEC1_SEL);
  nand _329 (DEC2_6, _334_out, _328_out, _332_out, DEC2_SEL);
  nand _333 (_333_out, _327_out, _328_out, _330_out, DEC2_SEL);
  nand _285 (DEC2_2, _327_out, _328_out, _332_out, DEC2_SEL);
  nand _287 (DEC2_4, _334_out, _328_out, _330_out, DEC2_SEL);
  nand _331 (DEC2_7, _334_out, _336_out, _332_out, DEC2_SEL);
  nand _283 (DEC2_3, _327_out, _336_out, _332_out, DEC2_SEL);
  nand _284 (DEC2_5, _334_out, _336_out, _330_out, DEC2_SEL);
  nand _286 (DEC2_1, _327_out, _336_out, _330_out, DEC2_SEL);
  // NOT_Gate not_17 is placed but not wired

  // Other names for the same wires on the sheet: VA4_i = VA4; VA3_i = VA3; VA2_i = VA2; VA1_i = VA1; VA7_i = VA7;
  //   VA6_i = VA6; VA5_i = VA5; ZA7_i = ZA7; ZA6_i = ZA6; ZA5_i = ZA5; ZA0_i = ZA0; ZA4_i = ZA4; ZA3_i = ZA3;
  //   ZA2_i = ZA2; ZA1_i = ZA1

  // Notes on the sheet:
  //   23
  //   45
  //   248
  //   388
  //   !
  //   295
  //   295
  //   228
  //   180
  //   178
  //   181
  //   232
  //   230
  //   233
  //   235
  //   291
  //   343
  //   B
  //   A
  //   !
  //   NEGEDGE
  //   SEGA 315-5309
  //   SIPO SR 4bit
  //   SIPO SR 4bit
  //   392
  //   209
  //   303
  //   298
  //   257
  //   299
  //   309
  //   271
  //   276
  //   317
  //   90
  //   91
  //   147
  //   89
  //   94
  //   204
  //   313
  //   387
  //   253
  //   201
  //   323
  //   144
  //   162
  //   289
  //   77
  //   292
  //   76
  //   290
  //   74
  //   293
  //   199
  //   43
  //   127
  //   339
  //   NC
  //   INTERNAL DATA BUS
  //   6
  //   NC
  //   2
  //   4
  //   0
  //   NC
  //   1
  //   3
  //   NC
  //   7
  //   5
  //   4
  //   NC
  //   0
  //   6
  //   2
  //   NC
  //   7
  //   NC
  //   5
  //   NC
  //   1
  //   NC
  //   3
  //   6
  //   0
  //   NC
  //   2
  //   4
  //   7
  //   3
  //   5
  //   1
endmodule

// COUNTER 1BIT
module _1_bit_cnt (
  input  C,
  input  CIN,
  input  VAL,
  input  nLD,
  input  nRES,
  output Q,
  output nQ,
  output CO
);

  wire d_ff_1_q, multiplexer_1_out, not_1_out, not_2_out, xor_1_out;

  not not_1 (not_1_out, nRES);
  xor xor_1 (xor_1_out, Q, CIN);
  and and_1 (CO, Q, CIN);
  Multiplexer #(.disabled(0), .enable("false")) multiplexer_1 (
    .in0(VAL), .in1(xor_1_out), .out(multiplexer_1_out), .sel(nLD));
  not not_2 (not_2_out, C);
  D_Flip_Flop #(.trigger("high")) d_ff_1 (
    .clk(C), .D(multiplexer_1_out), .Q(d_ff_1_q), .reset(not_1_out));  // open: Qn, preset, en
  D_Flip_Flop #(.trigger("high")) d_ff_2 (
    .clk(not_2_out), .D(d_ff_1_q), .Q(Q), .Qn(nQ), .reset(not_1_out));  // open: preset, en

  // Notes on the sheet:
  //   C
  //   VAL
  //   LD
  //   /RES
  //   CIN
  //   CNT BIT
  //   Q
  //   nQ
  //   CO
endmodule

module RC_DELAY (
  input  IN,
  output OUT
);

  wire xor_1_out, xor_2_out, xor_3_out, xor_4_out, xor_5_out;

  xor xor_1 (xor_1_out, IN, 1'b0);
  xor xor_2 (xor_2_out, xor_1_out, 1'b0);
  xor xor_3 (xor_3_out, xor_2_out, 1'b0);
  xor xor_4 (xor_4_out, xor_3_out, 1'b0);
  xor xor_5 (xor_5_out, xor_4_out, 1'b0);
  xor xor_6 (OUT, xor_5_out, 1'b0);
endmodule

module S_latch (
  input  EN,
  input  D,
  output Q,
  output nQ
);

  D_Flip_Flop #(.trigger("high")) d_ff_1 (.clk(EN), .D(D), .Q(Q), .Qn(nQ));  // open: preset, en, reset
endmodule

module muxer (
  output VA7,
  output VA6,
  output VA5,
  output VA4,
  output VA3,
  output VA2,
  output VA1,
  output ZD7_o,
  output ZD6_o,
  output ZD5_o,
  output ZD4_o,
  output ZD3_o,
  output ZD2_o,
  output ZD1_o,
  output ZD0_o,
  output VD0_o,
  output VD1_o,
  output VD2_o,
  output VD3_o,
  output VD4_o,
  output VD5_o,
  output VD6_o,
  output VD7_o,
  output VD8_o,
  output VD9_o,
  output VD10_o,
  output VD11_o,
  output VD12_o,
  output VD13_o,
  output VD14_o,
  output VD15_o,
  output ZA1_o,
  output ZA2_o,
  output ZA3_o,
  output ZA4_o,
  output ZA5_o,
  output ZA6_o,
  output ZA7_o
);

  wire _1_out, _2_out, _3_out, _4_out, _67_out, _68_out, _69_out, _70_out, _71_out, _72_out, _73_out,
       _111_out, _125_out, _126_out, _167_out, _198_out, _288_out, _324_out, _338_out, ADR0, ADR1, ADR2,
       ADR3, DB0, DB1, DB2, DB3, DB4, DB5, DB6, DB7, g_340, multiplexer_29_out, MUX_CTRL, nCAS0, nM3, nM3_0,
       not_2_out, not_out, nVTOZ, nZTOV, VA1_i, VA2_i, VA3_i, VA4_i, VA5_i, VA6_i, VA7_i, VD0_i, VD0_o_t,
       VD1_i, VD1_o_t, VD2_i, VD2_o_t, VD3_i, VD3_o_t, VD4_i, VD4_o_t, VD5_i, VD5_o_t, VD6_i, VD6_o_t, VD7_i,
       VD7_o_t, VD8_i, VD9_i, VD10_i, VD11_i, VD12_i, VD13_i, VD14_i, VD15_i, ZA0_i, ZA1_i, ZA2_i, ZA3_i,
       ZA4_i, ZA5_i, ZA6_i, ZA7_i, ZD0_i, ZD1_i, ZD2_i, ZD3_i, ZD4_i, ZD5_i, ZD6_i, ZD7_i;
  wire [0:0] controlled_buffer_1_out;
  wire [2:0] _322_out;
  wire [3:0] multiplexer_1_out, multiplexer_5_out, multiplexer_9_out, multiplexer_13_out, multiplexer_17_out,
       multiplexer_18_out, multiplexer_23_out, multiplexer_24_out, multiplexer_25_out, multiplexer_26_out,
       multiplexer_27_out, multiplexer_28_out;

  Multiplexer #(.select(3), .disabled(0), .enable("false")) multiplexer_1 (
    .out(multiplexer_1_out[0]), .sel(_322_out));  // open: in0, in1, in2, in3, in4, in5, in6, in7
  Multiplexer #(.select(3), .disabled(0), .enable("false")) multiplexer_2 (
    .out(multiplexer_1_out[1]), .sel(_322_out));  // open: in0, in1, in2, in3, in4, in5, in6, in7
  Multiplexer #(.select(3), .disabled(0), .enable("false")) multiplexer_3 (
    .out(multiplexer_1_out[2]), .sel(_322_out));  // open: in0, in1, in2, in3, in4, in5, in6, in7
  Multiplexer #(.select(3), .disabled(0), .enable("false")) multiplexer_4 (
    .out(multiplexer_1_out[3]), .sel(_322_out));  // open: in0, in1, in2, in3, in4, in5, in6, in7
  Multiplexer #(.select(3), .disabled(0), .enable("false")) multiplexer_5 (
    .out(multiplexer_5_out[0]), .sel(_322_out));  // open: in0, in1, in2, in3, in4, in5, in6, in7
  Multiplexer #(.select(3), .disabled(0), .enable("false")) multiplexer_6 (
    .out(multiplexer_5_out[1]), .sel(_322_out));  // open: in0, in1, in2, in3, in4, in5, in6, in7
  Multiplexer #(.select(3), .disabled(0), .enable("false")) multiplexer_7 (
    .out(multiplexer_5_out[2]), .sel(_322_out));  // open: in0, in1, in2, in3, in4, in5, in6, in7
  Multiplexer #(.select(3), .disabled(0), .enable("false")) multiplexer_8 (
    .out(multiplexer_5_out[3]), .sel(_322_out));  // open: in0, in1, in2, in3, in4, in5, in6, in7
  Multiplexer #(.select(3), .disabled(0), .enable("false")) multiplexer_9 (
    .out(multiplexer_9_out[0]), .sel(_322_out));  // open: in0, in1, in2, in3, in4, in5, in6, in7
  Multiplexer #(.select(3), .disabled(0), .enable("false")) multiplexer_10 (
    .out(multiplexer_9_out[1]), .sel(_322_out));  // open: in0, in1, in2, in3, in4, in5, in6, in7
  Multiplexer #(.select(3), .disabled(0), .enable("false")) multiplexer_11 (
    .out(multiplexer_9_out[2]), .sel(_322_out));  // open: in0, in1, in2, in3, in4, in5, in6, in7
  Multiplexer #(.select(3), .disabled(0), .enable("false")) multiplexer_12 (
    .out(multiplexer_9_out[3]), .sel(_322_out));  // open: in0, in1, in2, in3, in4, in5, in6, in7
  Multiplexer #(.select(3), .disabled(0), .enable("false")) multiplexer_13 (
    .out(multiplexer_13_out[0]), .sel(_322_out));  // open: in0, in1, in2, in3, in4, in5, in6, in7
  Multiplexer #(.select(3), .disabled(0), .enable("false")) multiplexer_14 (
    .out(multiplexer_13_out[1]), .sel(_322_out));  // open: in0, in1, in2, in3, in4, in5, in6, in7
  Multiplexer #(.select(3), .disabled(0), .enable("false")) multiplexer_15 (
    .out(multiplexer_13_out[2]), .sel(_322_out));  // open: in0, in1, in2, in3, in4, in5, in6, in7
  Multiplexer #(.select(3), .disabled(0), .enable("false")) multiplexer_16 (
    .out(multiplexer_13_out[3]), .sel(_322_out));  // open: in0, in1, in2, in3, in4, in5, in6, in7
  Multiplexer #(.width(4), .disabled(0), .enable("false")) multiplexer_17 (
    .in0(multiplexer_1_out), .in1(multiplexer_5_out), .out(multiplexer_17_out), .sel(_198_out));
  and _198 (_198_out, nM3, ADR3);
  Multiplexer #(.width(4), .disabled(0), .enable("false")) multiplexer_18 (
    .in0(multiplexer_9_out), .in1(multiplexer_13_out), .out(multiplexer_18_out), .sel(_198_out));
  xnor _324 (_324_out, ADR0, nM3);
  buf _322 (_322_out[0], _324_out);
  or _2 (_2_out, _1_out, _3_out);
  buf _135 (_322_out[1], _2_out);
  buf _163 (_322_out[2], _167_out);
  and _1 (_1_out, nM3, ADR1);
  nor _3 (_3_out, nM3, _4_out);
  and _167 (_167_out, nM3, ADR2);
  Multiplexer #(.width(4), .disabled(0), .enable("false")) multiplexer_19 (
    .in0({ZD4_i, ZD5_i, ZD6_i, ZD7_i}), .in1(multiplexer_17_out), .out({VD4_o_t, VD5_o_t, VD6_o_t, VD7_o_t}),
    .sel(MUX_CTRL));
  Multiplexer #(.width(4), .disabled(0), .enable("false")) multiplexer_20 (
    .in0({ZD0_i, ZD1_i, ZD2_i, ZD3_i}), .in1(multiplexer_18_out), .out({VD0_o_t, VD1_o_t, VD2_o_t, VD3_o_t}),
    .sel(MUX_CTRL));
  not _4 (_4_out, ADR0);
  not _288 (_288_out, nM3_0);
  and _125 (_125_out, nM3_0, _126_out);
  not _126 (_126_out, ZA0_i);
  Multiplexer #(.width(4), .disabled(0), .enable("false")) multiplexer_21 (
    .in0({VD4_i, VD5_i, VD6_i, VD7_i}), .in1({ZD4_i, ZD5_i, ZD6_i, ZD7_i}), .out({DB4, DB5, DB6, DB7}),
    .sel(_288_out));
  Multiplexer #(.width(4), .disabled(0), .enable("false")) multiplexer_22 (
    .in0({VD0_i, VD1_i, VD2_i, VD3_i}), .in1({ZD0_i, ZD1_i, ZD2_i, ZD3_i}), .out({DB0, DB1, DB2, DB3}),
    .sel(_288_out));
  Multiplexer #(.width(4), .disabled(0), .enable("false")) multiplexer_23 (
    .in0({VD4_i, VD5_i, VD6_i, VD7_i}), .in1({VD12_i, VD13_i, VD14_i, VD15_i}), .out(multiplexer_23_out),
    .sel(_125_out));
  Multiplexer #(.width(4), .disabled(0), .enable("false")) multiplexer_24 (
    .in0({VD0_i, VD1_i, VD2_i, VD3_i}), .in1({VD8_i, VD9_i, VD10_i, VD11_i}), .out(multiplexer_24_out),
    .sel(_125_out));
  not _69 (_69_out, nCAS0);
  Multiplexer #(.width(4), .disabled(0), .enable("false")) multiplexer_25 (
    .in0({ZA4_i, ZA5_i, ZA6_i, 1'b0}), .in1({ZA5_i, ZA6_i, ZA7_i, 1'b0}), .out(multiplexer_25_out), .sel(nM3));
  Multiplexer #(.width(4), .disabled(0), .enable("false")) multiplexer_26 (
    .in0({ZA0_i, ZA1_i, ZA2_i, ZA3_i}), .in1({ZA1_i, ZA2_i, ZA3_i, ZA4_i}), .out(multiplexer_26_out),
    .sel(nM3));
  Multiplexer #(.width(4), .disabled(0), .enable("false")) multiplexer_27 (
    .in0(multiplexer_23_out), .in1(multiplexer_17_out), .out(multiplexer_27_out), .sel(MUX_CTRL));
  Multiplexer #(.width(4), .disabled(0), .enable("false")) multiplexer_28 (
    .in0(multiplexer_24_out), .in1(multiplexer_18_out), .out(multiplexer_28_out), .sel(MUX_CTRL));
  or _73 (_73_out, nZTOV, nCAS0);
  or _71 (_71_out, nVTOZ, _69_out);
  or _68 (_68_out, nZTOV, _69_out);
  or _70 (_70_out, nCAS0, nVTOZ);
  nand _111 (_111_out, MUX_CTRL, nM3_0);
  assign {VA5, VA6, VA7, controlled_buffer_1_out[0]} = not_out ? multiplexer_25_out : 4'bz;  // Controlled_Buffer controlled_buffer_1
  not \not  (not_out, nZTOV);
  assign {VA1, VA2, VA3, VA4} = not_out ? multiplexer_26_out : 4'bz;  // Controlled_Buffer controlled_buffer_2
  assign {ZD4_o, ZD5_o, ZD6_o, ZD7_o} = _72_out ? multiplexer_27_out : 4'bz;  // Controlled_Buffer controlled_buffer_3
  assign {ZD0_o, ZD1_o, ZD2_o, ZD3_o} = _72_out ? multiplexer_28_out : 4'bz;  // Controlled_Buffer controlled_buffer_4
  and _72 (_72_out, _73_out, _71_out);
  and _338 (_338_out, nM3_0, _67_out);
  and _67 (_67_out, _68_out, _70_out, _111_out);
  assign VD0_o = _67_out ? VD0_o_t : 1'bz;  // Controlled_Buffer controlled_buffer_5
  assign VD1_o = _67_out ? VD1_o_t : 1'bz;  // Controlled_Buffer controlled_buffer_6
  assign VD2_o = _67_out ? VD2_o_t : 1'bz;  // Controlled_Buffer controlled_buffer_7
  assign VD3_o = _67_out ? VD3_o_t : 1'bz;  // Controlled_Buffer controlled_buffer_8
  assign VD4_o = _67_out ? VD4_o_t : 1'bz;  // Controlled_Buffer controlled_buffer_9
  assign VD5_o = _67_out ? VD5_o_t : 1'bz;  // Controlled_Buffer controlled_buffer_10
  assign VD6_o = _67_out ? VD6_o_t : 1'bz;  // Controlled_Buffer controlled_buffer_11
  assign VD7_o = _67_out ? VD7_o_t : 1'bz;  // Controlled_Buffer controlled_buffer_12
  Multiplexer #(.disabled(0), .enable("false")) multiplexer_29 (
    .in0(g_340), .in1(VD0_o_t), .out(multiplexer_29_out), .sel(nM3_0));
  not not_2 (not_2_out, nVTOZ);
  assign VD8_o = _338_out ? multiplexer_29_out : 1'bz;  // Controlled_Buffer controlled_buffer_13
  assign VD9_o = _338_out ? VD1_o_t : 1'bz;  // Controlled_Buffer controlled_buffer_14
  assign VD10_o = _338_out ? VD2_o_t : 1'bz;  // Controlled_Buffer controlled_buffer_15
  assign VD11_o = _338_out ? VD3_o_t : 1'bz;  // Controlled_Buffer controlled_buffer_16
  assign VD12_o = _338_out ? VD4_o_t : 1'bz;  // Controlled_Buffer controlled_buffer_17
  assign VD13_o = _338_out ? VD5_o_t : 1'bz;  // Controlled_Buffer controlled_buffer_18
  assign VD14_o = _338_out ? VD6_o_t : 1'bz;  // Controlled_Buffer controlled_buffer_19
  assign VD15_o = _338_out ? VD7_o_t : 1'bz;  // Controlled_Buffer controlled_buffer_20
  assign ZA1_o = not_2_out ? VA1_i : 1'bz;  // Controlled_Buffer controlled_buffer_21
  assign ZA2_o = not_2_out ? VA2_i : 1'bz;  // Controlled_Buffer controlled_buffer_22
  assign ZA3_o = not_2_out ? VA3_i : 1'bz;  // Controlled_Buffer controlled_buffer_23
  assign ZA4_o = not_2_out ? VA4_i : 1'bz;  // Controlled_Buffer controlled_buffer_24
  assign ZA5_o = not_2_out ? VA5_i : 1'bz;  // Controlled_Buffer controlled_buffer_25
  assign ZA6_o = not_2_out ? VA6_i : 1'bz;  // Controlled_Buffer controlled_buffer_26
  assign ZA7_o = not_2_out ? VA7_i : 1'bz;  // Controlled_Buffer controlled_buffer_27

  // Notes on the sheet:
  //   303
  //   298
  //   257
  //   299
  //   309
  //   271
  //   276
  //   317
  //   90
  //   91
  //   147
  //   89
  //   94
  //   204
  //   313
  //   387
  //   253
  //   201
  //   323
  //   144
  //   162
  //   289
  //   77
  //   292
  //   76
  //   290
  //   74
  //   43
  //   127
  //   293
  //   199
  //   339
  //   NC
endmodule
