// Logisim project ymcells.circ as structural Verilog
module cell32__NOT4 (
  input  in_1,
  input  in_2,
  output out_3,
  output out_4
);

  wire not_1_out, not_2_out, not_3_out, transistor_1_out, transistor_2_out, transistor_5_out;

  Transistor transistor_1 (.in(1'b1), .out(transistor_1_out), .gate(transistor_2_out));
  Transistor transistor_2 (.in(1'b1), .out(transistor_2_out), .gate(in_1));
  Transistor #(.\type ("n")) transistor_3 (.in(1'b0), .out(transistor_1_out), .gate(transistor_2_out));
  Transistor #(.\type ("n")) transistor_4 (.in(1'b0), .out(transistor_2_out), .gate(in_1));
  Transistor transistor_5 (.in(1'b1), .out(transistor_5_out), .gate(transistor_1_out));
  Transistor #(.\type ("n")) transistor_6 (.in(1'b0), .out(transistor_5_out), .gate(transistor_1_out));
  Transistor transistor_7 (.in(1'b1), .out(out_3), .gate(transistor_5_out));
  Transistor #(.\type ("n")) transistor_8 (.in(1'b0), .out(out_3), .gate(transistor_5_out));
  not not_1 (not_1_out, in_2);
  not not_2 (not_2_out, not_1_out);
  not not_3 (not_3_out, not_2_out);
  not not_4 (out_4, not_3_out);

  // Notes on the sheet:
  //   ~
  //   NOT4
endmodule

module cell33 (
  input  a,
  input  a_2,
  output b,
  output b_2,
  output c,
  output c_2
);

  wire not_1_out, transistor_3_out;

  Transistor transistor_1 (.in(1'b1), .out(b), .gate(a));
  Transistor #(.\type ("n")) transistor_2 (.in(1'b0), .out(b), .gate(a));
  Transistor transistor_3 (.in(1'b1), .out(transistor_3_out), .gate(a));
  Transistor #(.\type ("n")) transistor_4 (.in(1'b0), .out(transistor_3_out), .gate(a));
  Transistor transistor_5 (.in(1'b1), .out(b), .gate(a));
  Transistor #(.\type ("n")) transistor_6 (.in(1'b0), .out(b), .gate(a));
  Transistor transistor_7 (.in(1'b1), .out(c_2), .gate(transistor_3_out));
  Transistor transistor_8 (.in(1'b1), .out(c_2), .gate(transistor_3_out));
  Transistor #(.\type ("n")) transistor_9 (.in(1'b0), .out(c_2), .gate(transistor_3_out));
  Transistor #(.\type ("n")) transistor_10 (.in(1'b0), .out(c_2), .gate(transistor_3_out));
  not not_1 (not_1_out, a_2);
  not not_2 (b_2, a_2);
  not not_3 (c, not_1_out);

  // Notes on the sheet:
  //   ~
endmodule

module cell35__OR5 (
  input  b,
  input  c,
  input  b_2,
  input  c_2,
  input  d,
  input  e,
  input  d_2,
  input  f,
  input  e_2,
  input  f_2,
  output a,
  output a_2
);

  wire nor_1_out, nor_2_out, transistor_1_out, transistor_2_out, transistor_5_out, transistor_6_out,
       transistor_7_out, transistor_14_out;

  Transistor transistor_1 (.in(1'b1), .out(transistor_1_out), .gate(b));
  Transistor transistor_2 (.in(transistor_1_out), .out(transistor_2_out), .gate(c));
  Transistor #(.\type ("n")) transistor_3 (.in(1'b0), .out(transistor_2_out), .gate(c));
  Transistor #(.\type ("n")) transistor_4 (.in(1'b0), .out(transistor_2_out), .gate(b));
  Transistor transistor_5 (.in(1'b1), .out(transistor_5_out), .gate(d_2));
  Transistor transistor_6 (.in(transistor_5_out), .out(transistor_6_out), .gate(e_2));
  Transistor transistor_7 (.in(transistor_6_out), .out(transistor_7_out), .gate(f_2));
  Transistor #(.\type ("n")) transistor_8 (.in(1'b0), .out(transistor_7_out), .gate(d_2));
  Transistor #(.\type ("n")) transistor_9 (.in(1'b0), .out(transistor_7_out), .gate(e_2));
  Transistor transistor_10 (.in(1'b1), .out(a), .gate(transistor_2_out));
  Transistor #(.\type ("n")) transistor_11 (.in(1'b0), .out(transistor_7_out), .gate(f_2));
  Transistor transistor_12 (.in(1'b1), .out(a), .gate(transistor_7_out));
  Transistor #(.\type ("n")) transistor_13 (.in(transistor_14_out), .out(a), .gate(transistor_2_out));
  Transistor #(.\type ("n")) transistor_14 (.in(1'b0), .out(transistor_14_out), .gate(transistor_7_out));
  nor nor_1 (nor_1_out, b_2, c_2);
  nor nor_2 (nor_2_out, d, e, f);
  nand nand_1 (a_2, nor_1_out, nor_2_out);

  // Notes on the sheet:
  //   ~
  //   OR5
endmodule

module cell36__4NOR (
  input  a,
  input  b,
  input  c,
  input  a_2,
  input  d,
  input  b_2,
  input  c_2,
  input  d_2,
  output e,
  output e_2
);

  wire transistor_1_out, transistor_2_out, transistor_3_out;

  Transistor transistor_1 (.in(1'b1), .out(transistor_1_out), .gate(a));
  Transistor transistor_2 (.in(transistor_1_out), .out(transistor_2_out), .gate(b));
  Transistor transistor_3 (.in(transistor_2_out), .out(transistor_3_out), .gate(c));
  Transistor transistor_4 (.in(transistor_3_out), .out(e), .gate(d));
  Transistor #(.\type ("n")) transistor_5 (.in(1'b0), .out(e), .gate(a));
  Transistor #(.\type ("n")) transistor_6 (.in(1'b0), .out(e), .gate(b));
  Transistor #(.\type ("n")) transistor_7 (.in(1'b0), .out(e), .gate(d));
  Transistor #(.\type ("n")) transistor_8 (.in(1'b0), .out(e), .gate(c));
  nor nor_1 (e_2, a_2, b_2, c_2, d_2);

  // Notes on the sheet:
  //   ~
  //   4NOR
endmodule

module cell37__4NAND (
  input  a,
  input  b,
  input  c,
  input  a_2,
  input  d,
  input  b_2,
  input  c_2,
  input  d_2,
  output e,
  output e_2
);

  wire transistor_4_out, transistor_5_out, transistor_6_out;

  Transistor transistor_1 (.in(1'b1), .out(e), .gate(c_2));
  Transistor transistor_2 (.in(1'b1), .out(e), .gate(d_2));
  Transistor #(.\type ("n")) transistor_3 (.in(transistor_4_out), .out(e), .gate(a_2));
  Transistor #(.\type ("n")) transistor_4 (.in(transistor_5_out), .out(transistor_4_out), .gate(b_2));
  Transistor #(.\type ("n")) transistor_5 (.in(transistor_6_out), .out(transistor_5_out), .gate(c_2));
  Transistor #(.\type ("n")) transistor_6 (.in(1'b0), .out(transistor_6_out), .gate(d_2));
  Transistor transistor_7 (.in(1'b1), .out(e), .gate(a_2));
  Transistor transistor_8 (.in(1'b1), .out(e), .gate(b_2));
  nand nand_1 (e_2, a, b, c, d);

  // Notes on the sheet:
  //   ~
  //   4NAND
endmodule

module cell38 (
  input  a,
  input  b,
  input  c,
  input  a_2,
  input  b_2,
  input  c_2,
  input  d,
  input  d_2,
  input  e,
  input  e_2,
  input  f,
  input  f_2,
  output g,
  output g_2
);

  wire nor_1_out, nor_2_out, transistor_1_out, transistor_2_out, transistor_3_out, transistor_6_out,
       transistor_7_out, transistor_8_out, transistor_16_out;

  Transistor transistor_1 (.in(1'b1), .out(transistor_1_out), .gate(a));
  Transistor transistor_2 (.in(transistor_1_out), .out(transistor_2_out), .gate(b));
  Transistor transistor_3 (.in(transistor_2_out), .out(transistor_3_out), .gate(c));
  Transistor #(.\type ("n")) transistor_4 (.in(1'b0), .out(transistor_3_out), .gate(b));
  Transistor #(.\type ("n")) transistor_5 (.in(1'b0), .out(transistor_3_out), .gate(a));
  Transistor transistor_6 (.in(1'b1), .out(transistor_6_out), .gate(d_2));
  Transistor transistor_7 (.in(transistor_6_out), .out(transistor_7_out), .gate(e_2));
  Transistor transistor_8 (.in(transistor_7_out), .out(transistor_8_out), .gate(f_2));
  Transistor #(.\type ("n")) transistor_9 (.in(1'b0), .out(transistor_8_out), .gate(e_2));
  Transistor #(.\type ("n")) transistor_10 (.in(1'b0), .out(transistor_8_out), .gate(d_2));
  Transistor #(.\type ("n")) transistor_11 (.in(1'b0), .out(transistor_3_out), .gate(c));
  Transistor transistor_12 (.in(1'b1), .out(g), .gate(transistor_3_out));
  Transistor #(.\type ("n")) transistor_13 (.in(1'b0), .out(transistor_8_out), .gate(f_2));
  Transistor transistor_14 (.in(1'b1), .out(g), .gate(transistor_8_out));
  Transistor #(.\type ("n")) transistor_15 (.in(transistor_16_out), .out(g), .gate(transistor_3_out));
  Transistor #(.\type ("n")) transistor_16 (.in(1'b0), .out(transistor_16_out), .gate(transistor_8_out));
  nor nor_1 (nor_1_out, a_2, b_2, c_2);
  nor nor_2 (nor_2_out, d, e, f);
  nand nand_1 (g_2, nor_1_out, nor_2_out);

  // Notes on the sheet:
  //   ~
endmodule

module cell39 (
  input  a,
  input  b,
  input  c,
  input  a_2,
  input  b_2,
  input  c_2,
  input  d,
  input  d_2,
  input  e,
  input  e_2,
  input  f,
  input  f_2,
  output g,
  output g_2
);

  wire nor_1_out, nor_2_out, transistor_1_out, transistor_2_out, transistor_3_out, transistor_6_out,
       transistor_7_out, transistor_8_out, transistor_12_out, transistor_16_out;

  Transistor transistor_1 (.in(1'b1), .out(transistor_1_out), .gate(a));
  Transistor transistor_2 (.in(transistor_1_out), .out(transistor_2_out), .gate(b));
  Transistor transistor_3 (.in(transistor_2_out), .out(transistor_3_out), .gate(c));
  Transistor #(.\type ("n")) transistor_4 (.in(1'b0), .out(transistor_3_out), .gate(a));
  Transistor #(.\type ("n")) transistor_5 (.in(1'b0), .out(transistor_3_out), .gate(b));
  Transistor transistor_6 (.in(1'b1), .out(transistor_6_out), .gate(d_2));
  Transistor transistor_7 (.in(transistor_6_out), .out(transistor_7_out), .gate(e_2));
  Transistor transistor_8 (.in(transistor_7_out), .out(transistor_8_out), .gate(f_2));
  Transistor #(.\type ("n")) transistor_9 (.in(1'b0), .out(transistor_8_out), .gate(d_2));
  Transistor #(.\type ("n")) transistor_10 (.in(1'b0), .out(transistor_8_out), .gate(e_2));
  Transistor #(.\type ("n")) transistor_11 (.in(1'b0), .out(transistor_3_out), .gate(c));
  Transistor transistor_12 (.in(1'b1), .out(transistor_12_out), .gate(transistor_3_out));
  Transistor #(.\type ("n")) transistor_13 (.in(1'b0), .out(transistor_8_out), .gate(f_2));
  Transistor transistor_14 (.in(1'b1), .out(transistor_12_out), .gate(transistor_8_out));
  Transistor #(.\type ("n")) transistor_15 (.in(transistor_16_out), .out(transistor_12_out), .gate(transistor_3_out));
  Transistor #(.\type ("n")) transistor_16 (.in(1'b0), .out(transistor_16_out), .gate(transistor_8_out));
  Transistor transistor_17 (.in(1'b1), .out(g), .gate(transistor_12_out));
  Transistor #(.\type ("n")) transistor_18 (.in(1'b0), .out(g), .gate(transistor_12_out));
  nor nor_1 (nor_1_out, a_2, b_2, c_2);
  nor nor_2 (nor_2_out, d, e, f);
  and and_1 (g_2, nor_1_out, nor_2_out);

  // Notes on the sheet:
  //   ~
endmodule

module cell40__5AND (
  input  b,
  input  c,
  input  b_2,
  input  c_2,
  input  d,
  input  e,
  input  f,
  input  d_2,
  input  e_2,
  input  f_2,
  output a,
  output a_2
);

  wire nand_1_out, nand_2_out, transistor_1_out, transistor_4_out, transistor_5_out, transistor_8_out,
       transistor_9_out, transistor_11_out;

  Transistor transistor_1 (.in(1'b1), .out(transistor_1_out), .gate(c));
  Transistor transistor_2 (.in(1'b1), .out(transistor_1_out), .gate(b));
  Transistor #(.\type ("n")) transistor_3 (.in(transistor_4_out), .out(transistor_1_out), .gate(b));
  Transistor #(.\type ("n")) transistor_4 (.in(1'b0), .out(transistor_4_out), .gate(c));
  Transistor transistor_5 (.in(1'b1), .out(transistor_5_out), .gate(e_2));
  Transistor transistor_6 (.in(1'b1), .out(transistor_5_out), .gate(f_2));
  Transistor #(.\type ("n")) transistor_7 (.in(transistor_8_out), .out(transistor_5_out), .gate(d_2));
  Transistor #(.\type ("n")) transistor_8 (.in(transistor_9_out), .out(transistor_8_out), .gate(e_2));
  Transistor #(.\type ("n")) transistor_9 (.in(1'b0), .out(transistor_9_out), .gate(f_2));
  Transistor transistor_10 (.in(1'b1), .out(transistor_5_out), .gate(d_2));
  Transistor transistor_11 (.in(1'b1), .out(transistor_11_out), .gate(transistor_5_out));
  Transistor transistor_12 (.in(transistor_11_out), .out(a), .gate(transistor_1_out));
  Transistor #(.\type ("n")) transistor_13 (.in(1'b0), .out(a), .gate(transistor_5_out));
  Transistor #(.\type ("n")) transistor_14 (.in(1'b0), .out(a), .gate(transistor_1_out));
  nand nand_1 (nand_1_out, b_2, c_2);
  nand nand_2 (nand_2_out, d, e, f);
  nor nor_1 (a_2, nand_1_out, nand_2_out);

  // Notes on the sheet:
  //   ~
  //   5AND
endmodule

module cell41__4OR (
  input  a,
  input  b,
  input  c,
  input  a_2,
  input  d,
  input  b_2,
  input  c_2,
  input  d_2,
  output e,
  output e_2
);

  wire transistor_1_out, transistor_2_out, transistor_3_out, transistor_4_out;

  Transistor transistor_1 (.in(1'b1), .out(transistor_1_out), .gate(a));
  Transistor transistor_2 (.in(transistor_1_out), .out(transistor_2_out), .gate(b));
  Transistor transistor_3 (.in(transistor_2_out), .out(transistor_3_out), .gate(c));
  Transistor transistor_4 (.in(transistor_3_out), .out(transistor_4_out), .gate(d));
  Transistor #(.\type ("n")) transistor_5 (.in(1'b0), .out(transistor_4_out), .gate(a));
  Transistor #(.\type ("n")) transistor_6 (.in(1'b0), .out(transistor_4_out), .gate(b));
  Transistor #(.\type ("n")) transistor_7 (.in(1'b0), .out(transistor_4_out), .gate(c));
  Transistor transistor_8 (.in(1'b1), .out(e), .gate(transistor_4_out));
  Transistor #(.\type ("n")) transistor_9 (.in(1'b0), .out(transistor_4_out), .gate(d));
  Transistor #(.\type ("n")) transistor_10 (.in(1'b0), .out(e), .gate(transistor_4_out));
  or or_1 (e_2, a_2, b_2, c_2, d_2);

  // Notes on the sheet:
  //   ~
  //   4OR
endmodule

module cell42__4AND (
  input  a,
  input  b,
  input  c,
  input  a_2,
  input  d,
  input  b_2,
  input  c_2,
  input  d_2,
  output e,
  output e_2
);

  wire transistor_1_out, transistor_4_out, transistor_5_out, transistor_6_out;

  Transistor transistor_1 (.in(1'b1), .out(transistor_1_out), .gate(d_2));
  Transistor transistor_2 (.in(1'b1), .out(transistor_1_out), .gate(c_2));
  Transistor #(.\type ("n")) transistor_3 (.in(transistor_4_out), .out(transistor_1_out), .gate(a_2));
  Transistor #(.\type ("n")) transistor_4 (.in(transistor_5_out), .out(transistor_4_out), .gate(b_2));
  Transistor #(.\type ("n")) transistor_5 (.in(transistor_6_out), .out(transistor_5_out), .gate(c_2));
  Transistor #(.\type ("n")) transistor_6 (.in(1'b0), .out(transistor_6_out), .gate(d_2));
  Transistor transistor_7 (.in(1'b1), .out(transistor_1_out), .gate(b_2));
  Transistor transistor_8 (.in(1'b1), .out(transistor_1_out), .gate(a_2));
  Transistor transistor_9 (.in(1'b1), .out(e), .gate(transistor_1_out));
  Transistor #(.\type ("n")) transistor_10 (.in(1'b0), .out(e), .gate(transistor_1_out));
  and and_1 (e_2, a, b, c, d);

  // Notes on the sheet:
  //   ~
  //   4AND
endmodule

module cell43__AOI22 (
  input  c,
  input  b,
  input  c_2,
  input  d,
  input  b_2,
  input  d_2,
  input  e,
  input  e_2,
  output a,
  output a_2
);

  wire and_1_out, and_2_out, transistor_1_out, transistor_4_out, transistor_8_out;

  Transistor transistor_1 (.in(1'b1), .out(transistor_1_out), .gate(b));
  Transistor transistor_2 (.in(transistor_1_out), .out(a), .gate(d));
  Transistor #(.\type ("n")) transistor_3 (.in(transistor_4_out), .out(a), .gate(c));
  Transistor #(.\type ("n")) transistor_4 (.in(1'b0), .out(transistor_4_out), .gate(b));
  Transistor transistor_5 (.in(1'b1), .out(transistor_1_out), .gate(c));
  Transistor transistor_6 (.in(transistor_1_out), .out(a), .gate(e_2));
  Transistor #(.\type ("n")) transistor_7 (.in(transistor_8_out), .out(a), .gate(d));
  Transistor #(.\type ("n")) transistor_8 (.in(1'b0), .out(transistor_8_out), .gate(e_2));
  and and_1 (and_1_out, c_2, b_2);
  and and_2 (and_2_out, d_2, e);
  nor nor_1 (a_2, and_1_out, and_2_out);

  // Notes on the sheet:
  //   ~
  //   AOI22
endmodule

module cell44__AOI2222 (
  input  b,
  input  b_2,
  input  c,
  input  c_2,
  input  d,
  input  d_2,
  input  e,
  input  e_2,
  input  f,
  input  f_2,
  input  g,
  input  g_2,
  input  h,
  input  h_2,
  input  i,
  input  i_2,
  output a,
  output a_2
);

  wire and_1_out, and_2_out, and_3_out, and_4_out, transistor_2_out, transistor_3_out, transistor_5_out,
       transistor_7_out, transistor_13_out, transistor_14_out, transistor_16_out;

  Transistor #(.\type ("n")) transistor_1 (.in(transistor_2_out), .out(a), .gate(c));
  Transistor #(.\type ("n")) transistor_2 (.in(1'b0), .out(transistor_2_out), .gate(b));
  Transistor transistor_3 (.in(1'b1), .out(transistor_3_out), .gate(h));
  Transistor transistor_4 (.in(1'b1), .out(transistor_3_out), .gate(i));
  Transistor transistor_5 (.in(transistor_3_out), .out(transistor_5_out), .gate(f));
  Transistor transistor_6 (.in(transistor_3_out), .out(transistor_5_out), .gate(g));
  Transistor transistor_7 (.in(transistor_5_out), .out(transistor_7_out), .gate(d));
  Transistor transistor_8 (.in(transistor_5_out), .out(transistor_7_out), .gate(e));
  Transistor transistor_9 (.in(transistor_7_out), .out(a), .gate(c));
  Transistor transistor_10 (.in(transistor_7_out), .out(a), .gate(b));
  Transistor #(.\type ("n")) transistor_11 (.in(transistor_14_out), .out(a), .gate(g));
  Transistor #(.\type ("n")) transistor_12 (.in(transistor_13_out), .out(a), .gate(d));
  Transistor #(.\type ("n")) transistor_13 (.in(1'b0), .out(transistor_13_out), .gate(e));
  Transistor #(.\type ("n")) transistor_14 (.in(1'b0), .out(transistor_14_out), .gate(f));
  Transistor #(.\type ("n")) transistor_15 (.in(transistor_16_out), .out(a), .gate(h));
  Transistor #(.\type ("n")) transistor_16 (.in(1'b0), .out(transistor_16_out), .gate(i));
  and and_1 (and_1_out, b_2, c_2);
  and and_2 (and_2_out, d_2, e_2);
  and and_3 (and_3_out, f_2, g_2);
  and and_4 (and_4_out, h_2, i_2);
  nor nor_1 (a_2, and_1_out, and_2_out, and_3_out, and_4_out);

  // Notes on the sheet:
  //   ~
  //   AOI2222
endmodule

module cell45 (
  input  na,
  input  b,
  input  a,
  output c
);

  wire transistor_1_out, transistor_3_out, transistor_5_out;

  Transistor transistor_1 (.in(1'b1), .out(transistor_1_out), .gate(b));
  Transistor #(.\type ("n")) transistor_2 (.in(1'b0), .out(transistor_1_out), .gate(b));
  Transistor transistor_3 (.in(b), .out(transistor_3_out), .gate(na));
  Transistor #(.\type ("n")) transistor_4 (.in(b), .out(transistor_3_out), .gate(a));
  Transistor transistor_5 (.in(1'b1), .out(transistor_5_out), .gate(transistor_3_out));
  Transistor transistor_6 (.in(transistor_5_out), .out(c), .gate(transistor_1_out));
  Transistor #(.\type ("n")) transistor_7 (.in(1'b0), .out(c), .gate(transistor_1_out));
  Transistor #(.\type ("n")) transistor_8 (.in(1'b0), .out(c), .gate(transistor_3_out));
endmodule

module cell46 (
  input  a,
  input  b,
  input  a_2,
  input  c,
  input  b_2,
  input  d,
  input  c_2,
  input  e,
  input  f,
  input  g,
  input  d_2,
  input  e_2,
  input  f_2,
  input  g_2,
  output h,
  output h_2
);

  wire nand_1_out, nand_2_out, transistor_1_out, transistor_3_out, transistor_4_out, transistor_5_out,
       transistor_7_out, transistor_8_out, transistor_9_out, transistor_15_out;

  Transistor transistor_1 (.in(1'b1), .out(transistor_1_out), .gate(c_2));
  Transistor #(.\type ("n")) transistor_2 (.in(transistor_3_out), .out(transistor_1_out), .gate(a_2));
  Transistor #(.\type ("n")) transistor_3 (.in(transistor_4_out), .out(transistor_3_out), .gate(b_2));
  Transistor #(.\type ("n")) transistor_4 (.in(1'b0), .out(transistor_4_out), .gate(c_2));
  Transistor transistor_5 (.in(1'b1), .out(transistor_5_out), .gate(g_2));
  Transistor #(.\type ("n")) transistor_6 (.in(transistor_7_out), .out(transistor_5_out), .gate(d_2));
  Transistor #(.\type ("n")) transistor_7 (.in(transistor_8_out), .out(transistor_7_out), .gate(e_2));
  Transistor #(.\type ("n")) transistor_8 (.in(transistor_9_out), .out(transistor_8_out), .gate(f_2));
  Transistor #(.\type ("n")) transistor_9 (.in(1'b0), .out(transistor_9_out), .gate(g_2));
  Transistor transistor_10 (.in(1'b1), .out(transistor_1_out), .gate(b_2));
  Transistor transistor_11 (.in(1'b1), .out(transistor_1_out), .gate(a_2));
  Transistor transistor_12 (.in(1'b1), .out(transistor_5_out), .gate(f_2));
  Transistor transistor_13 (.in(1'b1), .out(transistor_5_out), .gate(e_2));
  Transistor transistor_14 (.in(1'b1), .out(transistor_5_out), .gate(d_2));
  Transistor transistor_15 (.in(1'b1), .out(transistor_15_out), .gate(transistor_5_out));
  Transistor transistor_16 (.in(transistor_15_out), .out(h), .gate(transistor_1_out));
  Transistor #(.\type ("n")) transistor_17 (.in(1'b0), .out(h), .gate(transistor_1_out));
  Transistor #(.\type ("n")) transistor_18 (.in(1'b0), .out(h), .gate(transistor_5_out));
  nand nand_1 (nand_1_out, a, b, c);
  nand nand_2 (nand_2_out, d, e, f, g);
  nor nor_1 (h_2, nand_1_out, nand_2_out);

  // Notes on the sheet:
  //   ~
endmodule

module cell47__6AND (
  input  a,
  input  a_2,
  input  b,
  input  b_2,
  input  c,
  input  c_2,
  input  d,
  input  e,
  input  f,
  input  d_2,
  input  e_2,
  input  f_2,
  output g,
  output g_2
);

  wire nand_1_out, nand_2_out, transistor_1_out, transistor_4_out, transistor_5_out, transistor_6_out,
       transistor_9_out, transistor_10_out, transistor_13_out;

  Transistor transistor_1 (.in(1'b1), .out(transistor_1_out), .gate(b_2));
  Transistor transistor_2 (.in(1'b1), .out(transistor_1_out), .gate(c_2));
  Transistor #(.\type ("n")) transistor_3 (.in(transistor_4_out), .out(transistor_1_out), .gate(a_2));
  Transistor #(.\type ("n")) transistor_4 (.in(transistor_5_out), .out(transistor_4_out), .gate(b_2));
  Transistor #(.\type ("n")) transistor_5 (.in(1'b0), .out(transistor_5_out), .gate(c_2));
  Transistor transistor_6 (.in(1'b1), .out(transistor_6_out), .gate(e_2));
  Transistor transistor_7 (.in(1'b1), .out(transistor_6_out), .gate(f_2));
  Transistor #(.\type ("n")) transistor_8 (.in(transistor_9_out), .out(transistor_6_out), .gate(d_2));
  Transistor #(.\type ("n")) transistor_9 (.in(transistor_10_out), .out(transistor_9_out), .gate(e_2));
  Transistor #(.\type ("n")) transistor_10 (.in(1'b0), .out(transistor_10_out), .gate(f_2));
  Transistor transistor_11 (.in(1'b1), .out(transistor_1_out), .gate(a_2));
  Transistor transistor_12 (.in(1'b1), .out(transistor_6_out), .gate(d_2));
  Transistor transistor_13 (.in(1'b1), .out(transistor_13_out), .gate(transistor_6_out));
  Transistor transistor_14 (.in(transistor_13_out), .out(g), .gate(transistor_1_out));
  Transistor #(.\type ("n")) transistor_15 (.in(1'b0), .out(g), .gate(transistor_1_out));
  Transistor #(.\type ("n")) transistor_16 (.in(1'b0), .out(g), .gate(transistor_6_out));
  nand nand_1 (nand_1_out, a, c);
  nand nand_2 (nand_2_out, d, f);
  nor nor_1 (g_2, nand_1_out, nand_2_out);

  // Notes on the sheet:
  //   ~
  //   6AND
endmodule

module cell48__5NOR (
  input  a,
  input  b,
  input  c,
  input  a_2,
  input  b_2,
  input  c_2,
  input  d,
  input  d_2,
  input  e,
  input  e_2,
  output f,
  output f_2
);

  wire nor_1_out, nor_2_out, transistor_1_out, transistor_2_out, transistor_3_out, transistor_6_out,
       transistor_7_out, transistor_11_out, transistor_13_out;

  Transistor transistor_1 (.in(1'b1), .out(transistor_1_out), .gate(a));
  Transistor transistor_2 (.in(transistor_1_out), .out(transistor_2_out), .gate(b));
  Transistor transistor_3 (.in(transistor_2_out), .out(transistor_3_out), .gate(c));
  Transistor #(.\type ("n")) transistor_4 (.in(1'b0), .out(transistor_3_out), .gate(a));
  Transistor #(.\type ("n")) transistor_5 (.in(1'b0), .out(transistor_3_out), .gate(b));
  Transistor transistor_6 (.in(1'b1), .out(transistor_6_out), .gate(d_2));
  Transistor transistor_7 (.in(transistor_6_out), .out(transistor_7_out), .gate(e));
  Transistor #(.\type ("n")) transistor_8 (.in(1'b0), .out(transistor_7_out), .gate(e));
  Transistor #(.\type ("n")) transistor_9 (.in(1'b0), .out(transistor_7_out), .gate(d_2));
  Transistor #(.\type ("n")) transistor_10 (.in(1'b0), .out(transistor_3_out), .gate(c));
  Transistor transistor_11 (.in(1'b1), .out(transistor_11_out), .gate(transistor_3_out));
  Transistor #(.\type ("n")) transistor_12 (.in(transistor_13_out), .out(transistor_11_out), .gate(transistor_7_out));
  Transistor #(.\type ("n")) transistor_13 (.in(1'b0), .out(transistor_13_out), .gate(transistor_3_out));
  Transistor transistor_14 (.in(1'b1), .out(transistor_11_out), .gate(transistor_7_out));
  Transistor transistor_15 (.in(1'b1), .out(f), .gate(transistor_11_out));
  Transistor #(.\type ("n")) transistor_16 (.in(1'b0), .out(f), .gate(transistor_11_out));
  nor nor_1 (nor_1_out, a_2, b_2, c_2);
  nor nor_2 (nor_2_out, d, e_2);
  and and_1 (f_2, nor_1_out, nor_2_out);

  // Notes on the sheet:
  //   ~
  //   5NOR
endmodule

module cell49 (
  input  b,
  input  b_2,
  input  c,
  input  c_2,
  output a,
  output a_2
);

  wire transistor_1_out, transistor_3_out, transistor_4_out, transistor_7_out, transistor_8_out;

  Transistor transistor_1 (.in(1'b1), .out(transistor_1_out), .gate(c_2));
  Transistor #(.\type ("n")) transistor_2 (.in(transistor_3_out), .out(transistor_1_out), .gate(c_2));
  Transistor #(.\type ("n")) transistor_3 (.in(1'b0), .out(transistor_3_out), .gate(b));
  Transistor transistor_4 (.in(1'b1), .out(transistor_4_out), .gate(c_2));
  Transistor #(.\type ("n")) transistor_5 (.in(1'b0), .out(transistor_4_out), .gate(c_2));
  Transistor transistor_6 (.in(1'b1), .out(transistor_1_out), .gate(b));
  Transistor transistor_7 (.in(1'b1), .out(transistor_7_out), .gate(b));
  Transistor transistor_8 (.in(transistor_7_out), .out(transistor_8_out), .gate(transistor_4_out));
  Transistor #(.\type ("n")) transistor_9 (.in(1'b0), .out(transistor_8_out), .gate(b));
  Transistor #(.\type ("n")) transistor_10 (.in(1'b0), .out(transistor_8_out), .gate(transistor_4_out));
  Transistor transistor_11 (.in(1'b1), .out(a_2), .gate(transistor_1_out));
  Transistor transistor_12 (.in(1'b1), .out(a_2), .gate(transistor_1_out));
  Transistor #(.\type ("n")) transistor_13 (.in(1'b0), .out(a_2), .gate(transistor_8_out));
  Transistor #(.\type ("n")) transistor_14 (.in(1'b0), .out(a_2), .gate(transistor_8_out));
  assign a = c ? b_2 : 1'bz;  // Controlled_Buffer controlled_buffer_1

  // Notes on the sheet:
  //   ~
endmodule

module cell50__N_tran (
  input  in_1
);

  wire transistor_1_out, undriven;

  Transistor #(.\type ("n")) transistor_1 (.in(undriven), .out(transistor_1_out), .gate(in_1));
  // also tied to GND on the sheet: transistor_1_out
endmodule

module cell51 (
  input  b,
  input  c,
  input  d,
  input  e,
  input  f,
  output a
);

  wire transistor_1_out, transistor_3_out, transistor_5_out, transistor_6_out, transistor_8_out,
       transistor_10_out;

  Transistor transistor_1 (.in(1'b1), .out(transistor_1_out), .gate(b));
  Transistor transistor_2 (.in(1'b1), .out(transistor_1_out), .gate(c));
  Transistor transistor_3 (.in(transistor_1_out), .out(transistor_3_out), .gate(e));
  Transistor #(.\type ("n")) transistor_4 (.in(transistor_5_out), .out(transistor_3_out), .gate(d));
  Transistor #(.\type ("n")) transistor_5 (.in(transistor_6_out), .out(transistor_5_out), .gate(c));
  Transistor #(.\type ("n")) transistor_6 (.in(1'b0), .out(transistor_6_out), .gate(b));
  Transistor transistor_7 (.in(1'b1), .out(transistor_1_out), .gate(d));
  Transistor transistor_8 (.in(transistor_1_out), .out(transistor_8_out), .gate(f));
  Transistor #(.\type ("n")) transistor_9 (.in(transistor_10_out), .out(transistor_8_out), .gate(e));
  Transistor #(.\type ("n")) transistor_10 (.in(1'b0), .out(transistor_10_out), .gate(f));
  Transistor transistor_11 (.in(1'b1), .out(a), .gate(transistor_3_out));
  Transistor #(.\type ("n")) transistor_12 (.in(1'b0), .out(a), .gate(transistor_3_out));
endmodule

module cell72 (
  input  clk,
  input  d_in,
  input  r,
  output d_out
);

  wire transistor_1_out, transistor_3_out, transistor_5_out, transistor_7_out, transistor_9_out,
       transistor_10_out, transistor_11_out, transistor_15_out, transistor_16_out, transistor_17_out,
       transistor_19_out, transistor_21_out, transistor_23_out, transistor_24_out, transistor_26_out,
       transistor_27_out, transistor_30_out, transistor_31_out, transistor_33_out;

  Transistor transistor_1 (.in(1'b1), .out(transistor_1_out), .gate(clk));
  Transistor #(.\type ("n")) transistor_2 (.in(1'b0), .out(transistor_1_out), .gate(clk));
  Transistor transistor_3 (.in(1'b1), .out(transistor_3_out), .gate(clk));
  Transistor #(.\type ("n")) transistor_4 (.in(1'b0), .out(transistor_3_out), .gate(clk));
  Transistor transistor_5 (.in(1'b1), .out(transistor_5_out), .gate(transistor_3_out));
  Transistor #(.\type ("n")) transistor_6 (.in(1'b0), .out(transistor_5_out), .gate(transistor_3_out));
  Transistor transistor_7 (.in(1'b1), .out(transistor_7_out), .gate(d_in));
  Transistor #(.\type ("n")) transistor_8 (.in(1'b0), .out(transistor_7_out), .gate(d_in));
  Transistor transistor_9 (.in(1'b1), .out(transistor_9_out), .gate(transistor_7_out));
  Transistor transistor_10 (.in(1'b1), .out(transistor_10_out), .gate(transistor_19_out));
  Transistor transistor_11 (.in(transistor_10_out), .out(transistor_11_out), .gate(transistor_1_out));
  Transistor transistor_12 (.in(transistor_9_out), .out(transistor_11_out), .gate(transistor_5_out));
  Transistor #(.\type ("n")) transistor_13 (.in(transistor_15_out), .out(transistor_11_out), .gate(transistor_5_out));
  Transistor #(.\type ("n")) transistor_14 (.in(transistor_16_out), .out(transistor_11_out), .gate(transistor_7_out));
  Transistor #(.\type ("n")) transistor_15 (.in(1'b0), .out(transistor_15_out), .gate(transistor_19_out));
  Transistor #(.\type ("n")) transistor_16 (.in(1'b0), .out(transistor_16_out), .gate(transistor_1_out));
  Transistor transistor_17 (.in(1'b1), .out(transistor_17_out), .gate(r));
  Transistor #(.\type ("n")) transistor_18 (.in(1'b0), .out(transistor_17_out), .gate(r));
  Transistor transistor_19 (.in(1'b1), .out(transistor_19_out), .gate(transistor_11_out));
  Transistor #(.\type ("n")) transistor_20 (.in(transistor_21_out), .out(transistor_19_out), .gate(transistor_11_out));
  Transistor #(.\type ("n")) transistor_21 (.in(1'b0), .out(transistor_21_out), .gate(transistor_17_out));
  Transistor transistor_22 (.in(1'b1), .out(transistor_19_out), .gate(transistor_17_out));
  Transistor transistor_23 (.in(1'b1), .out(transistor_23_out), .gate(transistor_19_out));
  Transistor transistor_24 (.in(transistor_23_out), .out(transistor_24_out), .gate(transistor_1_out));
  Transistor #(.\type ("n")) transistor_25 (.in(transistor_26_out), .out(transistor_24_out), .gate(transistor_5_out));
  Transistor #(.\type ("n")) transistor_26 (.in(1'b0), .out(transistor_26_out), .gate(transistor_19_out));
  Transistor transistor_27 (.in(1'b1), .out(transistor_27_out), .gate(transistor_31_out));
  Transistor transistor_28 (.in(transistor_27_out), .out(transistor_24_out), .gate(transistor_5_out));
  Transistor #(.\type ("n")) transistor_29 (.in(transistor_30_out), .out(transistor_24_out), .gate(transistor_1_out));
  Transistor #(.\type ("n")) transistor_30 (.in(1'b0), .out(transistor_30_out), .gate(transistor_31_out));
  Transistor transistor_31 (.in(1'b1), .out(transistor_31_out), .gate(transistor_24_out));
  Transistor #(.\type ("n")) transistor_32 (.in(transistor_33_out), .out(transistor_31_out), .gate(transistor_24_out));
  Transistor #(.\type ("n")) transistor_33 (.in(1'b0), .out(transistor_33_out), .gate(transistor_17_out));
  Transistor transistor_34 (.in(1'b1), .out(d_out), .gate(transistor_31_out));
  Transistor transistor_35 (.in(1'b1), .out(transistor_31_out), .gate(transistor_17_out));
  Transistor #(.\type ("n")) transistor_36 (.in(1'b0), .out(d_out), .gate(transistor_31_out));
endmodule

module cell52 (
  input  nload,
  input  val,
  input  nc1,
  input  nc2,
  input  load,
  input  c_in,
  input  r,
  input  c1,
  input  c2,
  output c_out,
  output s
);

  wire transistor_1_out, transistor_3_out, transistor_7_out, transistor_8_out, transistor_9_out,
       transistor_12_out, transistor_13_out, transistor_16_out, transistor_17_out, transistor_19_out,
       transistor_20_out, transistor_22_out, transistor_25_out, transistor_26_out, transistor_28_out,
       transistor_29_out, transistor_30_out, transistor_32_out;

  Transistor transistor_1 (.in(1'b1), .out(transistor_1_out), .gate(c_in));
  Transistor #(.\type ("n")) transistor_2 (.in(1'b0), .out(transistor_1_out), .gate(c_in));
  Transistor transistor_3 (.in(1'b1), .out(transistor_3_out), .gate(transistor_26_out));
  Transistor transistor_4 (.in(transistor_3_out), .out(c_out), .gate(transistor_1_out));
  Transistor #(.\type ("n")) transistor_5 (.in(1'b0), .out(c_out), .gate(transistor_1_out));
  Transistor #(.\type ("n")) transistor_6 (.in(1'b0), .out(c_out), .gate(transistor_26_out));
  Transistor transistor_7 (.in(1'b1), .out(transistor_7_out), .gate(transistor_1_out));
  Transistor transistor_8 (.in(transistor_7_out), .out(transistor_8_out), .gate(c_out));
  Transistor transistor_9 (.in(transistor_8_out), .out(transistor_9_out), .gate(r));
  Transistor #(.\type ("n")) transistor_10 (.in(1'b0), .out(transistor_9_out), .gate(r));
  Transistor #(.\type ("n")) transistor_11 (.in(1'b0), .out(transistor_9_out), .gate(c_out));
  Transistor transistor_12 (.in(1'b1), .out(transistor_12_out), .gate(c_out));
  Transistor transistor_13 (.in(transistor_12_out), .out(transistor_13_out), .gate(transistor_26_out));
  Transistor transistor_14 (.in(transistor_13_out), .out(transistor_9_out), .gate(r));
  Transistor #(.\type ("n")) transistor_15 (.in(transistor_16_out), .out(transistor_9_out), .gate(transistor_26_out));
  Transistor #(.\type ("n")) transistor_16 (.in(1'b0), .out(transistor_16_out), .gate(transistor_1_out));
  Transistor transistor_17 (.in(transistor_9_out), .out(transistor_17_out), .gate(nc1));
  Transistor #(.\type ("n")) transistor_18 (.in(transistor_9_out), .out(transistor_17_out), .gate(c1));
  Transistor transistor_19 (.in(1'b1), .out(transistor_19_out), .gate(transistor_17_out));
  Transistor transistor_20 (.in(transistor_19_out), .out(transistor_20_out), .gate(nc2));
  Transistor #(.\type ("n")) transistor_21 (.in(transistor_22_out), .out(transistor_20_out), .gate(c2));
  Transistor #(.\type ("n")) transistor_22 (.in(1'b0), .out(transistor_22_out), .gate(transistor_17_out));
  Transistor transistor_23 (.in(1'b1), .out(s), .gate(transistor_20_out));
  Transistor #(.\type ("n")) transistor_24 (.in(1'b0), .out(s), .gate(transistor_20_out));
  Transistor transistor_25 (.in(1'b1), .out(transistor_25_out), .gate(s));
  Transistor transistor_26 (.in(transistor_25_out), .out(transistor_26_out), .gate(load));
  Transistor #(.\type ("n"), .gate("br")) transistor_27 (.in(transistor_28_out), .out(transistor_26_out), .gate(nload));
  Transistor #(.\type ("n")) transistor_28 (.in(1'b0), .out(transistor_28_out), .gate(s));
  Transistor transistor_29 (.in(1'b1), .out(transistor_29_out), .gate(val));
  Transistor transistor_30 (.in(transistor_29_out), .out(transistor_30_out), .gate(nload));
  Transistor #(.\type ("n")) transistor_31 (.in(transistor_32_out), .out(transistor_30_out), .gate(load));
  Transistor #(.\type ("n")) transistor_32 (.in(1'b0), .out(transistor_32_out), .gate(val));
endmodule

module cell53__AON222 (
  input  a,
  input  b,
  input  c,
  input  d,
  input  a_2,
  input  b_2,
  input  e,
  input  d_2,
  input  c_2,
  input  e_2,
  input  f,
  input  f_2,
  output g,
  output g_2
);

  wire and_1_out, and_2_out, and_3_out, transistor_1_out, transistor_2_out, transistor_3_out,
       transistor_6_out, transistor_7_out, transistor_14_out;

  Transistor transistor_1 (.in(1'b1), .out(transistor_1_out), .gate(b));
  Transistor transistor_2 (.in(transistor_1_out), .out(transistor_2_out), .gate(d));
  Transistor transistor_3 (.in(transistor_2_out), .out(transistor_3_out), .gate(e));
  Transistor #(.\type ("n")) transistor_4 (.in(transistor_6_out), .out(transistor_3_out), .gate(a));
  Transistor #(.\type ("n")) transistor_5 (.in(transistor_7_out), .out(transistor_3_out), .gate(c));
  Transistor #(.\type ("n")) transistor_6 (.in(1'b0), .out(transistor_6_out), .gate(b));
  Transistor #(.\type ("n")) transistor_7 (.in(1'b0), .out(transistor_7_out), .gate(d));
  Transistor transistor_8 (.in(1'b1), .out(transistor_1_out), .gate(a));
  Transistor transistor_9 (.in(transistor_1_out), .out(transistor_2_out), .gate(c));
  Transistor transistor_10 (.in(1'b1), .out(g), .gate(transistor_3_out));
  Transistor transistor_11 (.in(transistor_2_out), .out(transistor_3_out), .gate(f_2));
  Transistor #(.\type ("n")) transistor_12 (.in(transistor_14_out), .out(transistor_3_out), .gate(e));
  Transistor #(.\type ("n")) transistor_13 (.in(1'b0), .out(g), .gate(transistor_3_out));
  Transistor #(.\type ("n")) transistor_14 (.in(1'b0), .out(transistor_14_out), .gate(f_2));
  and and_1 (and_1_out, a_2, b_2);
  and and_2 (and_2_out, d_2, c_2);
  and and_3 (and_3_out, e_2, f);
  or or_1 (g_2, and_1_out, and_2_out, and_3_out);

  // Notes on the sheet:
  //   ~
  //   AON222
endmodule

module cell54__AOI222222 (
  input  a,
  input  a_2,
  input  b,
  input  b_2,
  input  d,
  input  c,
  input  c_2,
  input  d_2,
  input  e,
  input  e_2,
  input  f,
  input  f_2,
  input  h,
  input  i,
  input  j,
  input  k,
  input  l,
  input  m,
  input  h_2,
  input  i_2,
  input  j_2,
  input  k_2,
  input  l_2,
  input  m_2,
  output g,
  output g_2
);

  wire and_1_out, and_2_out, and_3_out, and_4_out, and_5_out, and_6_out, nor_1_out, nor_2_out,
       transistor_1_out, transistor_2_out, transistor_3_out, transistor_5_out, transistor_6_out,
       transistor_7_out, transistor_8_out, transistor_10_out, transistor_16_out, transistor_17_out,
       transistor_23_out, transistor_24_out, transistor_25_out, transistor_28_out;

  Transistor transistor_1 (.in(1'b1), .out(transistor_1_out), .gate(e_2));
  Transistor transistor_2 (.in(transistor_1_out), .out(transistor_2_out), .gate(d_2));
  Transistor transistor_3 (.in(transistor_2_out), .out(transistor_3_out), .gate(b_2));
  Transistor #(.\type ("n")) transistor_4 (.in(transistor_5_out), .out(transistor_3_out), .gate(f_2));
  Transistor #(.\type ("n")) transistor_5 (.in(1'b0), .out(transistor_5_out), .gate(e_2));
  Transistor transistor_6 (.in(1'b1), .out(transistor_6_out), .gate(i_2));
  Transistor transistor_7 (.in(transistor_6_out), .out(transistor_7_out), .gate(j_2));
  Transistor transistor_8 (.in(transistor_7_out), .out(transistor_8_out), .gate(l_2));
  Transistor #(.\type ("n")) transistor_9 (.in(transistor_10_out), .out(transistor_8_out), .gate(h_2));
  Transistor #(.\type ("n")) transistor_10 (.in(1'b0), .out(transistor_10_out), .gate(i_2));
  Transistor transistor_11 (.in(1'b1), .out(transistor_1_out), .gate(f_2));
  Transistor transistor_12 (.in(transistor_1_out), .out(transistor_2_out), .gate(c));
  Transistor transistor_13 (.in(transistor_2_out), .out(transistor_3_out), .gate(a_2));
  Transistor #(.\type ("n")) transistor_14 (.in(transistor_16_out), .out(transistor_3_out), .gate(c));
  Transistor #(.\type ("n")) transistor_15 (.in(transistor_17_out), .out(transistor_3_out), .gate(b_2));
  Transistor #(.\type ("n")) transistor_16 (.in(1'b0), .out(transistor_16_out), .gate(d_2));
  Transistor #(.\type ("n")) transistor_17 (.in(1'b0), .out(transistor_17_out), .gate(a_2));
  Transistor transistor_18 (.in(1'b1), .out(transistor_6_out), .gate(h_2));
  Transistor transistor_19 (.in(transistor_6_out), .out(transistor_7_out), .gate(k_2));
  Transistor transistor_20 (.in(transistor_7_out), .out(transistor_8_out), .gate(m_2));
  Transistor #(.\type ("n")) transistor_21 (.in(transistor_24_out), .out(transistor_8_out), .gate(l_2));
  Transistor #(.\type ("n")) transistor_22 (.in(transistor_23_out), .out(transistor_8_out), .gate(k_2));
  Transistor #(.\type ("n")) transistor_23 (.in(1'b0), .out(transistor_23_out), .gate(j_2));
  Transistor #(.\type ("n")) transistor_24 (.in(1'b0), .out(transistor_24_out), .gate(m_2));
  Transistor transistor_25 (.in(1'b1), .out(transistor_25_out), .gate(transistor_8_out));
  Transistor transistor_26 (.in(1'b1), .out(transistor_25_out), .gate(transistor_3_out));
  Transistor #(.\type ("n")) transistor_27 (.in(transistor_28_out), .out(transistor_25_out), .gate(transistor_3_out));
  Transistor #(.\type ("n")) transistor_28 (.in(1'b0), .out(transistor_28_out), .gate(transistor_8_out));
  Transistor transistor_29 (.in(1'b1), .out(g_2), .gate(transistor_25_out));
  Transistor #(.\type ("n")) transistor_30 (.in(1'b0), .out(g_2), .gate(transistor_25_out));
  and and_1 (and_1_out, a, b);
  and and_2 (and_2_out, d, c_2);
  and and_3 (and_3_out, e, f);
  and and_4 (and_4_out, h, i);
  and and_5 (and_5_out, j, k);
  and and_6 (and_6_out, l, m);
  nor nor_1 (nor_1_out, and_1_out, and_2_out, and_3_out);
  nor nor_2 (nor_2_out, and_4_out, and_5_out, and_6_out);
  and and_7 (g, nor_1_out, nor_2_out);

  // Notes on the sheet:
  //   ~
  //   AOI222222
endmodule

module cell55__AON22222222 (
  input  a,
  input  a_2,
  input  i,
  input  b,
  input  b_2,
  input  j,
  input  c,
  input  c_2,
  input  k,
  input  d,
  input  d_2,
  input  l,
  input  e,
  input  e_2,
  input  m,
  input  f,
  input  f_2,
  input  n,
  input  g,
  input  g_2,
  input  o,
  input  h,
  input  h_2,
  input  p,
  input  i_2,
  input  j_2,
  input  k_2,
  input  l_2,
  input  m_2,
  input  n_2,
  input  o_2,
  input  p_2,
  output X,
  output X_2
);

  wire and_1_out, and_2_out, and_3_out, and_4_out, and_5_out, and_6_out, and_7_out, and_8_out, nor_1_out,
       nor_2_out, transistor_1_out, transistor_2_out, transistor_3_out, transistor_5_out, transistor_7_out,
       transistor_13_out, transistor_14_out, transistor_16_out, transistor_17_out, transistor_18_out,
       transistor_19_out, transistor_20_out, transistor_21_out, transistor_24_out, transistor_30_out,
       transistor_32_out, transistor_35_out;

  Transistor #(.\type ("n")) transistor_1 (.in(transistor_2_out), .out(transistor_1_out), .gate(b_2));
  Transistor #(.\type ("n")) transistor_2 (.in(1'b0), .out(transistor_2_out), .gate(a_2));
  Transistor transistor_3 (.in(1'b1), .out(transistor_3_out), .gate(g_2));
  Transistor transistor_4 (.in(1'b1), .out(transistor_3_out), .gate(h_2));
  Transistor transistor_5 (.in(transistor_3_out), .out(transistor_5_out), .gate(e_2));
  Transistor transistor_6 (.in(transistor_3_out), .out(transistor_5_out), .gate(f_2));
  Transistor transistor_7 (.in(transistor_5_out), .out(transistor_7_out), .gate(c_2));
  Transistor transistor_8 (.in(transistor_5_out), .out(transistor_7_out), .gate(d_2));
  Transistor transistor_9 (.in(transistor_7_out), .out(transistor_1_out), .gate(b_2));
  Transistor transistor_10 (.in(transistor_7_out), .out(transistor_1_out), .gate(a_2));
  Transistor #(.\type ("n")) transistor_11 (.in(transistor_14_out), .out(transistor_1_out), .gate(f_2));
  Transistor #(.\type ("n")) transistor_12 (.in(transistor_13_out), .out(transistor_1_out), .gate(c_2));
  Transistor #(.\type ("n")) transistor_13 (.in(1'b0), .out(transistor_13_out), .gate(d_2));
  Transistor #(.\type ("n")) transistor_14 (.in(1'b0), .out(transistor_14_out), .gate(e_2));
  Transistor #(.\type ("n")) transistor_15 (.in(transistor_16_out), .out(transistor_1_out), .gate(g_2));
  Transistor #(.\type ("n")) transistor_16 (.in(1'b0), .out(transistor_16_out), .gate(h_2));
  Transistor #(.\type ("n")) transistor_17 (.in(transistor_18_out), .out(transistor_17_out), .gate(j));
  Transistor #(.\type ("n")) transistor_18 (.in(1'b0), .out(transistor_18_out), .gate(i));
  Transistor transistor_19 (.in(1'b1), .out(transistor_19_out), .gate(o));
  Transistor transistor_20 (.in(transistor_19_out), .out(transistor_20_out), .gate(m));
  Transistor transistor_21 (.in(transistor_20_out), .out(transistor_21_out), .gate(k));
  Transistor transistor_22 (.in(transistor_21_out), .out(transistor_17_out), .gate(i));
  Transistor #(.\type ("n")) transistor_23 (.in(transistor_24_out), .out(transistor_17_out), .gate(k));
  Transistor #(.\type ("n")) transistor_24 (.in(1'b0), .out(transistor_24_out), .gate(l));
  Transistor transistor_25 (.in(1'b1), .out(transistor_19_out), .gate(p));
  Transistor transistor_26 (.in(transistor_19_out), .out(transistor_20_out), .gate(n));
  Transistor transistor_27 (.in(transistor_20_out), .out(transistor_21_out), .gate(l));
  Transistor transistor_28 (.in(transistor_21_out), .out(transistor_17_out), .gate(j));
  Transistor #(.\type ("n")) transistor_29 (.in(transistor_30_out), .out(transistor_17_out), .gate(n));
  Transistor #(.\type ("n")) transistor_30 (.in(1'b0), .out(transistor_30_out), .gate(m));
  Transistor #(.\type ("n")) transistor_31 (.in(transistor_32_out), .out(transistor_17_out), .gate(o));
  Transistor #(.\type ("n")) transistor_32 (.in(1'b0), .out(transistor_32_out), .gate(p));
  Transistor transistor_33 (.in(1'b1), .out(X), .gate(transistor_1_out));
  Transistor #(.\type ("n")) transistor_34 (.in(transistor_35_out), .out(X), .gate(transistor_1_out));
  Transistor #(.\type ("n")) transistor_35 (.in(1'b0), .out(transistor_35_out), .gate(transistor_17_out));
  Transistor transistor_36 (.in(1'b1), .out(X), .gate(transistor_17_out));
  and and_1 (and_1_out, a, b);
  and and_2 (and_2_out, c, d);
  and and_3 (and_3_out, e, f);
  and and_4 (and_4_out, g, h);
  and and_5 (and_5_out, i_2, j_2);
  and and_6 (and_6_out, k_2, l_2);
  and and_7 (and_7_out, m_2, n_2);
  and and_8 (and_8_out, o_2, p_2);
  nor nor_1 (nor_1_out, and_1_out, and_2_out, and_3_out, and_4_out);
  nor nor_2 (nor_2_out, and_5_out, and_6_out, and_7_out, and_8_out);
  nand nand_1 (X_2, nor_1_out, nor_2_out);

  // Notes on the sheet:
  //   ~
  //   AON22222222
endmodule

module cell56 (
  input  nc2,
  input  nc2_2,
  input  in_3,
  input  c1,
  input  c2,
  output out_6
);

  wire transistor_2_out, transistor_4_out, transistor_6_out, transistor_7_out, transistor_9_out;

  Transistor transistor_1 (.in(1'b1), .out(in_3), .gate(nc2_2));
  Transistor transistor_2 (.in(1'b1), .out(transistor_2_out), .gate(in_3));
  Transistor #(.\type ("n")) transistor_3 (.in(1'b0), .out(transistor_2_out), .gate(in_3));
  Transistor transistor_4 (.in(transistor_2_out), .out(transistor_4_out), .gate(nc2));
  Transistor #(.\type ("n")) transistor_5 (.in(transistor_2_out), .out(transistor_4_out), .gate(c1));
  Transistor transistor_6 (.in(1'b1), .out(transistor_6_out), .gate(transistor_4_out));
  Transistor transistor_7 (.in(transistor_6_out), .out(transistor_7_out), .gate(nc2_2));
  Transistor #(.\type ("n")) transistor_8 (.in(transistor_9_out), .out(transistor_7_out), .gate(c2));
  Transistor #(.\type ("n")) transistor_9 (.in(1'b0), .out(transistor_9_out), .gate(transistor_4_out));
  Transistor transistor_10 (.in(1'b1), .out(out_6), .gate(transistor_7_out));
  Transistor #(.\type ("n")) transistor_11 (.in(1'b0), .out(out_6), .gate(transistor_7_out));
endmodule

module cell57__AOI33 (
  input  a,
  input  b,
  input  a_2,
  input  c,
  input  b_2,
  input  c_2,
  input  d,
  input  d_2,
  input  e,
  input  e_2,
  input  f,
  input  f_2,
  output g,
  output g_2
);

  wire and_1_out, and_2_out, transistor_1_out, transistor_4_out, transistor_5_out, transistor_11_out,
       transistor_12_out;

  Transistor transistor_1 (.in(1'b1), .out(transistor_1_out), .gate(d_2));
  Transistor transistor_2 (.in(transistor_1_out), .out(g), .gate(a));
  Transistor #(.\type ("n")) transistor_3 (.in(transistor_4_out), .out(g), .gate(c));
  Transistor #(.\type ("n")) transistor_4 (.in(transistor_5_out), .out(transistor_4_out), .gate(b));
  Transistor #(.\type ("n")) transistor_5 (.in(1'b0), .out(transistor_5_out), .gate(a));
  Transistor transistor_6 (.in(1'b1), .out(transistor_1_out), .gate(e_2));
  Transistor transistor_7 (.in(transistor_1_out), .out(g), .gate(b));
  Transistor transistor_8 (.in(1'b1), .out(transistor_1_out), .gate(f_2));
  Transistor transistor_9 (.in(transistor_1_out), .out(g), .gate(c));
  Transistor #(.\type ("n")) transistor_10 (.in(transistor_11_out), .out(g), .gate(d_2));
  Transistor #(.\type ("n")) transistor_11 (.in(transistor_12_out), .out(transistor_11_out), .gate(e_2));
  Transistor #(.\type ("n")) transistor_12 (.in(1'b0), .out(transistor_12_out), .gate(f_2));
  and and_1 (and_1_out, a_2, b_2, c_2);
  and and_2 (and_2_out, d, e, f);
  nor nor_1 (g_2, and_1_out, and_2_out);

  // Notes on the sheet:
  //   ~
  //   AOI33
endmodule

module cell58__AOI333 (
  input  a,
  input  a_2,
  input  b,
  input  b_2,
  input  c,
  input  c_2,
  input  d,
  input  d_2,
  input  e,
  input  e_2,
  input  f,
  input  f_2,
  input  g,
  input  g_2,
  input  h,
  input  h_2,
  input  i,
  input  i_2,
  output j,
  output j_2
);

  wire and_1_out, and_2_out, and_3_out, transistor_1_out, transistor_2_out, transistor_5_out,
       transistor_6_out, transistor_11_out, transistor_12_out, transistor_17_out, transistor_18_out;

  Transistor transistor_1 (.in(1'b1), .out(transistor_1_out), .gate(a_2));
  Transistor transistor_2 (.in(transistor_1_out), .out(transistor_2_out), .gate(d_2));
  Transistor transistor_3 (.in(transistor_2_out), .out(j), .gate(g_2));
  Transistor #(.\type ("n")) transistor_4 (.in(transistor_5_out), .out(j), .gate(c_2));
  Transistor #(.\type ("n")) transistor_5 (.in(transistor_6_out), .out(transistor_5_out), .gate(b_2));
  Transistor #(.\type ("n")) transistor_6 (.in(1'b0), .out(transistor_6_out), .gate(a_2));
  Transistor transistor_7 (.in(1'b1), .out(transistor_1_out), .gate(b_2));
  Transistor transistor_8 (.in(transistor_1_out), .out(transistor_2_out), .gate(e_2));
  Transistor transistor_9 (.in(transistor_2_out), .out(j), .gate(h_2));
  Transistor #(.\type ("n")) transistor_10 (.in(transistor_11_out), .out(j), .gate(d_2));
  Transistor #(.\type ("n")) transistor_11 (.in(transistor_12_out), .out(transistor_11_out), .gate(e_2));
  Transistor #(.\type ("n")) transistor_12 (.in(1'b0), .out(transistor_12_out), .gate(f_2));
  Transistor transistor_13 (.in(1'b1), .out(transistor_1_out), .gate(c_2));
  Transistor transistor_14 (.in(transistor_1_out), .out(transistor_2_out), .gate(f_2));
  Transistor transistor_15 (.in(transistor_2_out), .out(j), .gate(i_2));
  Transistor #(.\type ("n")) transistor_16 (.in(transistor_17_out), .out(j), .gate(i_2));
  Transistor #(.\type ("n")) transistor_17 (.in(transistor_18_out), .out(transistor_17_out), .gate(h_2));
  Transistor #(.\type ("n")) transistor_18 (.in(1'b0), .out(transistor_18_out), .gate(g_2));
  and and_1 (and_1_out, a, b, c);
  and and_2 (and_2_out, d, e, f);
  and and_3 (and_3_out, g, h, i);
  nor nor_1 (j_2, and_1_out, and_2_out, and_3_out);

  // Notes on the sheet:
  //   ~
  //   AOI333
endmodule

module cell59__AON3333 (
  input  a,
  input  b,
  input  a_2,
  input  c,
  input  b_2,
  input  d,
  input  c_2,
  input  e,
  input  d_2,
  input  f,
  input  e_2,
  input  g,
  input  f_2,
  input  h,
  input  g_2,
  input  i,
  input  h_2,
  input  j,
  input  i_2,
  input  k,
  input  j_2,
  input  l,
  input  k_2,
  input  l_2,
  output m,
  output m_2
);

  wire and_1_out, and_2_out, and_3_out, and_4_out, transistor_1_out, transistor_2_out, transistor_3_out,
       transistor_4_out, transistor_5_out, transistor_6_out, transistor_9_out, transistor_10_out,
       transistor_20_out, transistor_21_out, transistor_25_out, transistor_26_out;

  Transistor #(.\type ("n")) transistor_1 (.in(transistor_2_out), .out(transistor_1_out), .gate(c));
  Transistor #(.\type ("n")) transistor_2 (.in(transistor_3_out), .out(transistor_2_out), .gate(b));
  Transistor #(.\type ("n")) transistor_3 (.in(1'b0), .out(transistor_3_out), .gate(a));
  Transistor transistor_4 (.in(1'b1), .out(transistor_4_out), .gate(c));
  Transistor transistor_5 (.in(transistor_4_out), .out(transistor_5_out), .gate(f));
  Transistor transistor_6 (.in(transistor_5_out), .out(transistor_6_out), .gate(i));
  Transistor transistor_7 (.in(transistor_6_out), .out(transistor_1_out), .gate(l));
  Transistor #(.\type ("n")) transistor_8 (.in(transistor_9_out), .out(transistor_1_out), .gate(d));
  Transistor #(.\type ("n")) transistor_9 (.in(transistor_10_out), .out(transistor_9_out), .gate(e));
  Transistor #(.\type ("n")) transistor_10 (.in(1'b0), .out(transistor_10_out), .gate(f));
  Transistor transistor_11 (.in(1'b1), .out(transistor_4_out), .gate(b));
  Transistor transistor_12 (.in(1'b1), .out(transistor_4_out), .gate(a));
  Transistor transistor_13 (.in(transistor_4_out), .out(transistor_5_out), .gate(d));
  Transistor transistor_14 (.in(transistor_4_out), .out(transistor_5_out), .gate(e));
  Transistor transistor_15 (.in(transistor_5_out), .out(transistor_6_out), .gate(h));
  Transistor transistor_16 (.in(transistor_5_out), .out(transistor_6_out), .gate(g));
  Transistor transistor_17 (.in(transistor_6_out), .out(transistor_1_out), .gate(k));
  Transistor transistor_18 (.in(transistor_6_out), .out(transistor_1_out), .gate(j));
  Transistor #(.\type ("n")) transistor_19 (.in(transistor_20_out), .out(transistor_1_out), .gate(i));
  Transistor #(.\type ("n")) transistor_20 (.in(transistor_21_out), .out(transistor_20_out), .gate(h));
  Transistor #(.\type ("n")) transistor_21 (.in(1'b0), .out(transistor_21_out), .gate(g));
  Transistor transistor_22 (.in(1'b1), .out(m), .gate(transistor_1_out));
  Transistor #(.\type ("n")) transistor_23 (.in(1'b0), .out(m), .gate(transistor_1_out));
  Transistor #(.\type ("n")) transistor_24 (.in(transistor_25_out), .out(transistor_1_out), .gate(j));
  Transistor #(.\type ("n")) transistor_25 (.in(transistor_26_out), .out(transistor_25_out), .gate(k));
  Transistor #(.\type ("n")) transistor_26 (.in(1'b0), .out(transistor_26_out), .gate(l));
  and and_1 (and_1_out, a_2, b_2, c_2);
  and and_2 (and_2_out, d_2, e_2, f_2);
  and and_3 (and_3_out, g_2, h_2, i_2);
  and and_4 (and_4_out, j_2, k_2, l_2);
  or or_1 (m_2, and_1_out, and_2_out, and_3_out, and_4_out);

  // Notes on the sheet:
  //   ~
  //   AON3333
endmodule

module cell60 (
  input  nc1,
  input  a,
  input  c1,
  output b
);

  wire transistor_1_out;

  Transistor transistor_1 (.in(a), .out(transistor_1_out), .gate(nc1));
  Transistor #(.\type ("n")) transistor_2 (.in(a), .out(transistor_1_out), .gate(c1));
  Transistor transistor_3 (.in(1'b1), .out(b), .gate(transistor_1_out));
  Transistor #(.\type ("n")) transistor_4 (.in(1'b0), .out(b), .gate(transistor_1_out));
  Transistor transistor_5 (.in(1'b1), .out(b), .gate(transistor_1_out));
  Transistor #(.\type ("n")) transistor_6 (.in(1'b0), .out(b), .gate(transistor_1_out));
endmodule

module cell61__AON21SR (
  input  nc1,
  input  nc2,
  input  a,
  input  a_2,
  input  c1,
  input  c2,
  input  b,
  input  b_2,
  input  c,
  input  c_2,
  input  c1_2,
  input  c2_2,
  output d,
  output d_2
);

  wire and_1_out, d_ff_1_qn, nor_1_out, transistor_1_out, transistor_2_out, transistor_4_out,
       transistor_7_out, transistor_8_out, transistor_10_out, transistor_11_out, transistor_12_out,
       transistor_14_out;

  Transistor transistor_1 (.in(1'b1), .out(transistor_1_out), .gate(a));
  Transistor transistor_2 (.in(transistor_1_out), .out(transistor_2_out), .gate(c_2));
  Transistor #(.\type ("n")) transistor_3 (.in(transistor_4_out), .out(transistor_2_out), .gate(b_2));
  Transistor #(.\type ("n")) transistor_4 (.in(1'b0), .out(transistor_4_out), .gate(a));
  Transistor transistor_5 (.in(1'b1), .out(transistor_1_out), .gate(b_2));
  Transistor #(.\type ("n")) transistor_6 (.in(1'b0), .out(transistor_2_out), .gate(c_2));
  Transistor transistor_7 (.in(1'b1), .out(transistor_7_out), .gate(transistor_2_out));
  Transistor transistor_8 (.in(transistor_7_out), .out(transistor_8_out), .gate(nc1));
  Transistor #(.\type ("n")) transistor_9 (.in(transistor_10_out), .out(transistor_8_out), .gate(c1_2));
  Transistor #(.\type ("n")) transistor_10 (.in(1'b0), .out(transistor_10_out), .gate(transistor_2_out));
  Transistor transistor_11 (.in(1'b1), .out(transistor_11_out), .gate(transistor_8_out));
  Transistor transistor_12 (.in(transistor_11_out), .out(transistor_12_out), .gate(nc2));
  Transistor #(.\type ("n")) transistor_13 (.in(transistor_14_out), .out(transistor_12_out), .gate(c2_2));
  Transistor #(.\type ("n")) transistor_14 (.in(1'b0), .out(transistor_14_out), .gate(transistor_8_out));
  Transistor transistor_15 (.in(1'b1), .out(d), .gate(transistor_12_out));
  Transistor #(.\type ("n")) transistor_16 (.in(1'b0), .out(d), .gate(transistor_12_out));
  and and_1 (and_1_out, a_2, b);
  nor nor_1 (nor_1_out, and_1_out, c);
  D_Flip_Flop #(.trigger("high")) d_ff_1 (.clk(c1), .D(nor_1_out), .Qn(d_ff_1_qn));  // open: Q, preset, en, reset
  D_Flip_Flop #(.trigger("high")) d_ff_2 (.clk(c2), .D(d_ff_1_qn), .Qn(d_2));  // open: Q, preset, en, reset

  // Notes on the sheet:
  //   ~
  //   AON21SR
endmodule

module cell62__AOI221 (
  input  b,
  input  c,
  input  d,
  input  b_2,
  input  c_2,
  input  e,
  input  d_2,
  input  f,
  input  e_2,
  input  f_2,
  output X,
  output X_2
);

  wire and_1_out, and_2_out, transistor_2_out, transistor_3_out, transistor_6_out, transistor_10_out;

  Transistor #(.\type ("n")) transistor_1 (.in(1'b0), .out(X_2), .gate(b));
  Transistor transistor_2 (.in(1'b1), .out(transistor_2_out), .gate(c));
  Transistor transistor_3 (.in(transistor_2_out), .out(transistor_3_out), .gate(f));
  Transistor transistor_4 (.in(transistor_3_out), .out(X_2), .gate(b));
  Transistor #(.\type ("n")) transistor_5 (.in(transistor_6_out), .out(X_2), .gate(c));
  Transistor #(.\type ("n")) transistor_6 (.in(1'b0), .out(transistor_6_out), .gate(d));
  Transistor transistor_7 (.in(1'b1), .out(transistor_2_out), .gate(d));
  Transistor transistor_8 (.in(transistor_2_out), .out(transistor_3_out), .gate(e));
  Transistor #(.\type ("n")) transistor_9 (.in(transistor_10_out), .out(X_2), .gate(f));
  Transistor #(.\type ("n")) transistor_10 (.in(1'b0), .out(transistor_10_out), .gate(e));
  and and_1 (and_1_out, c_2, d_2);
  and and_2 (and_2_out, e_2, f_2);
  nor nor_1 (X, b_2, and_1_out, and_2_out);

  // Notes on the sheet:
  //   ~
  //   AOI221
endmodule

module cell63___NAND5 (
  input  a,
  input  b,
  input  c,
  input  a_2,
  input  b_2,
  input  d,
  input  c_2,
  input  d_2,
  input  e,
  input  e_2,
  output X,
  output X_2
);

  wire transistor_1_out, transistor_3_out, transistor_4_out, transistor_5_out, transistor_8_out,
       transistor_10_out, transistor_12_out;

  Transistor transistor_1 (.in(1'b1), .out(transistor_1_out), .gate(c));
  Transistor #(.\type ("n")) transistor_2 (.in(transistor_3_out), .out(transistor_1_out), .gate(a));
  Transistor #(.\type ("n")) transistor_3 (.in(transistor_4_out), .out(transistor_3_out), .gate(b));
  Transistor #(.\type ("n")) transistor_4 (.in(1'b0), .out(transistor_4_out), .gate(c));
  Transistor transistor_5 (.in(1'b1), .out(transistor_5_out), .gate(d));
  Transistor transistor_6 (.in(1'b1), .out(transistor_5_out), .gate(e));
  Transistor #(.\type ("n")) transistor_7 (.in(transistor_8_out), .out(transistor_5_out), .gate(d));
  Transistor #(.\type ("n")) transistor_8 (.in(1'b0), .out(transistor_8_out), .gate(e));
  Transistor transistor_9 (.in(1'b1), .out(transistor_1_out), .gate(b));
  Transistor #(.\type ("n")) transistor_10 (.in(1'b0), .out(transistor_10_out), .gate(transistor_5_out));
  Transistor transistor_11 (.in(1'b1), .out(transistor_1_out), .gate(a));
  Transistor transistor_12 (.in(1'b1), .out(transistor_12_out), .gate(transistor_5_out));
  Transistor transistor_13 (.in(transistor_12_out), .out(transistor_10_out), .gate(transistor_1_out));
  Transistor #(.\type ("n")) transistor_14 (.in(1'b0), .out(transistor_10_out), .gate(transistor_1_out));
  Transistor transistor_15 (.in(1'b1), .out(X), .gate(transistor_10_out));
  Transistor #(.\type ("n")) transistor_16 (.in(1'b0), .out(X), .gate(transistor_10_out));
  nand nand_1 (X_2, a_2, b_2, c_2, d_2, e_2);

  // Notes on the sheet:
  //   ~
  //   NAND5
endmodule

module cell64__AON33 (
  input  a,
  input  b,
  input  a_2,
  input  c,
  input  b_2,
  input  d,
  input  c_2,
  input  e,
  input  d_2,
  input  f,
  input  e_2,
  input  f_2,
  output g,
  output g_2
);

  wire and_1_out, and_2_out, transistor_1_out, transistor_3_out, transistor_6_out, transistor_7_out,
       transistor_11_out, transistor_12_out;

  Transistor transistor_1 (.in(1'b1), .out(transistor_1_out), .gate(e));
  Transistor transistor_2 (.in(1'b1), .out(transistor_1_out), .gate(d));
  Transistor transistor_3 (.in(transistor_1_out), .out(transistor_3_out), .gate(a));
  Transistor transistor_4 (.in(transistor_1_out), .out(transistor_3_out), .gate(b));
  Transistor #(.\type ("n")) transistor_5 (.in(transistor_6_out), .out(transistor_3_out), .gate(c));
  Transistor #(.\type ("n")) transistor_6 (.in(transistor_7_out), .out(transistor_6_out), .gate(b));
  Transistor #(.\type ("n")) transistor_7 (.in(1'b0), .out(transistor_7_out), .gate(a));
  Transistor transistor_8 (.in(1'b1), .out(transistor_1_out), .gate(f));
  Transistor transistor_9 (.in(transistor_1_out), .out(transistor_3_out), .gate(c));
  Transistor #(.\type ("n")) transistor_10 (.in(transistor_11_out), .out(transistor_3_out), .gate(d));
  Transistor #(.\type ("n")) transistor_11 (.in(transistor_12_out), .out(transistor_11_out), .gate(e));
  Transistor #(.\type ("n")) transistor_12 (.in(1'b0), .out(transistor_12_out), .gate(f));
  Transistor transistor_13 (.in(1'b1), .out(g), .gate(transistor_3_out));
  Transistor #(.\type ("n")) transistor_14 (.in(1'b0), .out(g), .gate(transistor_3_out));
  and and_1 (and_1_out, a_2, b_2, c_2);
  or or_1 (g_2, and_1_out, and_2_out);
  and and_2 (and_2_out, d_2, e_2, f_2);

  // Notes on the sheet:
  //   ~
  //   AON33
endmodule

module cell65 (
  input  nc1,
  input  nc2,
  input  c,
  input  a,
  input  b,
  input  c1,
  input  c2,
  input  clk,
  input  C_2,
  input  A_2,
  input  B_2,
  output ns,
  output s,
  output c_out,
  output nQ,
  output Q,
  output c_out_2
);

  wire adder_1_out, d_ff_1_qn, not_1_out, transistor_1_out, transistor_2_out, transistor_4_out,
       transistor_7_out, transistor_8_out, transistor_11_out, transistor_12_out, transistor_14_out,
       transistor_19_out, transistor_20_out, transistor_23_out, transistor_24_out, transistor_25_out,
       transistor_26_out, transistor_28_out, transistor_31_out, transistor_32_out, transistor_34_out;

  Transistor transistor_1 (.in(1'b1), .out(transistor_1_out), .gate(a));
  Transistor transistor_2 (.in(transistor_1_out), .out(transistor_2_out), .gate(c));
  Transistor #(.\type ("n")) transistor_3 (.in(transistor_4_out), .out(transistor_2_out), .gate(c));
  Transistor #(.\type ("n")) transistor_4 (.in(1'b0), .out(transistor_4_out), .gate(a));
  Transistor transistor_5 (.in(1'b1), .out(transistor_1_out), .gate(b));
  Transistor #(.\type ("n")) transistor_6 (.in(1'b0), .out(transistor_4_out), .gate(b));
  Transistor transistor_7 (.in(1'b1), .out(transistor_7_out), .gate(c));
  Transistor transistor_8 (.in(1'b1), .out(transistor_8_out), .gate(b));
  Transistor transistor_9 (.in(transistor_8_out), .out(transistor_2_out), .gate(a));
  Transistor #(.\type ("n")) transistor_10 (.in(transistor_12_out), .out(transistor_2_out), .gate(a));
  Transistor #(.\type ("n")) transistor_11 (.in(1'b0), .out(transistor_11_out), .gate(c));
  Transistor #(.\type ("n")) transistor_12 (.in(1'b0), .out(transistor_12_out), .gate(b));
  Transistor transistor_13 (.in(1'b1), .out(transistor_7_out), .gate(a));
  Transistor transistor_14 (.in(transistor_7_out), .out(transistor_14_out), .gate(transistor_2_out));
  Transistor #(.\type ("n")) transistor_15 (.in(transistor_11_out), .out(transistor_14_out), .gate(transistor_2_out));
  Transistor #(.\type ("n")) transistor_16 (.in(1'b0), .out(transistor_11_out), .gate(a));
  Transistor transistor_17 (.in(1'b1), .out(transistor_7_out), .gate(b));
  Transistor #(.\type ("n")) transistor_18 (.in(1'b0), .out(transistor_11_out), .gate(b));
  Transistor transistor_19 (.in(1'b1), .out(transistor_19_out), .gate(b));
  Transistor transistor_20 (.in(transistor_19_out), .out(transistor_20_out), .gate(a));
  Transistor transistor_21 (.in(transistor_20_out), .out(transistor_14_out), .gate(c));
  Transistor #(.\type ("n")) transistor_22 (.in(transistor_23_out), .out(transistor_14_out), .gate(c));
  Transistor #(.\type ("n")) transistor_23 (.in(transistor_24_out), .out(transistor_23_out), .gate(a));
  Transistor #(.\type ("n")) transistor_24 (.in(1'b0), .out(transistor_24_out), .gate(b));
  Adder #(.width(1)) adder_1 (.a(A_2), .b(B_2), .out(adder_1_out), .cin(C_2), .cout(c_out_2));
  Transistor transistor_25 (.in(1'b1), .out(transistor_25_out), .gate(transistor_14_out));
  Transistor transistor_26 (.in(transistor_25_out), .out(transistor_26_out), .gate(nc1));
  Transistor #(.\type ("n")) transistor_27 (.in(transistor_28_out), .out(transistor_26_out), .gate(c1));
  Transistor #(.\type ("n")) transistor_28 (.in(1'b0), .out(transistor_28_out), .gate(transistor_14_out));
  Transistor transistor_29 (.in(1'b1), .out(c_out), .gate(transistor_2_out));
  Transistor #(.\type ("n")) transistor_30 (.in(1'b0), .out(c_out), .gate(transistor_2_out));
  not not_1 (not_1_out, clk);
  D_Flip_Flop #(.trigger("high")) d_ff_1 (.clk(clk), .D(adder_1_out), .Qn(d_ff_1_qn));  // open: Q, preset, en, reset
  D_Flip_Flop #(.trigger("high")) d_ff_2 (.clk(not_1_out), .D(d_ff_1_qn), .Q(nQ), .Qn(Q));  // open: preset, en, reset
  Transistor transistor_31 (.in(1'b1), .out(transistor_31_out), .gate(transistor_26_out));
  Transistor transistor_32 (.in(transistor_31_out), .out(transistor_32_out), .gate(nc2));
  Transistor #(.\type ("n")) transistor_33 (.in(transistor_34_out), .out(transistor_32_out), .gate(c2));
  Transistor #(.\type ("n")) transistor_34 (.in(1'b0), .out(transistor_34_out), .gate(transistor_26_out));
  Transistor transistor_35 (.in(1'b1), .out(s), .gate(transistor_32_out));
  Transistor #(.\type ("n")) transistor_36 (.in(1'b0), .out(s), .gate(transistor_32_out));
  Transistor transistor_37 (.in(1'b1), .out(ns), .gate(s));
  Transistor #(.\type ("n")) transistor_38 (.in(1'b0), .out(ns), .gate(s));

  // Notes on the sheet:
  //   ~
endmodule

module cell66___AOI222 (
  input  a,
  input  b,
  input  a_2,
  input  c,
  input  b_2,
  input  d,
  input  c_2,
  input  e,
  input  d_2,
  input  f,
  input  e_2,
  input  f_2,
  output g,
  output g_2
);

  wire and_1_out, and_2_out, and_3_out, transistor_1_out, transistor_2_out, transistor_5_out,
       transistor_11_out, transistor_12_out;

  Transistor transistor_1 (.in(1'b1), .out(transistor_1_out), .gate(b));
  Transistor transistor_2 (.in(transistor_1_out), .out(transistor_2_out), .gate(c));
  Transistor transistor_3 (.in(transistor_2_out), .out(g), .gate(e));
  Transistor #(.\type ("n")) transistor_4 (.in(transistor_5_out), .out(g), .gate(a));
  Transistor #(.\type ("n")) transistor_5 (.in(1'b0), .out(transistor_5_out), .gate(b));
  Transistor transistor_6 (.in(1'b1), .out(transistor_1_out), .gate(a));
  Transistor transistor_7 (.in(transistor_1_out), .out(transistor_2_out), .gate(d));
  Transistor transistor_8 (.in(transistor_2_out), .out(g), .gate(f));
  Transistor #(.\type ("n")) transistor_9 (.in(transistor_11_out), .out(g), .gate(e));
  Transistor #(.\type ("n")) transistor_10 (.in(transistor_12_out), .out(g), .gate(d));
  Transistor #(.\type ("n")) transistor_11 (.in(1'b0), .out(transistor_11_out), .gate(f));
  Transistor #(.\type ("n")) transistor_12 (.in(1'b0), .out(transistor_12_out), .gate(c));
  and and_1 (and_1_out, a_2, b_2);
  and and_2 (and_2_out, c_2, d_2);
  and and_3 (and_3_out, e_2, f_2);
  nor nor_1 (g_2, and_1_out, and_2_out, and_3_out);

  // Notes on the sheet:
  //   ~
  //   AOI222
endmodule

module cell67__OR8 (
  input  b,
  input  c,
  input  d,
  input  e,
  input  b_2,
  input  c_2,
  input  d_2,
  input  e_2,
  input  f,
  input  g,
  input  f_2,
  input  h,
  input  g_2,
  input  i,
  input  h_2,
  input  i_2,
  output j,
  output j_2
);

  wire nor_1_out, nor_2_out, transistor_1_out, transistor_2_out, transistor_3_out, transistor_4_out,
       transistor_7_out, transistor_8_out, transistor_9_out, transistor_10_out, transistor_20_out;

  Transistor transistor_1 (.in(1'b1), .out(transistor_1_out), .gate(b));
  Transistor transistor_2 (.in(transistor_1_out), .out(transistor_2_out), .gate(c));
  Transistor transistor_3 (.in(transistor_2_out), .out(transistor_3_out), .gate(d));
  Transistor transistor_4 (.in(transistor_3_out), .out(transistor_4_out), .gate(e));
  Transistor #(.\type ("n")) transistor_5 (.in(1'b0), .out(transistor_4_out), .gate(c));
  Transistor #(.\type ("n")) transistor_6 (.in(1'b0), .out(transistor_4_out), .gate(b));
  Transistor transistor_7 (.in(1'b1), .out(transistor_7_out), .gate(f_2));
  Transistor transistor_8 (.in(transistor_7_out), .out(transistor_8_out), .gate(g_2));
  Transistor transistor_9 (.in(transistor_8_out), .out(transistor_9_out), .gate(h_2));
  Transistor transistor_10 (.in(transistor_9_out), .out(transistor_10_out), .gate(i_2));
  Transistor #(.\type ("n")) transistor_11 (.in(1'b0), .out(transistor_10_out), .gate(g_2));
  Transistor #(.\type ("n")) transistor_12 (.in(1'b0), .out(transistor_10_out), .gate(f_2));
  Transistor #(.\type ("n")) transistor_13 (.in(1'b0), .out(transistor_4_out), .gate(e));
  Transistor #(.\type ("n")) transistor_14 (.in(1'b0), .out(transistor_4_out), .gate(d));
  Transistor #(.\type ("n")) transistor_15 (.in(1'b0), .out(transistor_10_out), .gate(h_2));
  Transistor #(.\type ("n")) transistor_16 (.in(1'b0), .out(transistor_10_out), .gate(i_2));
  Transistor transistor_17 (.in(1'b1), .out(j), .gate(transistor_10_out));
  Transistor transistor_18 (.in(1'b1), .out(j), .gate(transistor_4_out));
  Transistor #(.\type ("n")) transistor_19 (.in(transistor_20_out), .out(j), .gate(transistor_4_out));
  Transistor #(.\type ("n")) transistor_20 (.in(1'b0), .out(transistor_20_out), .gate(transistor_10_out));
  nor nor_1 (nor_1_out, b_2, c_2, d_2, e_2);
  nor nor_2 (nor_2_out, f, g, h, i);
  nand nand_1 (j_2, nor_1_out, nor_2_out);

  // Notes on the sheet:
  //   ~
  //   OR8
endmodule

module cell68__OR7 (
  input  a,
  input  b,
  input  c,
  input  a_2,
  input  b_2,
  input  c_2,
  input  d,
  input  d_2,
  input  e,
  input  e_2,
  input  f,
  input  f_2,
  input  g,
  input  g_2,
  output h,
  output h_2
);

  wire nor_1_out, nor_2_out, transistor_1_out, transistor_3_out, transistor_4_out, transistor_5_out,
       transistor_6_out, transistor_9_out, transistor_10_out, transistor_18_out;

  Transistor #(.\type ("n")) transistor_1 (.in(1'b0), .out(transistor_1_out), .gate(a));
  Transistor #(.\type ("n")) transistor_2 (.in(1'b0), .out(transistor_1_out), .gate(b));
  Transistor transistor_3 (.in(1'b1), .out(transistor_3_out), .gate(d_2));
  Transistor transistor_4 (.in(transistor_3_out), .out(transistor_4_out), .gate(e_2));
  Transistor transistor_5 (.in(transistor_4_out), .out(transistor_5_out), .gate(f_2));
  Transistor transistor_6 (.in(transistor_5_out), .out(transistor_6_out), .gate(g_2));
  Transistor #(.\type ("n")) transistor_7 (.in(1'b0), .out(transistor_6_out), .gate(d_2));
  Transistor #(.\type ("n")) transistor_8 (.in(1'b0), .out(transistor_6_out), .gate(e_2));
  Transistor transistor_9 (.in(1'b1), .out(transistor_9_out), .gate(c));
  Transistor transistor_10 (.in(transistor_9_out), .out(transistor_10_out), .gate(b));
  Transistor transistor_11 (.in(transistor_10_out), .out(transistor_1_out), .gate(a));
  Transistor #(.\type ("n")) transistor_12 (.in(1'b0), .out(transistor_1_out), .gate(c));
  Transistor #(.\type ("n")) transistor_13 (.in(1'b0), .out(transistor_6_out), .gate(g_2));
  Transistor #(.\type ("n")) transistor_14 (.in(1'b0), .out(transistor_6_out), .gate(f_2));
  Transistor transistor_15 (.in(1'b1), .out(h_2), .gate(transistor_6_out));
  Transistor transistor_16 (.in(1'b1), .out(h_2), .gate(transistor_1_out));
  Transistor #(.\type ("n")) transistor_17 (.in(transistor_18_out), .out(h_2), .gate(transistor_1_out));
  Transistor #(.\type ("n")) transistor_18 (.in(1'b0), .out(transistor_18_out), .gate(transistor_6_out));
  nor nor_1 (nor_1_out, a_2, b_2, c_2);
  nor nor_2 (nor_2_out, d, e, f, g);
  nand nand_1 (h, nor_1_out, nor_2_out);

  // Notes on the sheet:
  //   ~
  //   OR7
endmodule

module cell69__NAND7 (
  input  b,
  input  c,
  input  b_2,
  input  d,
  input  c_2,
  input  e,
  input  f,
  input  d_2,
  input  g,
  input  e_2,
  input  h,
  input  f_2,
  input  g_2,
  input  h_2,
  output a,
  output a_2
);

  wire nand_1_out, nand_2_out, transistor_1_out, transistor_4_out, transistor_5_out, transistor_6_out,
       transistor_7_out, transistor_13_out, transistor_14_out, transistor_15_out, transistor_16_out;

  Transistor transistor_1 (.in(1'b1), .out(transistor_1_out), .gate(e_2));
  Transistor transistor_2 (.in(1'b1), .out(transistor_1_out), .gate(d_2));
  Transistor #(.\type ("n")) transistor_3 (.in(transistor_4_out), .out(transistor_1_out), .gate(b_2));
  Transistor #(.\type ("n")) transistor_4 (.in(transistor_5_out), .out(transistor_4_out), .gate(c_2));
  Transistor #(.\type ("n")) transistor_5 (.in(transistor_6_out), .out(transistor_5_out), .gate(d_2));
  Transistor #(.\type ("n")) transistor_6 (.in(1'b0), .out(transistor_6_out), .gate(e_2));
  Transistor transistor_7 (.in(1'b1), .out(transistor_7_out), .gate(h_2));
  Transistor transistor_8 (.in(1'b1), .out(transistor_7_out), .gate(g_2));
  Transistor transistor_9 (.in(1'b1), .out(transistor_1_out), .gate(c_2));
  Transistor transistor_10 (.in(1'b1), .out(transistor_1_out), .gate(b_2));
  Transistor transistor_11 (.in(1'b1), .out(transistor_7_out), .gate(f_2));
  Transistor #(.\type ("n")) transistor_12 (.in(transistor_13_out), .out(transistor_7_out), .gate(h_2));
  Transistor #(.\type ("n")) transistor_13 (.in(transistor_14_out), .out(transistor_13_out), .gate(g_2));
  Transistor #(.\type ("n")) transistor_14 (.in(1'b0), .out(transistor_14_out), .gate(f_2));
  Transistor transistor_15 (.in(1'b1), .out(transistor_15_out), .gate(transistor_7_out));
  Transistor transistor_16 (.in(transistor_15_out), .out(transistor_16_out), .gate(transistor_1_out));
  Transistor #(.\type ("n")) transistor_17 (.in(1'b0), .out(transistor_16_out), .gate(transistor_7_out));
  Transistor #(.\type ("n")) transistor_18 (.in(1'b0), .out(transistor_16_out), .gate(transistor_1_out));
  Transistor transistor_19 (.in(1'b1), .out(a), .gate(transistor_16_out));
  Transistor #(.\type ("n")) transistor_20 (.in(1'b0), .out(a), .gate(transistor_16_out));
  nand nand_1 (nand_1_out, b, c, d, e);
  nand nand_2 (nand_2_out, f, g, h);
  or or_1 (a_2, nand_1_out, nand_2_out);

  // Notes on the sheet:
  //   ~
  //   NAND7
endmodule

module cell70 (
  input  a,
  input  b,
  input  c,
  output e,
  output d
);

  wire transistor_1_out, transistor_2_out, transistor_4_out, transistor_5_out, transistor_6_out,
       transistor_8_out, transistor_14_out, transistor_18_out;

  Transistor transistor_1 (.in(1'b1), .out(transistor_1_out), .gate(transistor_6_out));
  Transistor transistor_2 (.in(transistor_1_out), .out(transistor_2_out), .gate(a));
  Transistor #(.\type ("n")) transistor_3 (.in(transistor_4_out), .out(transistor_2_out), .gate(b));
  Transistor #(.\type ("n")) transistor_4 (.in(1'b0), .out(transistor_4_out), .gate(a));
  Transistor transistor_5 (.in(1'b1), .out(transistor_5_out), .gate(transistor_2_out));
  Transistor transistor_6 (.in(transistor_5_out), .out(transistor_6_out), .gate(c));
  Transistor #(.\type ("n")) transistor_7 (.in(transistor_8_out), .out(transistor_6_out), .gate(b));
  Transistor #(.\type ("n")) transistor_8 (.in(1'b0), .out(transistor_8_out), .gate(c));
  Transistor transistor_9 (.in(transistor_1_out), .out(transistor_2_out), .gate(b));
  Transistor #(.\type ("n")) transistor_10 (.in(1'b0), .out(transistor_2_out), .gate(transistor_6_out));
  Transistor transistor_11 (.in(transistor_5_out), .out(transistor_6_out), .gate(b));
  Transistor #(.\type ("n")) transistor_12 (.in(1'b0), .out(transistor_6_out), .gate(transistor_2_out));
  Transistor transistor_13 (.in(1'b1), .out(e), .gate(transistor_14_out));
  Transistor transistor_14 (.in(1'b1), .out(transistor_14_out), .gate(transistor_2_out));
  Transistor #(.\type ("n")) transistor_15 (.in(1'b0), .out(transistor_14_out), .gate(transistor_2_out));
  Transistor #(.\type ("n")) transistor_16 (.in(1'b0), .out(e), .gate(transistor_14_out));
  Transistor transistor_17 (.in(1'b1), .out(d), .gate(transistor_18_out));
  Transistor transistor_18 (.in(1'b1), .out(transistor_18_out), .gate(transistor_6_out));
  Transistor #(.\type ("n")) transistor_19 (.in(1'b0), .out(d), .gate(transistor_18_out));
  Transistor #(.\type ("n")) transistor_20 (.in(1'b0), .out(transistor_18_out), .gate(transistor_6_out));
endmodule

module cell71 (
  input  a,
  input  b,
  output d,
  output e
);

  wire transistor_1_out, transistor_2_out, transistor_4_out, transistor_5_out, transistor_10_out,
       transistor_13_out;

  Transistor transistor_1 (.in(1'b1), .out(transistor_1_out), .gate(transistor_5_out));
  Transistor transistor_2 (.in(transistor_1_out), .out(transistor_2_out), .gate(a));
  Transistor #(.\type ("n")) transistor_3 (.in(1'b0), .out(transistor_2_out), .gate(a));
  Transistor transistor_4 (.in(1'b1), .out(transistor_4_out), .gate(transistor_2_out));
  Transistor transistor_5 (.in(transistor_4_out), .out(transistor_5_out), .gate(b));
  Transistor #(.\type ("n")) transistor_6 (.in(1'b0), .out(transistor_5_out), .gate(b));
  Transistor #(.\type ("n")) transistor_7 (.in(1'b0), .out(transistor_2_out), .gate(transistor_5_out));
  Transistor #(.\type ("n")) transistor_8 (.in(1'b0), .out(transistor_5_out), .gate(transistor_2_out));
  Transistor transistor_9 (.in(1'b1), .out(d), .gate(transistor_10_out));
  Transistor transistor_10 (.in(1'b1), .out(transistor_10_out), .gate(transistor_2_out));
  Transistor #(.\type ("n")) transistor_11 (.in(1'b0), .out(d), .gate(transistor_10_out));
  Transistor #(.\type ("n")) transistor_12 (.in(1'b0), .out(transistor_10_out), .gate(transistor_2_out));
  Transistor transistor_13 (.in(1'b1), .out(transistor_13_out), .gate(transistor_5_out));
  Transistor transistor_14 (.in(1'b1), .out(e), .gate(transistor_13_out));
  Transistor #(.\type ("n")) transistor_15 (.in(1'b0), .out(transistor_13_out), .gate(transistor_5_out));
  Transistor #(.\type ("n")) transistor_16 (.in(1'b0), .out(e), .gate(transistor_13_out));
endmodule

module cell73__OAI211 (
  input  a,
  input  b,
  input  a_2,
  input  c,
  input  b_2,
  input  d,
  input  c_2,
  input  d_2,
  output e,
  output e_2
);

  wire and_1_out, or_1_out, transistor_4_out, transistor_5_out, transistor_7_out;

  Transistor transistor_1 (.in(1'b1), .out(e), .gate(c));
  Transistor transistor_2 (.in(1'b1), .out(e), .gate(d));
  Transistor #(.\type ("n")) transistor_3 (.in(transistor_4_out), .out(e), .gate(d));
  Transistor #(.\type ("n")) transistor_4 (.in(transistor_5_out), .out(transistor_4_out), .gate(c));
  Transistor #(.\type ("n")) transistor_5 (.in(1'b0), .out(transistor_5_out), .gate(b));
  Transistor #(.\type ("n")) transistor_6 (.in(1'b0), .out(transistor_5_out), .gate(a));
  Transistor transistor_7 (.in(1'b1), .out(transistor_7_out), .gate(a));
  Transistor transistor_8 (.in(transistor_7_out), .out(e), .gate(b));
  or or_1 (or_1_out, a_2, b_2);
  and and_1 (and_1_out, c_2, d_2);
  nand nand_1 (e_2, or_1_out, and_1_out);

  // Notes on the sheet:
  //   ~
  //   OAI211
endmodule

module cell74__BNUFIF0 (
  input  a,
  input  a_2,
  input  c,
  input  c_2,
  output out_5,
  output out_6
);

  wire not_1_out, transistor_1_out, transistor_3_out, transistor_5_out, transistor_8_out;

  Transistor transistor_1 (.in(1'b1), .out(transistor_1_out), .gate(a));
  Transistor #(.\type ("n")) transistor_2 (.in(1'b0), .out(transistor_1_out), .gate(a));
  Transistor transistor_3 (.in(1'b1), .out(transistor_3_out), .gate(c_2));
  Transistor #(.\type ("n")) transistor_4 (.in(1'b0), .out(transistor_3_out), .gate(c_2));
  Transistor transistor_5 (.in(1'b1), .out(transistor_5_out), .gate(transistor_3_out));
  Transistor transistor_6 (.in(transistor_5_out), .out(out_5), .gate(a));
  Transistor #(.\type ("n")) transistor_7 (.in(transistor_8_out), .out(out_5), .gate(transistor_1_out));
  Transistor #(.\type ("n")) transistor_8 (.in(1'b0), .out(transistor_8_out), .gate(transistor_3_out));
  not not_1 (not_1_out, a_2);
  assign out_6 = not_1_out ? c : 1'bz;  // Controlled_Buffer controlled_buffer_1

  // Notes on the sheet:
  //   BUFIF0
endmodule

module cell75__DLATCH_R (
  input  a,
  input  b,
  input  a_2,
  input  b_2,
  input  d,
  input  c,
  input  d_2,
  output e,
  output e_2
);

  wire multiplexer_1_out, nor_1_out, not_1_out, not_2_out, transistor_1_out, transistor_2_out,
       transistor_4_out, transistor_5_out, transistor_8_out, transistor_9_out, transistor_10_out,
       transistor_13_out;

  Transistor transistor_1 (.in(1'b1), .out(transistor_1_out), .gate(a));
  Transistor transistor_2 (.in(transistor_1_out), .out(transistor_2_out), .gate(c));
  Transistor #(.\type ("n")) transistor_3 (.in(transistor_4_out), .out(transistor_2_out), .gate(b));
  Transistor #(.\type ("n")) transistor_4 (.in(1'b0), .out(transistor_4_out), .gate(a));
  Transistor transistor_5 (.in(1'b1), .out(transistor_5_out), .gate(transistor_10_out));
  Transistor transistor_6 (.in(transistor_5_out), .out(transistor_2_out), .gate(b));
  Transistor #(.\type ("n")) transistor_7 (.in(transistor_8_out), .out(transistor_2_out), .gate(c));
  Transistor #(.\type ("n")) transistor_8 (.in(1'b0), .out(transistor_8_out), .gate(transistor_10_out));
  Transistor transistor_9 (.in(1'b1), .out(transistor_9_out), .gate(transistor_2_out));
  Transistor transistor_10 (.in(transistor_9_out), .out(transistor_10_out), .gate(d_2));
  Transistor #(.\type ("n")) transistor_11 (.in(1'b0), .out(transistor_10_out), .gate(d_2));
  Transistor #(.\type ("n")) transistor_12 (.in(1'b0), .out(transistor_10_out), .gate(transistor_2_out));
  Transistor transistor_13 (.in(1'b1), .out(transistor_13_out), .gate(transistor_10_out));
  Transistor transistor_14 (.in(1'b1), .out(e_2), .gate(transistor_13_out));
  Transistor #(.\type ("n")) transistor_15 (.in(1'b0), .out(transistor_13_out), .gate(transistor_10_out));
  Transistor #(.\type ("n")) transistor_16 (.in(1'b0), .out(e_2), .gate(transistor_13_out));
  Multiplexer #(.disabled(0), .enable("false")) multiplexer_1 (
    .in0(nor_1_out), .in1(a_2), .out(multiplexer_1_out), .sel(b_2));
  not not_1 (not_1_out, multiplexer_1_out);
  nor nor_1 (nor_1_out, not_1_out, d);
  not not_2 (not_2_out, nor_1_out);
  not not_3 (e, not_2_out);

  // Notes on the sheet:
  //   ~
  //   DLATCH_R
endmodule

module cell76 (
  input  nc1,
  input  nc2,
  input  c_in,
  input  r,
  input  c1,
  input  c2,
  input  a,
  output c_out,
  output ns,
  output s
);

  wire transistor_1_out, transistor_3_out, transistor_7_out, transistor_8_out, transistor_9_out,
       transistor_12_out, transistor_13_out, transistor_16_out, transistor_17_out, transistor_18_out,
       transistor_20_out, transistor_21_out, transistor_22_out, transistor_24_out, transistor_25_out,
       transistor_26_out;

  Transistor transistor_1 (.in(1'b1), .out(transistor_1_out), .gate(c_in));
  Transistor #(.\type ("n")) transistor_2 (.in(1'b0), .out(transistor_1_out), .gate(c_in));
  Transistor #(.gate("br")) transistor_3 (.in(1'b1), .out(transistor_3_out), .gate(transistor_26_out));
  Transistor transistor_4 (.in(transistor_3_out), .out(c_out), .gate(transistor_1_out));
  Transistor #(.\type ("n")) transistor_5 (.in(1'b0), .out(c_out), .gate(transistor_1_out));
  Transistor #(.\type ("n")) transistor_6 (.in(1'b0), .out(c_out), .gate(transistor_26_out));
  Transistor transistor_7 (.in(1'b1), .out(transistor_7_out), .gate(transistor_1_out));
  Transistor transistor_8 (.in(transistor_7_out), .out(transistor_8_out), .gate(c_out));
  Transistor transistor_9 (.in(transistor_8_out), .out(transistor_9_out), .gate(r));
  Transistor #(.\type ("n")) transistor_10 (.in(1'b0), .out(transistor_9_out), .gate(r));
  Transistor #(.\type ("n")) transistor_11 (.in(1'b0), .out(transistor_9_out), .gate(c_out));
  Transistor transistor_12 (.in(1'b1), .out(transistor_12_out), .gate(c_out));
  Transistor transistor_13 (.in(transistor_12_out), .out(transistor_13_out), .gate(transistor_26_out));
  Transistor transistor_14 (.in(transistor_13_out), .out(transistor_9_out), .gate(r));
  Transistor #(.\type ("n")) transistor_15 (.in(transistor_16_out), .out(transistor_9_out), .gate(transistor_26_out));
  Transistor #(.\type ("n")) transistor_16 (.in(1'b0), .out(transistor_16_out), .gate(transistor_1_out));
  Transistor transistor_17 (.in(1'b1), .out(transistor_17_out), .gate(transistor_9_out));
  Transistor transistor_18 (.in(transistor_17_out), .out(transistor_18_out), .gate(nc1));
  Transistor #(.\type ("n")) transistor_19 (.in(transistor_20_out), .out(transistor_18_out), .gate(c1));
  Transistor #(.\type ("n")) transistor_20 (.in(1'b0), .out(transistor_20_out), .gate(transistor_9_out));
  Transistor transistor_21 (.in(1'b1), .out(transistor_21_out), .gate(transistor_18_out));
  Transistor transistor_22 (.in(transistor_21_out), .out(transistor_22_out), .gate(nc2));
  Transistor #(.\type ("n")) transistor_23 (.in(transistor_24_out), .out(transistor_22_out), .gate(c2));
  Transistor #(.\type ("n")) transistor_24 (.in(1'b0), .out(transistor_24_out), .gate(transistor_18_out));
  Transistor transistor_25 (.in(1'b1), .out(transistor_25_out), .gate(a));
  Transistor transistor_26 (.in(transistor_25_out), .out(transistor_26_out), .gate(transistor_22_out));
  Transistor #(.\type ("n")) transistor_27 (.in(1'b0), .out(transistor_26_out), .gate(transistor_22_out));
  Transistor #(.\type ("n")) transistor_28 (.in(1'b0), .out(transistor_26_out), .gate(a));
  Transistor transistor_29 (.in(1'b1), .out(s), .gate(transistor_26_out));
  Transistor #(.\type ("n")) transistor_30 (.in(1'b0), .out(s), .gate(transistor_26_out));
  Transistor transistor_31 (.in(1'b1), .out(ns), .gate(s));
  Transistor #(.\type ("n")) transistor_32 (.in(1'b0), .out(ns), .gate(s));
endmodule

module cell77__CNT_BIT_REV (
  input  r,
  input  nc1,
  input  nc2,
  input  c,
  input  c1,
  input  c2,
  input  a,
  input  r_2,
  input  clk,
  input  C_2,
  input  A_2,
  output s,
  output ns,
  output c_out,
  output Q,
  output c_out_2
);

  wire adder_1_out, d_ff_1_qn, nor_1_out, not_1_out, transistor_1_out, transistor_2_out, transistor_4_out,
       transistor_7_out, transistor_10_out, transistor_11_out, transistor_13_out, transistor_15_out,
       transistor_19_out, transistor_20_out, transistor_23_out, transistor_24_out, transistor_25_out,
       transistor_26_out, transistor_31_out, transistor_32_out, transistor_34_out, transistor_35_out,
       transistor_36_out, transistor_38_out;

  Transistor transistor_1 (.in(1'b1), .out(transistor_1_out), .gate(a));
  Transistor #(.\type ("n")) transistor_2 (.in(1'b0), .out(transistor_2_out), .gate(a));
  Transistor #(.gate("br")) transistor_3 (.in(1'b1), .out(transistor_1_out), .gate(transistor_36_out));
  Transistor transistor_4 (.in(transistor_1_out), .out(transistor_4_out), .gate(c));
  Transistor #(.\type ("n")) transistor_5 (.in(transistor_2_out), .out(transistor_4_out), .gate(c));
  Transistor #(.\type ("n"), .gate("br")) transistor_6 (.in(1'b0), .out(transistor_2_out), .gate(transistor_36_out));
  Transistor transistor_7 (.in(1'b1), .out(transistor_7_out), .gate(transistor_36_out));
  Transistor transistor_8 (.in(transistor_7_out), .out(transistor_4_out), .gate(a));
  Transistor #(.\type ("n")) transistor_9 (.in(transistor_10_out), .out(transistor_4_out), .gate(a));
  Transistor #(.\type ("n")) transistor_10 (.in(1'b0), .out(transistor_10_out), .gate(transistor_36_out));
  Transistor transistor_11 (.in(1'b1), .out(transistor_11_out), .gate(a));
  Transistor transistor_12 (.in(1'b1), .out(transistor_11_out), .gate(c));
  Transistor transistor_13 (.in(transistor_11_out), .out(transistor_13_out), .gate(transistor_4_out));
  Transistor #(.\type ("n")) transistor_14 (.in(transistor_15_out), .out(transistor_13_out), .gate(transistor_4_out));
  Transistor #(.\type ("n")) transistor_15 (.in(1'b0), .out(transistor_15_out), .gate(c));
  Transistor #(.\type ("n")) transistor_16 (.in(1'b0), .out(transistor_15_out), .gate(a));
  Adder #(.width(1)) adder_1 (.a(A_2), .b(Q), .out(adder_1_out), .cin(C_2), .cout(c_out_2));
  Transistor transistor_17 (.in(1'b1), .out(transistor_11_out), .gate(transistor_36_out));
  Transistor #(.\type ("n")) transistor_18 (.in(1'b0), .out(transistor_15_out), .gate(transistor_36_out));
  nor nor_1 (nor_1_out, r_2, adder_1_out);
  Transistor transistor_19 (.in(1'b1), .out(transistor_19_out), .gate(transistor_36_out));
  Transistor transistor_20 (.in(transistor_19_out), .out(transistor_20_out), .gate(a));
  Transistor transistor_21 (.in(transistor_20_out), .out(transistor_13_out), .gate(c));
  Transistor #(.\type ("n")) transistor_22 (.in(transistor_23_out), .out(transistor_13_out), .gate(c));
  Transistor #(.\type ("n")) transistor_23 (.in(transistor_24_out), .out(transistor_23_out), .gate(a));
  Transistor #(.\type ("n")) transistor_24 (.in(1'b0), .out(transistor_24_out), .gate(transistor_36_out));
  not not_1 (not_1_out, clk);
  D_Flip_Flop #(.trigger("high")) d_ff_1 (.clk(clk), .D(nor_1_out), .Qn(d_ff_1_qn));  // open: Q, preset, en, reset
  Transistor transistor_25 (.in(1'b1), .out(transistor_25_out), .gate(r));
  Transistor transistor_26 (.in(transistor_25_out), .out(transistor_26_out), .gate(transistor_13_out));
  Transistor #(.\type ("n")) transistor_27 (.in(1'b0), .out(transistor_26_out), .gate(r));
  Transistor transistor_28 (.in(1'b1), .out(c_out), .gate(transistor_4_out));
  Transistor #(.\type ("n")) transistor_29 (.in(1'b0), .out(c_out), .gate(transistor_4_out));
  D_Flip_Flop #(.trigger("high")) d_ff_2 (.clk(not_1_out), .D(d_ff_1_qn), .Qn(Q));  // open: Q, preset, en, reset
  Transistor #(.\type ("n")) transistor_30 (.in(1'b0), .out(transistor_26_out), .gate(transistor_13_out));
  Transistor transistor_31 (.in(1'b1), .out(transistor_31_out), .gate(transistor_26_out));
  Transistor transistor_32 (.in(transistor_31_out), .out(transistor_32_out), .gate(nc1));
  Transistor #(.\type ("n")) transistor_33 (.in(transistor_34_out), .out(transistor_32_out), .gate(c1));
  Transistor #(.\type ("n")) transistor_34 (.in(1'b0), .out(transistor_34_out), .gate(transistor_26_out));
  Transistor transistor_35 (.in(1'b1), .out(transistor_35_out), .gate(transistor_32_out));
  Transistor transistor_36 (.in(transistor_35_out), .out(transistor_36_out), .gate(nc2));
  Transistor #(.\type ("n")) transistor_37 (.in(transistor_38_out), .out(transistor_36_out), .gate(c2));
  Transistor #(.\type ("n")) transistor_38 (.in(1'b0), .out(transistor_38_out), .gate(transistor_32_out));
  Transistor transistor_39 (.in(1'b1), .out(ns), .gate(transistor_36_out));
  Transistor #(.\type ("n")) transistor_40 (.in(1'b0), .out(ns), .gate(transistor_36_out));
  Transistor transistor_41 (.in(1'b1), .out(s), .gate(ns));
  Transistor #(.\type ("n")) transistor_42 (.in(1'b0), .out(s), .gate(ns));

  // Notes on the sheet:
  //   ~
  //   CNT_BIT_REV
endmodule

module cell78__AON333 (
  input  a,
  input  a_2,
  input  b,
  input  b_2,
  input  c,
  input  c_2,
  input  d,
  input  d_2,
  input  e,
  input  e_2,
  input  f,
  input  f_2,
  input  g,
  input  g_2,
  input  h,
  input  h_2,
  input  i,
  input  i_2,
  output j,
  output j_2
);

  wire and_1_out, and_2_out, and_3_out, transistor_1_out, transistor_2_out, transistor_3_out,
       transistor_5_out, transistor_6_out, transistor_11_out, transistor_12_out, transistor_17_out,
       transistor_18_out;

  Transistor transistor_1 (.in(1'b1), .out(transistor_1_out), .gate(g_2));
  Transistor transistor_2 (.in(transistor_1_out), .out(transistor_2_out), .gate(d_2));
  Transistor transistor_3 (.in(transistor_2_out), .out(transistor_3_out), .gate(a_2));
  Transistor #(.\type ("n")) transistor_4 (.in(transistor_5_out), .out(transistor_3_out), .gate(a_2));
  Transistor #(.\type ("n")) transistor_5 (.in(transistor_6_out), .out(transistor_5_out), .gate(b_2));
  Transistor #(.\type ("n")) transistor_6 (.in(1'b0), .out(transistor_6_out), .gate(c_2));
  Transistor transistor_7 (.in(1'b1), .out(transistor_1_out), .gate(h_2));
  Transistor transistor_8 (.in(transistor_1_out), .out(transistor_2_out), .gate(e_2));
  Transistor transistor_9 (.in(transistor_2_out), .out(transistor_3_out), .gate(b_2));
  Transistor #(.\type ("n")) transistor_10 (.in(transistor_11_out), .out(transistor_3_out), .gate(f_2));
  Transistor #(.\type ("n")) transistor_11 (.in(transistor_12_out), .out(transistor_11_out), .gate(e_2));
  Transistor #(.\type ("n")) transistor_12 (.in(1'b0), .out(transistor_12_out), .gate(d_2));
  Transistor transistor_13 (.in(1'b1), .out(transistor_1_out), .gate(i_2));
  Transistor transistor_14 (.in(transistor_1_out), .out(transistor_2_out), .gate(f_2));
  Transistor transistor_15 (.in(transistor_2_out), .out(transistor_3_out), .gate(c_2));
  Transistor #(.\type ("n")) transistor_16 (.in(transistor_17_out), .out(transistor_3_out), .gate(g_2));
  Transistor #(.\type ("n")) transistor_17 (.in(transistor_18_out), .out(transistor_17_out), .gate(h_2));
  Transistor #(.\type ("n")) transistor_18 (.in(1'b0), .out(transistor_18_out), .gate(i_2));
  Transistor transistor_19 (.in(1'b1), .out(j), .gate(transistor_3_out));
  Transistor #(.\type ("n")) transistor_20 (.in(1'b0), .out(j), .gate(transistor_3_out));
  and and_1 (and_1_out, a, b, c);
  and and_2 (and_2_out, d, e, f);
  and and_3 (and_3_out, g, h, i);
  or or_1 (j_2, and_1_out, and_2_out, and_3_out);

  // Notes on the sheet:
  //   ~
  //   AON333
endmodule

module cell79__OR9 (
  input  a,
  input  b,
  input  c,
  input  a_2,
  input  b_2,
  input  c_2,
  input  d,
  input  d_2,
  input  e,
  input  e_2,
  input  f,
  input  f_2,
  input  h,
  input  i,
  input  j,
  input  h_2,
  input  i_2,
  input  j_2,
  output g,
  output g_2
);

  wire nor_1_out, nor_2_out, nor_3_out, transistor_1_out, transistor_2_out, transistor_3_out,
       transistor_4_out, transistor_7_out, transistor_8_out, transistor_9_out, transistor_12_out,
       transistor_13_out, transistor_22_out, transistor_23_out;

  Transistor #(.\type ("n")) transistor_1 (.in(1'b0), .out(transistor_1_out), .gate(a));
  Transistor transistor_2 (.in(1'b1), .out(transistor_2_out), .gate(d));
  Transistor transistor_3 (.in(transistor_2_out), .out(transistor_3_out), .gate(e));
  Transistor transistor_4 (.in(transistor_3_out), .out(transistor_4_out), .gate(f_2));
  Transistor #(.\type ("n")) transistor_5 (.in(1'b0), .out(transistor_4_out), .gate(e));
  Transistor #(.\type ("n")) transistor_6 (.in(1'b0), .out(transistor_4_out), .gate(d));
  Transistor transistor_7 (.in(1'b1), .out(transistor_7_out), .gate(h_2));
  Transistor transistor_8 (.in(transistor_7_out), .out(transistor_8_out), .gate(i_2));
  Transistor transistor_9 (.in(transistor_8_out), .out(transistor_9_out), .gate(j_2));
  Transistor #(.\type ("n")) transistor_10 (.in(1'b0), .out(transistor_9_out), .gate(h_2));
  Transistor #(.\type ("n")) transistor_11 (.in(1'b0), .out(transistor_9_out), .gate(i_2));
  Transistor transistor_12 (.in(1'b1), .out(transistor_12_out), .gate(c));
  Transistor transistor_13 (.in(transistor_12_out), .out(transistor_13_out), .gate(b));
  Transistor transistor_14 (.in(transistor_13_out), .out(transistor_1_out), .gate(a));
  Transistor #(.\type ("n")) transistor_15 (.in(1'b0), .out(transistor_1_out), .gate(b));
  Transistor #(.\type ("n")) transistor_16 (.in(1'b0), .out(transistor_1_out), .gate(c));
  Transistor #(.\type ("n")) transistor_17 (.in(1'b0), .out(transistor_4_out), .gate(f_2));
  Transistor #(.\type ("n")) transistor_18 (.in(1'b0), .out(transistor_9_out), .gate(j_2));
  Transistor transistor_19 (.in(1'b1), .out(g), .gate(transistor_1_out));
  Transistor transistor_20 (.in(1'b1), .out(g), .gate(transistor_4_out));
  Transistor #(.\type ("n")) transistor_21 (.in(transistor_22_out), .out(g), .gate(transistor_9_out));
  Transistor #(.\type ("n")) transistor_22 (.in(transistor_23_out), .out(transistor_22_out), .gate(transistor_1_out));
  Transistor #(.\type ("n")) transistor_23 (.in(1'b0), .out(transistor_23_out), .gate(transistor_4_out));
  Transistor transistor_24 (.in(1'b1), .out(g), .gate(transistor_9_out));
  nor nor_1 (nor_1_out, a_2, b_2, c_2);
  nor nor_2 (nor_2_out, d_2, e_2, f);
  nor nor_3 (nor_3_out, h, i, j);
  nand nand_1 (g_2, nor_1_out, nor_2_out, nor_3_out);

  // Notes on the sheet:
  //   ~
  //   OR9
endmodule

module cell80__NOR8 (
  input  b,
  input  c,
  input  d,
  input  e,
  input  b_2,
  input  c_2,
  input  d_2,
  input  e_2,
  input  f,
  input  g,
  input  f_2,
  input  h,
  input  g_2,
  input  i,
  input  h_2,
  input  i_2,
  output a,
  output a_2
);

  wire nor_1_out, nor_2_out, transistor_1_out, transistor_2_out, transistor_3_out, transistor_4_out,
       transistor_7_out, transistor_8_out, transistor_9_out, transistor_10_out, transistor_17_out,
       transistor_20_out;

  Transistor transistor_1 (.in(1'b1), .out(transistor_1_out), .gate(b));
  Transistor transistor_2 (.in(transistor_1_out), .out(transistor_2_out), .gate(c));
  Transistor transistor_3 (.in(transistor_2_out), .out(transistor_3_out), .gate(d));
  Transistor transistor_4 (.in(transistor_3_out), .out(transistor_4_out), .gate(e));
  Transistor #(.\type ("n")) transistor_5 (.in(1'b0), .out(transistor_4_out), .gate(b));
  Transistor #(.\type ("n")) transistor_6 (.in(1'b0), .out(transistor_4_out), .gate(c));
  Transistor transistor_7 (.in(1'b1), .out(transistor_7_out), .gate(f_2));
  Transistor transistor_8 (.in(transistor_7_out), .out(transistor_8_out), .gate(g_2));
  Transistor transistor_9 (.in(transistor_8_out), .out(transistor_9_out), .gate(h_2));
  Transistor transistor_10 (.in(transistor_9_out), .out(transistor_10_out), .gate(i_2));
  Transistor #(.\type ("n")) transistor_11 (.in(1'b0), .out(transistor_10_out), .gate(g_2));
  Transistor #(.\type ("n")) transistor_12 (.in(1'b0), .out(transistor_10_out), .gate(f_2));
  Transistor #(.\type ("n")) transistor_13 (.in(1'b0), .out(transistor_4_out), .gate(d));
  Transistor #(.\type ("n")) transistor_14 (.in(1'b0), .out(transistor_4_out), .gate(e));
  Transistor #(.\type ("n")) transistor_15 (.in(1'b0), .out(transistor_10_out), .gate(i_2));
  Transistor #(.\type ("n")) transistor_16 (.in(1'b0), .out(transistor_10_out), .gate(h_2));
  Transistor transistor_17 (.in(1'b1), .out(transistor_17_out), .gate(transistor_10_out));
  Transistor transistor_18 (.in(1'b1), .out(transistor_17_out), .gate(transistor_4_out));
  Transistor #(.\type ("n")) transistor_19 (.in(transistor_20_out), .out(transistor_17_out), .gate(transistor_4_out));
  Transistor #(.\type ("n")) transistor_20 (.in(1'b0), .out(transistor_20_out), .gate(transistor_10_out));
  Transistor transistor_21 (.in(1'b1), .out(a), .gate(transistor_17_out));
  Transistor #(.\type ("n")) transistor_22 (.in(1'b0), .out(a), .gate(transistor_17_out));
  nor nor_1 (nor_1_out, b_2, c_2, d_2, e_2);
  nor nor_2 (nor_2_out, f, g, h, i);
  and and_1 (a_2, nor_1_out, nor_2_out);

  // Notes on the sheet:
  //   ~
  //   NOR8
endmodule

module cell84__2A3OI (
  input  a,
  input  b,
  input  c,
  input  d,
  input  a_2,
  input  b_2,
  input  c_2,
  input  d_2,
  output Q,
  output Q_2
);

  wire and_1_out, transistor_1_out, transistor_2_out, transistor_8_out;

  Transistor transistor_1 (.in(1'b1), .out(transistor_1_out), .gate(c_2));
  Transistor transistor_2 (.in(transistor_1_out), .out(transistor_2_out), .gate(b_2));
  Transistor transistor_3 (.in(transistor_2_out), .out(Q_2), .gate(a_2));
  Transistor #(.\type ("n")) transistor_4 (.in(1'b0), .out(Q_2), .gate(a_2));
  Transistor #(.\type ("n")) transistor_5 (.in(1'b0), .out(Q_2), .gate(b_2));
  Transistor transistor_6 (.in(1'b1), .out(transistor_1_out), .gate(d_2));
  Transistor #(.\type ("n")) transistor_7 (.in(transistor_8_out), .out(Q_2), .gate(c_2));
  Transistor #(.\type ("n")) transistor_8 (.in(1'b0), .out(transistor_8_out), .gate(d_2));
  and and_1 (and_1_out, c, d);
  nor nor_1 (Q, a, b, and_1_out);

  // Notes on the sheet:
  //   3
  //   2
  //   1
  //   5
  //   6
  //   4
  //   7
  //   8
  //   ~
  //   2A3OI
endmodule
module cell85__AOI31 (
  input  a,
  input  b,
  input  c,
  input  d,
  input  a_2,
  input  b_2,
  input  c_2,
  input  d_2,
  output Q,
  output X
);

  wire and_1_out, transistor_1_out, transistor_7_out, transistor_8_out;

  Transistor transistor_1 (.in(1'b1), .out(transistor_1_out), .gate(b_2));
  Transistor transistor_2 (.in(transistor_1_out), .out(X), .gate(a_2));
  Transistor #(.\type ("n")) transistor_3 (.in(1'b0), .out(X), .gate(a_2));
  Transistor transistor_4 (.in(1'b1), .out(transistor_1_out), .gate(c_2));
  Transistor transistor_5 (.in(1'b1), .out(transistor_1_out), .gate(d_2));
  Transistor #(.\type ("n")) transistor_6 (.in(transistor_7_out), .out(X), .gate(d_2));
  Transistor #(.\type ("n")) transistor_7 (.in(transistor_8_out), .out(transistor_7_out), .gate(c_2));
  Transistor #(.\type ("n")) transistor_8 (.in(1'b0), .out(transistor_8_out), .gate(b_2));
  and and_1 (and_1_out, b, c, d);
  nor nor_1 (Q, a, and_1_out);

  // Notes on the sheet:
  //   ~
  //   AOI31
endmodule

module cell86__COMB1 (
  input  a,
  input  b,
  input  c,
  input  a_2,
  input  d,
  input  b_2,
  input  c_2,
  input  d_2,
  output X,
  output X_2
);

  wire and_1_out, or_1_out, transistor_4_out, transistor_5_out, transistor_8_out;

  Transistor transistor_1 (.in(1'b1), .out(X_2), .gate(a_2));
  Transistor transistor_2 (.in(transistor_5_out), .out(X_2), .gate(b_2));
  Transistor #(.\type ("n")) transistor_3 (.in(transistor_4_out), .out(X_2), .gate(a_2));
  Transistor #(.\type ("n")) transistor_4 (.in(1'b0), .out(transistor_4_out), .gate(b_2));
  Transistor transistor_5 (.in(1'b1), .out(transistor_5_out), .gate(c_2));
  Transistor transistor_6 (.in(1'b1), .out(transistor_5_out), .gate(d_2));
  Transistor #(.\type ("n")) transistor_7 (.in(transistor_8_out), .out(transistor_4_out), .gate(d_2));
  Transistor #(.\type ("n")) transistor_8 (.in(1'b0), .out(transistor_8_out), .gate(c_2));
  and and_1 (and_1_out, c, d);
  or or_1 (or_1_out, b, and_1_out);
  nand nand_1 (X, a, or_1_out);

  // Notes on the sheet:
  //   ~
  //   COMB1
endmodule

module cell87__DDLATCH (
  input  B,
  input  A,
  input  C,
  output Q
);

  wire transistor_1_out, transistor_2_out, transistor_4_out;

  Transistor transistor_1 (.in(1'b1), .out(transistor_1_out), .gate(B));
  Transistor transistor_2 (.in(transistor_1_out), .out(transistor_2_out), .gate(A));
  Transistor #(.\type ("n")) transistor_3 (.in(transistor_4_out), .out(transistor_2_out), .gate(A));
  Transistor #(.\type ("n")) transistor_4 (.in(1'b0), .out(transistor_4_out), .gate(C));
  Transistor transistor_5 (.in(1'b1), .out(Q), .gate(transistor_2_out));
  Transistor #(.\type ("n")) transistor_6 (.in(1'b0), .out(Q), .gate(transistor_2_out));
endmodule

module cell90__AND9 (
  input  a,
  input  b,
  input  c,
  input  a_2,
  input  b_2,
  input  c_2,
  input  d,
  input  d_2,
  input  e,
  input  e_2,
  input  f,
  input  f_2,
  input  g,
  input  h,
  input  i,
  input  g_2,
  input  h_2,
  input  i_2,
  output X,
  output X_2
);

  wire nand_1_out, nand_2_out, nand_3_out, transistor_1_out, transistor_4_out, transistor_5_out,
       transistor_6_out, transistor_9_out, transistor_10_out, transistor_11_out, transistor_14_out,
       transistor_15_out, transistor_19_out, transistor_20_out;

  Transistor transistor_1 (.in(1'b1), .out(transistor_1_out), .gate(c));
  Transistor transistor_2 (.in(1'b1), .out(transistor_1_out), .gate(b));
  Transistor #(.\type ("n")) transistor_3 (.in(transistor_4_out), .out(transistor_1_out), .gate(a));
  Transistor #(.\type ("n")) transistor_4 (.in(transistor_5_out), .out(transistor_4_out), .gate(b));
  Transistor #(.\type ("n")) transistor_5 (.in(1'b0), .out(transistor_5_out), .gate(c));
  Transistor transistor_6 (.in(1'b1), .out(transistor_6_out), .gate(f_2));
  Transistor transistor_7 (.in(1'b1), .out(transistor_6_out), .gate(e));
  Transistor #(.\type ("n")) transistor_8 (.in(transistor_9_out), .out(transistor_6_out), .gate(d));
  Transistor #(.\type ("n")) transistor_9 (.in(transistor_10_out), .out(transistor_9_out), .gate(e));
  Transistor #(.\type ("n")) transistor_10 (.in(1'b0), .out(transistor_10_out), .gate(f_2));
  Transistor transistor_11 (.in(1'b1), .out(transistor_11_out), .gate(i_2));
  Transistor transistor_12 (.in(1'b1), .out(transistor_11_out), .gate(h_2));
  Transistor #(.\type ("n")) transistor_13 (.in(transistor_14_out), .out(transistor_11_out), .gate(g_2));
  Transistor #(.\type ("n")) transistor_14 (.in(transistor_15_out), .out(transistor_14_out), .gate(h_2));
  Transistor #(.\type ("n")) transistor_15 (.in(1'b0), .out(transistor_15_out), .gate(i_2));
  Transistor transistor_16 (.in(1'b1), .out(transistor_1_out), .gate(a));
  Transistor transistor_17 (.in(1'b1), .out(transistor_6_out), .gate(d));
  Transistor transistor_18 (.in(1'b1), .out(transistor_11_out), .gate(g_2));
  Transistor transistor_19 (.in(1'b1), .out(transistor_19_out), .gate(transistor_1_out));
  Transistor transistor_20 (.in(transistor_19_out), .out(transistor_20_out), .gate(transistor_6_out));
  Transistor transistor_21 (.in(transistor_20_out), .out(X), .gate(transistor_11_out));
  Transistor #(.\type ("n")) transistor_22 (.in(1'b0), .out(X), .gate(transistor_6_out));
  Transistor #(.\type ("n")) transistor_23 (.in(1'b0), .out(X), .gate(transistor_1_out));
  Transistor #(.\type ("n")) transistor_24 (.in(1'b0), .out(X), .gate(transistor_11_out));
  nand nand_1 (nand_1_out, a_2, b_2, c_2);
  nand nand_2 (nand_2_out, d_2, e_2, f);
  nand nand_3 (nand_3_out, g, h, i);
  nor nor_1 (X_2, nand_1_out, nand_2_out, nand_3_out);

  // Notes on the sheet:
  //   ~
  //   AND9
endmodule

module cell91__XNOR (
  input  B,
  input  A,
  input  A_2,
  input  B_2,
  output Q,
  output Q_2
);

  wire transistor_1_out, transistor_3_out, transistor_5_out, transistor_8_out, transistor_11_out;

  Transistor transistor_1 (.in(1'b1), .out(transistor_1_out), .gate(A));
  Transistor #(.\type ("n")) transistor_2 (.in(transistor_3_out), .out(transistor_1_out), .gate(A));
  Transistor #(.\type ("n")) transistor_3 (.in(1'b0), .out(transistor_3_out), .gate(B));
  Transistor #(.gate("br")) transistor_4 (.in(1'b1), .out(transistor_1_out), .gate(B));
  Transistor transistor_5 (.in(1'b1), .out(transistor_5_out), .gate(B));
  Transistor transistor_6 (.in(transistor_5_out), .out(Q), .gate(A));
  Transistor #(.\type ("n")) transistor_7 (.in(transistor_8_out), .out(Q), .gate(transistor_1_out));
  Transistor #(.\type ("n")) transistor_8 (.in(1'b0), .out(transistor_8_out), .gate(B));
  Transistor transistor_9 (.in(1'b1), .out(Q), .gate(transistor_1_out));
  Transistor #(.\type ("n")) transistor_10 (.in(transistor_11_out), .out(Q), .gate(transistor_1_out));
  Transistor #(.\type ("n")) transistor_11 (.in(1'b0), .out(transistor_11_out), .gate(A));
  xnor xnor_1 (Q_2, A_2, B_2);

  // Notes on the sheet:
  //   7
  //   1
  //   2
  //   8
  //   9
  //   10
  //   4
  //   3
  //   11
  //   5
  //   6
  //   ~
endmodule
